// Digital circuit aluop2ascii.dig as structural Verilog
module aluop2ascii (
  input  [4:0] I,
  output [6:0] L0,
  output [6:0] L1,
  output [6:0] L2,
  output [6:0] L3,
  output L_v,
  output R_v,
  output res_v
);

  Multiplexer #(.Selector_Bits(4), .Bits(7)) multiplexer_1 (
    .sel(I[3:0]), .in_0(7'b0100000), .in_1(7'b0100000), .in_2(7'b0100000), .in_3(7'b0100000),
    .in_4(7'b0100000), .in_5(7'b0100000), .in_6(7'b0100000), .in_7(7'b0100000), .in_8(7'b0100000),
    .in_9(7'b0100000), .in_10(7'b0100000), .in_11(7'b0100000), .in_12(7'b0100000), .in_13(7'b0100000),
    .in_14(7'b0100000), .in_15(7'b0100000), .out(L0));
  Multiplexer #(.Selector_Bits(4), .Bits(7)) multiplexer_2 (
    .sel(I[3:0]), .in_0(7'b0100000), .in_1(7'b0101011), .in_2(7'b0100000), .in_3(7'b0111100),
    .in_4(7'b0111100), .in_5(7'b0101101), .in_6(7'b0100000), .in_7(7'b0100000), .in_8(7'b0100000),
    .in_9(7'b0100000), .in_10(7'b0100000), .in_11(7'b0100000), .in_12(7'b0100000), .in_13(7'b0100000),
    .in_14(7'b0100000), .in_15(7'b0100000), .out(L1));
  Multiplexer #(.Selector_Bits(4), .Bits(7)) multiplexer_3 (
    .sel(I[3:0]), .in_0(7'b0100000), .in_1(7'b0100000), .in_2(7'b0100000), .in_3(7'b0101101),
    .in_4(7'b0111110), .in_5(7'b0100000), .in_6(7'b0100000), .in_7(7'b0100000), .in_8(7'b0100000),
    .in_9(7'b0100000), .in_10(7'b0100000), .in_11(7'b0100000), .in_12(7'b0100000), .in_13(7'b0100000),
    .in_14(7'b0100000), .in_15(7'b0100000), .out(L2));
  Multiplexer #(.Selector_Bits(4), .Bits(7)) multiplexer_4 (
    .sel(I[3:0]), .in_0(7'b0100000), .in_1(7'b0100000), .in_2(7'b0100000), .in_3(7'b0100000),
    .in_4(7'b0100000), .in_5(7'b0100000), .in_6(7'b0100000), .in_7(7'b0100000), .in_8(7'b0100000),
    .in_9(7'b0100000), .in_10(7'b0100000), .in_11(7'b0100000), .in_12(7'b0100000), .in_13(7'b0100000),
    .in_14(7'b0100000), .in_15(7'b0100000), .out(L3));
  Multiplexer #(.Selector_Bits(4)) multiplexer_5 (
    .sel(I[3:0]), .in_0(1'b0), .in_1(1'b1), .in_2(1'b0), .in_3(1'b0), .in_4(1'b1), .in_5(1'b1), .in_6(1'b0),
    .in_7(1'b0), .in_8(1'b0), .in_9(1'b0), .in_10(1'b0), .in_11(1'b0), .in_12(1'b0), .in_13(1'b0),
    .in_14(1'b0), .in_15(1'b0), .out(L_v));
  Multiplexer #(.Selector_Bits(4)) multiplexer_6 (
    .sel(I[3:0]), .in_0(1'b0), .in_1(1'b1), .in_2(1'b0), .in_3(1'b1), .in_4(1'b1), .in_5(1'b1), .in_6(1'b0),
    .in_7(1'b0), .in_8(1'b0), .in_9(1'b0), .in_10(1'b0), .in_11(1'b0), .in_12(1'b0), .in_13(1'b0),
    .in_14(1'b0), .in_15(1'b0), .out(R_v));
  Multiplexer #(.Selector_Bits(4)) multiplexer_7 (
    .sel(I[3:0]), .in_0(1'b0), .in_1(1'b1), .in_2(1'b0), .in_3(1'b1), .in_4(1'b0), .in_5(1'b1), .in_6(1'b0),
    .in_7(1'b0), .in_8(1'b0), .in_9(1'b0), .in_10(1'b0), .in_11(1'b0), .in_12(1'b0), .in_13(1'b0),
    .in_14(1'b0), .in_15(1'b0), .out(res_v));
  // Pins of 4 and 5 bits meet at I
  // Pins of 1 and 7 bits meet at L0
  // Pins of 1 and 7 bits meet at L1
  // Pins of 1 and 7 bits meet at L2
  // Pins of 1 and 7 bits meet at L3
endmodule
