// Digital circuit aluopdisplay.dig as structural Verilog
module aluopdisplay (
  input  [25:0] i,
  output [15:0] D1,
  output P1,
  output [15:0] D2,
  output P2,
  output [25:0] o
);

  wire [2:0] ctrldec_1_p2;
  wire [6:0] aluop2ascii_1_p2, aluop2ascii_1_p3;
  wire [15:0] debugval_1_q;

  debugval debugval_1 (.db_i(i), .sel(8'h11), .db_o(o), .Q(debugval_1_q));
  // ctrldec ctrldec_1: pin names not known; wires that end beside it: debugval_1_q, ctrldec_1_p2
  ROM #(.AddrBits(7), .Bits(16)) ASCII (.A(aluop2ascii_1_p2), .sel(1'b1), .D(D1));
  // aluop2ascii aluop2ascii_1: pin names not known; wires that end beside it: {1'b0, ctrldec_1_p2}, aluop2ascii_1_p2, aluop2ascii_1_p3
  ROM #(.AddrBits(7), .Bits(16)) ASCII_2 (.A(aluop2ascii_1_p3), .sel(1'b1), .D(D2));

  assign P1 = 1'b0;
  assign P2 = 1'b0;

  // Notes on the sheet:
  //   contents of ASCII (hex, n*v repeats v):
  //   90ff,c,377,33f,38c,3bb,3fb,f,3ff,3bf,3cf,4a3f,f3,483f,3f3,1c3,0,0,0,0,0,0,0,0,0,0,
  //   0,0,0,0,0,0,0,4800,0,0,0,0,2d79,0,0,0,0,4b00,0,300,0,0,90ff,c,377,33f,38c,3bb,3fb,
  //   f,3ff,3bf,0,0,3000,0,8400,0,0,3cf,4a3f,f3,483f,3f3,1c3,2fb,3cc,4833,7c,31c0,f0,14cc,
  //   24cc,ff,3c7,20ff,23c7,3bb,4803,fc,90c0,a0cc,b400,5400,9033,0,0,0,a000
  //   contents of ASCII_2 (hex, n*v repeats v):
  //   90ff,c,377,33f,38c,3bb,3fb,f,3ff,3bf,3cf,4a3f,f3,483f,3f3,1c3,0,0,0,0,0,0,0,0,0,0,
  //   0,0,0,0,0,0,0,4800,0,0,0,0,2d79,0,0,0,0,4b00,0,300,0,0,90ff,c,377,33f,38c,3bb,3fb,
  //   f,3ff,3bf,0,0,3000,0,8400,0,0,3cf,4a3f,f3,483f,3f3,1c3,2fb,3cc,4833,7c,31c0,f0,14cc,
  //   24cc,ff,3c7,20ff,23c7,3bb,4803,fc,90c0,a0cc,b400,5400,9033,0,0,0,a000
endmodule
