// Digital circuit bcd2ascii.dig as structural Verilog
module bcd2ascii (
  input  [19:0] N,
  input  s,
  output [6:0] d5,
  output [6:0] d4,
  output [6:0] d3,
  output [6:0] d2,
  output [6:0] d1,
  output [6:0] d0
);

  wire digit2asciiskip_1_s_o, digit2asciiskip_2_s_o, digit2asciiskip_3_s_o;

  Multiplexer #(.Bits(7)) multiplexer_1 (.sel(s), .in_0(7'b0100000), .in_1(7'b0101101), .out(d5));
  digit2asciiskip digit2asciiskip_1 (.i(N[19:16]), .s_i(1'b0), .a(d4), .s_o(digit2asciiskip_1_s_o));
  digit2asciiskip digit2asciiskip_2 (.i(N[15:12]), .s_i(digit2asciiskip_1_s_o), .a(d3), .s_o(digit2asciiskip_2_s_o));
  digit2asciiskip digit2asciiskip_3 (.i(N[11:8]), .s_i(digit2asciiskip_2_s_o), .a(d2), .s_o(digit2asciiskip_3_s_o));
  digit2asciiskip digit2asciiskip_4 (.i(N[7:4]), .s_i(digit2asciiskip_3_s_o), .a(d1));  // open: s_o
  digit2ascii digit2ascii_1 (.D(N[3:0]), .A(d0));
endmodule
