// Digital circuit bin2bcd.dig as structural Verilog
module bin2bcd (
  input  [31:0] I,
  output [39:0] O
);

  wire [31:0] div_1_q, div_2_q, div_3_q, div_4_q, div_5_q, div_6_q, div_7_q, div_8_q, div_9_q;
  wire [31:4] div_1_r, div_2_r, div_3_r, div_4_r, div_5_r, div_6_r, div_7_r, div_8_r, div_9_r, div_10_r;

  Div #(.Bits(32)) div_1 (.a(I), .b(32'ha), .q(div_1_q), .r({div_1_r, O[3:0]}));
  Div #(.Bits(32)) div_2 (.a(div_1_q), .b(32'ha), .q(div_2_q), .r({div_2_r, O[7:4]}));
  Div #(.Bits(32)) div_3 (.a(div_2_q), .b(32'ha), .q(div_3_q), .r({div_3_r, O[11:8]}));
  Div #(.Bits(32)) div_4 (.a(div_3_q), .b(32'ha), .q(div_4_q), .r({div_4_r, O[15:12]}));
  Div #(.Bits(32)) div_5 (.a(div_4_q), .b(32'ha), .q(div_5_q), .r({div_5_r, O[19:16]}));
  Div #(.Bits(32)) div_6 (.a(div_5_q), .b(32'ha), .q(div_6_q), .r({div_6_r, O[23:20]}));
  Div #(.Bits(32)) div_7 (.a(div_6_q), .b(32'ha), .q(div_7_q), .r({div_7_r, O[27:24]}));
  Div #(.Bits(32)) div_8 (.a(div_7_q), .b(32'ha), .q(div_8_q), .r({div_8_r, O[31:28]}));
  Div #(.Bits(32)) div_9 (.a(div_8_q), .b(32'ha), .q(div_9_q), .r({div_9_r, O[35:32]}));
  Div #(.Bits(32)) div_10 (.a(div_9_q), .b(32'ha), .r({div_10_r, O[39:36]}));  // open: q
endmodule
