// Digital circuit bin2bcdpiped.dig as structural Verilog
module bin2bcdpiped (
  input  [15:0] I,
  input  clock,
  output [19:0] O
);

  wire [2:0] register_3_q;
  wire [3:0] gt4add3_8_o, gt4add3_9_o, gt4add3_10_o, gt4add3_11_o, gt4add3_12_o, gt4add3_12_o_2,
       gt4add3_13_o, gt4add3_14_o, gt4add3_15_o, gt4add3_28_o, gt4add3_30_o, gt4add3_32_o, gt4add3_34_o,
       register_2_q_2, register_2_q_3, register_4_q, register_4_q_2, register_4_q_3, register_4_q_4;
  wire [3:3] gt4add3_9_o_2, register_2_q_4;
  wire [5:0] register_2_q;
  wire [8:0] register_1_q;
  wire [14:11] register_1_q_3;
  wire [15:13] gt4add3_2_o;
  wire [16:5] register_3_q_2;
  wire [16:10] gt4add3_6_o;
  wire [16:12] gt4add3_2_o_2;
  wire [17:9] register_1_q_2;
  wire [18:4] gt4add3_17_o;
  wire [19:3] gt4add3_17_o_2, gt4add3_20_o;
  wire [19:9] register_1_q_4;

  gt4add3 gt4add3_1 (.O(gt4add3_2_o_2[15:12]), .I({gt4add3_2_o, I[12]}));
  gt4add3 gt4add3_2 (.O({gt4add3_2_o_2[16], gt4add3_2_o}), .I({1'b0, I[15:13]}));
  Register #(.Bits(20)) register_1 (
    .D({3'b000, gt4add3_2_o_2, I[11:0]}), .C(clock), .en(1'b1),
    .Q({register_1_q_4[19:18], register_1_q_2[17:15], register_1_q_3, register_1_q_2[10:9], register_1_q}));
  gt4add3 gt4add3_3 (.O(register_1_q_4[16:13]), .I(gt4add3_6_o[16:13]));
  gt4add3 gt4add3_4 (.O({register_1_q_4[17], gt4add3_6_o[16:14]}), .I(register_1_q_2[17:14]));
  gt4add3 gt4add3_5 (.O(register_1_q_4[12:9]), .I({gt4add3_6_o[12:10], register_1_q_2[9]}));
  gt4add3 gt4add3_6 (.O(gt4add3_6_o[13:10]), .I(register_1_q_2[13:10]));
  gt4add3 gt4add3_7 (.O(register_1_q_2[14:11]), .I(register_1_q_3));
  Register #(.Bits(20)) register_2 (
    .D({register_1_q_4, register_1_q}), .C(clock), .en(1'b1),
    .Q({register_2_q_4[3], gt4add3_12_o_2[3:1], register_2_q_3, register_2_q_2, gt4add3_15_o[0], gt4add3_14_o[0], register_2_q}));
  gt4add3 gt4add3_8 (.O(gt4add3_8_o), .I(gt4add3_9_o));
  gt4add3 gt4add3_9 (.O({gt4add3_9_o_2[3], gt4add3_9_o[3:1]}), .I(gt4add3_12_o_2));
  gt4add3 gt4add3_10 (.O(gt4add3_10_o), .I(gt4add3_11_o));
  gt4add3 gt4add3_11 (.O({gt4add3_9_o[0], gt4add3_11_o[3:1]}), .I(gt4add3_12_o));
  gt4add3 gt4add3_12 (.O({gt4add3_12_o_2[0], gt4add3_12_o[3:1]}), .I(register_2_q_3));
  gt4add3 gt4add3_13 (.O(gt4add3_13_o), .I(gt4add3_14_o));
  gt4add3 gt4add3_14 (.O({gt4add3_11_o[0], gt4add3_14_o[3:1]}), .I(gt4add3_15_o));
  gt4add3 gt4add3_15 (.O({gt4add3_12_o[0], gt4add3_15_o[3:1]}), .I(register_2_q_2));
  Register #(.Bits(20)) register_3 (
    .D({register_2_q_4[3], gt4add3_9_o_2[3], gt4add3_8_o, gt4add3_10_o, gt4add3_13_o, register_2_q}),
    .C(clock), .en(1'b1), .Q({gt4add3_20_o[19:17], register_3_q_2, gt4add3_20_o[4:3], register_3_q}));
  gt4add3 gt4add3_16 (.O(gt4add3_17_o_2[18:15]), .I(gt4add3_17_o[18:15]));
  gt4add3 gt4add3_17 (.O({gt4add3_17_o_2[19], gt4add3_17_o[18:16]}), .I(gt4add3_20_o[19:16]));
  gt4add3 gt4add3_18 (.O(gt4add3_17_o_2[14:11]), .I(gt4add3_17_o[14:11]));
  gt4add3 gt4add3_19 (.O(gt4add3_17_o[15:12]), .I(gt4add3_20_o[15:12]));
  gt4add3 gt4add3_20 (.O(gt4add3_20_o[16:13]), .I(register_3_q_2[16:13]));
  gt4add3 gt4add3_21 (.O(gt4add3_17_o_2[10:7]), .I(gt4add3_17_o[10:7]));
  gt4add3 gt4add3_22 (.O(gt4add3_17_o[11:8]), .I(gt4add3_20_o[11:8]));
  gt4add3 gt4add3_23 (.O(gt4add3_20_o[12:9]), .I(register_3_q_2[12:9]));
  gt4add3 gt4add3_24 (.O(gt4add3_17_o_2[6:3]), .I({gt4add3_17_o[6:4], gt4add3_20_o[3]}));
  gt4add3 gt4add3_25 (.O(gt4add3_17_o[7:4]), .I(gt4add3_20_o[7:4]));
  gt4add3 gt4add3_26 (.O(gt4add3_20_o[8:5]), .I(register_3_q_2[8:5]));
  Register #(.Bits(20)) register_4 (
    .D({gt4add3_17_o_2, register_3_q}), .C(clock), .en(1'b1),
    .Q({O[19:18], register_4_q_4, register_4_q_3, register_4_q_2, register_4_q, gt4add3_34_o[0], O[0]}));
  gt4add3 gt4add3_27 (.O(O[16:13]), .I(gt4add3_28_o));
  gt4add3 gt4add3_28 (.O({O[17], gt4add3_28_o[3:1]}), .I(register_4_q_4));
  gt4add3 gt4add3_29 (.O(O[12:9]), .I(gt4add3_30_o));
  gt4add3 gt4add3_30 (.O({gt4add3_28_o[0], gt4add3_30_o[3:1]}), .I(register_4_q_3));
  gt4add3 gt4add3_31 (.O(O[8:5]), .I(gt4add3_32_o));
  gt4add3 gt4add3_32 (.O({gt4add3_30_o[0], gt4add3_32_o[3:1]}), .I(register_4_q_2));
  gt4add3 gt4add3_33 (.O(O[4:1]), .I(gt4add3_34_o));
  gt4add3 gt4add3_34 (.O({gt4add3_32_o[0], gt4add3_34_o[3:1]}), .I(register_4_q));

  // Other names for the same wires on the sheet: C = clock

  // Notes on the sheet:
  //   I: default 51384
  //   clock: Hz: 50
endmodule
