// Digital circuit busdisplay.dig as structural Verilog
module busdisplay (
  input  [25:0] i,
  input  H,
  input  [1:0] C,
  output [3:0] D1,
  output P1,
  output [3:0] D2,
  output P2,
  output [25:0] o,
  output [3:0] D3,
  output P3,
  output [3:0] D4,
  output P4,
  output [3:0] D5,
  output P5
);

  wire aluop2ascii_1_l_v, aluop2ascii_1_r_v, aluop2ascii_1_res_v, ctrldec_1_p3, debugval_1_p4,
       hexdisplay_1_p3;
  wire [2:0] ctrldec_1_p2;
  wire [7:0] multiplexer_1_out;
  wire [15:0] debugval_2_q;
  wire [25:0] debugval_1_p3;

  Multiplexer #(.Selector_Bits(2), .Bits(8)) multiplexer_1 (
    .sel(C), .in_0(8'h16), .in_1(8'h12), .in_2(8'h13), .in_3(8'h14), .out(multiplexer_1_out));
  // debugval debugval_1: pin names not known; wires that end beside it: i, multiplexer_1_out, debugval_1_p3, debugval_1_p4
  // hexdisplay hexdisplay_1: pin names not known; wires that end beside it: D1, P1, hexdisplay_1_p3, D2, P2, D3, debugval_1_p4, P3, D4, P4, H, D5, P5
  debugval debugval_2 (.db_i(debugval_1_p3), .sel(8'h11), .db_o(o), .Q(debugval_2_q));
  // ctrldec ctrldec_1: pin names not known; wires that end beside it: debugval_2_q, ctrldec_1_p2, ctrldec_1_p3
  aluop2ascii aluop2ascii_1 (
    .I({1'b0, ctrldec_1_p2}), .L_v(aluop2ascii_1_l_v), .R_v(aluop2ascii_1_r_v), .res_v(aluop2ascii_1_res_v));  // open: L0, L1, L2, L3
  Multiplexer #(.Selector_Bits(2)) multiplexer_2 (
    .sel(C), .in_0(ctrldec_1_p3), .in_1(aluop2ascii_1_l_v), .in_2(aluop2ascii_1_r_v),
    .in_3(aluop2ascii_1_res_v), .out(hexdisplay_1_p3));

  // Notes on the sheet:
  //   16: imm
  //   12: L
  //   13: R
  //   14: res
endmodule
