// Digital circuit bussplitter.dig as structural Verilog
module bussplitter (
  input  ready,
  input  [7:0] addr_in,
  input  [15:0] bus_in,
  input  [3:0] sel,
  input  [15:0] in_0,
  input  valid_0,
  input  [15:0] in_1,
  input  valid_1,
  input  [15:0] in_2,
  input  valid_2,
  input  [15:0] in_3,
  input  valid_3,
  output [15:0] bus_out,
  output valid,
  output ready_0,
  output ready_1,
  output ready_2,
  output ready_3,
  output [3:0] addr_out
);

  wire active_eq, and_1_out, multiplexer_2_out;
  wire [15:0] multiplexer_1_out;

  Comparator #(.Bits(4)) active (.a(addr_in[7:4]), .b(sel), .eq(active_eq));  // open: gt, lt
  and and_1 (and_1_out, ready, active_eq);
  Multiplexer #(.Selector_Bits(2), .Bits(16)) multiplexer_1 (
    .sel(addr_in[3:2]), .in_0(in_0), .in_1(in_1), .in_2(in_2), .in_3(in_3), .out(multiplexer_1_out));
  Multiplexer #(.Selector_Bits(2)) multiplexer_2 (
    .sel(addr_in[3:2]), .in_0(valid_0), .in_1(valid_1), .in_2(valid_2), .in_3(valid_3),
    .out(multiplexer_2_out));
  Demultiplexer #(.Selector_Bits(2)) demultiplexer_1 (
    .sel(addr_in[3:2]), .in(and_1_out), .out_0(ready_0), .out_1(ready_1), .out_2(ready_2), .out_3(ready_3));
  Multiplexer #(.Bits(16)) multiplexer_3 (.sel(active_eq), .in_0(bus_in), .in_1(multiplexer_1_out), .out(bus_out));
  and and_2 (valid, active_eq, multiplexer_2_out);

  assign addr_out = addr_in[3:0];
endmodule
