// Digital circuit control.dig as structural Verilog
module control (
  input  [4:0] op,
  input  stall,
  input  clock,
  input  skip_n,
  input  ack,
  output [2:0] aluop,
  output [2:0] cond,
  output skip,
  output halt,
  output error,
  output en_write,
  output mem,
  output store,
  output en_fetch,
  output jump,
  output write,
  output [1:0] wrmux
);

  wire and_1_out, and_4_out, busy, d_ff_1_q, en_skip, imm, nnbusy_t, or_2_out;
  wire [0:0] flags;
  wire [4:0] Microcode_d_2, Microcode_d_3;
  wire [5:0] mcsequencer_1_uop;
  wire [21:0] Microcode_d;

  mcsequencer mcsequencer_1 (
    .op(op), .clock(clock), .en(en_write), .flags({2'b00, flags[0]}), .fmask(Microcode_d[21:19]),
    .next_t(Microcode_d_2), .next_f(Microcode_d_3), .uop(mcsequencer_1_uop), .nnbusy(nnbusy_t), .busy(busy));
  and and_1 (and_1_out, mem, flags[0]);
  ROM #(.AddrBits(6), .Bits(32)) Microcode (
    .A(mcsequencer_1_uop), .sel(1'b1),
    .D({Microcode_d_3, Microcode_d_2, Microcode_d[21:15], imm, cond, wrmux, write, store, mem, aluop, jump, Microcode_d[1:0]}));
  D_FF d_ff_1 (.D(and_1_out), .C(clock), .Q(d_ff_1_q));  // open: nQ
  or or_1 (flags[0], ack, d_ff_1_q);
  and and_2 (halt, en_write, Microcode_d[0]);
  and and_3 (error, Microcode_d[1], en_write);
  or or_2 (or_2_out, and_4_out, skip_n);
  // Probe skip_n on skip_n
  // Probe busy on busy
  and and_4 (and_4_out, imm, skip);
  Register u_skip (.D(or_2_out), .C(clock), .en(en_skip), .Q(skip));
  or or_3 (en_skip, ~stall, busy);  // Or
  // Probe ~nbusy on nnbusy_t
  // Probe skip on skip
  // Probe en_skip on en_skip
  and and_5 (en_write, ~skip, en_skip);  // And
  and and_6 (en_fetch, en_skip, nnbusy_t);
  // Probe en_write on en_write
  // Probe en_fetch on en_fetch

  // Other names for the same wires on the sheet: C = clock; en_state = en_write

  // Notes on the sheet:
  //   contents of Microcode (hex, n*v repeats v):
  //   0,0,8400002,10800001,604,0,700,0,4,4000,304,4000,20c80040,314800c0,540,c0,100,108,
  //   100,108,128,130,138,118,110,120,808,1008,1808,2008,2808,3008,0,8400002,10800001,500,
  //   20c80040,0,314800c0
  //   Halt Logic
  //   Stall Logic
  //   Skip Logic
endmodule

/* Test case ALU Ops:
op      stall aluop jump halt error mem store write wrmux
0b10000 0     0     0    0    0     0   0     1     0
0b01000 0     0     0    0    0     0   0     0     0
0b10110 0     2     0    0    0     0   0     1     0
0b01011 0     0     0    0    0     0   0     0     0
0b10110 1     2     0    0    0     0   0     1     0
0b10001 1     1     0    0    0     0   0     1     0
*/

/* Test case Halt:
op      stall clock skip_n aluop jump halt error mem store

# with stall and skip clear
0b00010 0     0     0      0     0    0    1     0   0
0b00011 0     0     0      0     0    1    0     0   0

# with skip set
0b00010 0     1     1      0     0    0    0     0   0
0b00011 0     1     1      0     0    0    0     0   0

# reset skip
0b00011 0     0     0      0     0    0    0     0   0
0b00011 0     1     0      0     0    1    0     0   0

# check stall
0b00010 1     0     0      0     0    0    0     0   0
0b00011 1     0     0      0     0    0    0     0   0
0b00010 1     1     1      0     0    0    0     0   0
0b00011 1     1     1      0     0    0    0     0   0
*/

/* Test case Jump:
op      stall clock skip_n aluop jump en_fetch halt error mem store
0b11100 0     0     0      0     1    1        0    0     0   0

# stalled
0b11100 1     0     0      0     1    0        0    0     0   0
*/

/* Test case Mem Access:
op      stall aluop jump halt error mem store write wrmux

0b11110 0     0     0    0    0     1   0     1     2 
0b11111 0     0     0    0    0     1   1     0     0

0b11110 1     0     0    0    0     1   0     1     2
0b11111 1     0     0    0    0     1   1     0     0
*/

/* Test case Skip:
op      stall clock skip_n skip en_write en_fetch
0b00000 0     0     0      0    1        1

# skip stays low when stalled
0b00000 1     0     1      0    0        0
0b00000 1     1     1      0    0        0

# skip updates when stall goes low
0b00000 0     0     1      0    1        1
0b00000 0     1     1      1    0        1

# skip stays high when stalled
0b00000 1     0     0      1    0        0
0b00000 1     1     0      1    0        0

# skip stays high if kept high with skip_n
0b00000 0     0     1      1    0        1
0b00000 0     1     1      1    0        1

# skip goes back low after skip_n goes low
0b00000 0     0     0      1    0        1
0b00000 0     1     0      0    1        1
*/
