// Digital circuit ctrlbreakout.dig as structural Verilog
module ctrlbreakout (
  input  [33:0] ctrl,
  output [3:0] rs,
  output rsvalid,
  output [3:0] rd,
  output jump,
  output rdvalid,
  output [2:0] cond,
  output [4:0] op,
  output immvalid,
  output [1:0] wrmux,
  output en,
  output en_fetch,
  output write,
  output store,
  output mem,
  output [2:0] aluop,
  output error,
  output halt,
  output skip,
  output stall
);


  assign aluop = ctrl[7:5];
  assign cond = ctrl[23:21];
  assign en = ctrl[12];
  assign en_fetch = ctrl[11];
  assign error = ctrl[3];
  assign halt = ctrl[2];
  assign immvalid = ctrl[15];
  assign jump = ctrl[4];
  assign mem = ctrl[8];
  assign op = ctrl[20:16];
  assign rd = ctrl[28:25];
  assign rdvalid = ctrl[24];
  assign rs = ctrl[33:30];
  assign rsvalid = ctrl[29];
  assign skip = ctrl[1];
  assign stall = ctrl[0];
  assign store = ctrl[9];
  assign write = ctrl[10];
  assign wrmux = ctrl[14:13];
endmodule
