// Digital circuit ctrldec.dig as structural Verilog
module ctrldec (
  input  [15:0] ctrl,
  output stall,
  output skip,
  output halt,
  output error,
  output jump,
  output [2:0] aluop,
  output mem,
  output store,
  output write,
  output en_fetch,
  output en,
  output rdvalid,
  output rsvalid,
  output immv
);


  assign aluop = ctrl[7:5];
  assign en = ctrl[12];
  assign en_fetch = ctrl[11];
  assign error = ctrl[3];
  assign halt = ctrl[2];
  assign immv = ctrl[15];
  assign jump = ctrl[4];
  assign mem = ctrl[8];
  assign rdvalid = ctrl[13];
  assign rsvalid = ctrl[14];
  assign skip = ctrl[1];
  assign stall = ctrl[0];
  assign store = ctrl[9];
  assign write = ctrl[10];
endmodule
