// Digital circuit datamemio.dig as structural Verilog
module datamemio (
  input  we,
  input  [15:0] A,
  input  [15:0] D_in,
  input  req,
  input  clk,
  output ack,
  output [15:0] D_out
);

  wire ack2, and_1_out, and_2_out, comparator_1_eq, d_ff_3_q, d_ff_4_nq, demultiplexer_1_out_1, or_1_out,
       req1, req2, telnet_1_av;
  wire [7:0] d_ff_1_q, telnet_1_out;
  wire [15:0] Data_2_d;

  and and_1 (and_1_out, req2, we);
  and and_2 (and_2_out, req2, ~we, telnet_1_av);  // And
  // Probe data on D_in
  // Probe telnetwr on and_1_out
  or or_1 (or_1_out, and_1_out, and_2_out);
  // Probe addr on A
  BlockRAMDualPort #(.AddrBits(16), .Bits(16)) Data_2 (.A(A), .Din(D_in), .str(we), .C(clk), .D(Data_2_d));
  Telnet #(.port(2323)) telnet_1 (
    .in(D_in[7:0]), .C(clk), .wr(and_1_out), .rd(and_2_out), .out(telnet_1_out), .av(telnet_1_av));
  Comparator #(.Bits(16)) comparator_1 (.a(A), .b(16'h8000), .eq(comparator_1_eq));  // open: gt, lt
  D_FF #(.Bits(8)) d_ff_1 (.D(telnet_1_out), .C(clk), .Q(d_ff_1_q));  // open: nQ
  D_FF d_ff_2 (.D(or_1_out), .C(clk), .Q(ack2));  // open: nQ
  Multiplexer #(.Bits(16)) multiplexer_1 (
    .sel(comparator_1_eq), .in_0(Data_2_d), .in_1({{8{1'b0}}, d_ff_1_q}), .out(D_out));
  // Probe req on req
  Demultiplexer demultiplexer_1 (.sel(comparator_1_eq), .in(req), .out_0(req1), .out_1(demultiplexer_1_out_1));
  D_FF d_ff_3 (.D(req), .C(clk), .Q(d_ff_3_q));  // open: nQ
  D_FF d_ff_4 (.D(demultiplexer_1_out_1), .C(clk), .nQ(d_ff_4_nq));  // open: Q
  and and_3 (req2, demultiplexer_1_out_1, d_ff_4_nq);
  Multiplexer multiplexer_2 (.sel(comparator_1_eq), .in_0(d_ff_3_q), .in_1(ack2), .out(ack));
  // Probe ack on ack

  // Other names for the same wires on the sheet: C = clk
endmodule
