// Digital circuit debugbus.dig as structural Verilog
module debugbus (
  input  db_ready,
  input  clock,
  input  [15:0] ctrl,
  input  [15:0] wrval,
  input  [15:0] result,
  input  [15:0] L,
  input  [15:0] R,
  input  [15:0] imm,
  input  [15:0] pc,
  input  [15:0] fullop,
  input  [15:0] rdf,
  input  [15:0] rsf,
  output [25:0] db
);

  wire debugmux_1_ready_out, debugmux_1_valid_out, debugregs_1_ready_out, debugregs_1_valid_out;
  wire [7:0] Addr_Enumerator_out, debugmux_1_addr_out, debugregs_1_addr_out;
  wire [15:0] debugmux_1_data_out, debugregs_1_data_out;

  Counter #(.Bits(8)) Addr_Enumerator (
    .en(db_ready), .C(clock), .clr(~db[16]), .out(Addr_Enumerator_out));  // open: ovf
  debugregs debugregs_1 (
    .data_in({16{1'b0}}), .valid_in(1'b0), .addr_in(Addr_Enumerator_out), .ready_in(db_ready),
    .write(ctrl[10]), .en(ctrl[12]), .clock(clock), .rd(rdf[3:0]), .wrval(wrval), .sel({8{1'b0}}),
    .data_out(debugregs_1_data_out), .valid_out(debugregs_1_valid_out), .addr_out(debugregs_1_addr_out),
    .ready_out(debugregs_1_ready_out));
  debugmux debugmux_1 (
    .data_in(debugregs_1_data_out), .valid_in(debugregs_1_valid_out), .addr_in(debugregs_1_addr_out),
    .ready_in(debugregs_1_ready_out), .sel(8'h10), .in_0(fullop), .in_1(ctrl), .in_2(L), .in_3(R),
    .in_4(result), .in_5(wrval), .in_6(imm), .in_7(pc), .data_out(debugmux_1_data_out),
    .valid_out(debugmux_1_valid_out), .addr_out(debugmux_1_addr_out), .ready_out(debugmux_1_ready_out));
  debugmux debugmux_2 (
    .data_in(debugmux_1_data_out), .valid_in(debugmux_1_valid_out), .addr_in(debugmux_1_addr_out),
    .ready_in(debugmux_1_ready_out), .sel(8'h18), .in_0(rdf), .in_1(rsf), .in_2({16{1'b0}}),
    .in_3({16{1'b0}}), .in_4({16{1'b0}}), .in_5({16{1'b0}}), .in_6({16{1'b0}}), .in_7({16{1'b0}}),
    .data_out(db[15:0]), .valid_out(db[16]), .addr_out(db[24:17]));  // open: ready_out

  assign db[25] = clock;

  // Other names for the same wires on the sheet: C = clock

  // Notes on the sheet:
  //   clock: Hz: 2
  //   Memory Map:
  //   00-0F: registers
  //   10: ?
  //   11: ctrl
  //   12: L
  //   13: R
  //   14: result
  //   15: wrval
  //   16: imm
  //   17: pc
  //   18: fullop
  //   19: rdf
  //   20: rsf
endmodule
