// Digital circuit debugcopy.dig as structural Verilog
module debugcopy (
  input  [25:0] db,
  input  clock,
  input  e,
  input  rdy,
  output [21:0] db_new,
  output [15:0] decode,
  output [15:0] ctrl
);

  wire and_1_out;
  wire [24:0] register_1_q, register_2_q, register_3_q;
  wire [25:0] debugval_1_db_o;

  Register #(.Bits(25)) register_1 (.D(db[24:0]), .C(db[25]), .en(1'b1), .Q(register_1_q));
  Register #(.Bits(25)) register_2 (.D(register_1_q), .C(clock), .en(1'b1), .Q(register_2_q));
  Register #(.Bits(25)) register_3 (.D(register_2_q), .C(clock), .en(1'b1), .Q(register_3_q));
  and and_1 (and_1_out, e, register_3_q[16]);
  debugval debugval_1 (.db_i({clock, register_3_q}), .sel(8'h17), .db_o(debugval_1_db_o), .Q(decode));
  Counter #(.Bits(5)) Enum (.en(rdy), .C(clock), .clr(~db_new[16]), .out(db_new[21:17]));  // open: ovf
  RAMDualAccess #(.AddrBits(5), .Bits(17)) DB_Copy (
    .str(and_1_out), .C(clock), .ld(1'b0), .A1(register_3_q[21:17]), .Din1(register_3_q[16:0]),
    .A2(db_new[21:17]), .D2(db_new[16:0]));  // open: D1
  debugval debugval_2 (.db_i(debugval_1_db_o), .sel(8'h18), .Q(ctrl));  // open: db_o

  // Other names for the same wires on the sheet: C = clock
endmodule
