// Digital circuit debugmux.dig as structural Verilog
module debugmux (
  input  [15:0] data_in,
  input  valid_in,
  input  [7:0] addr_in,
  input  ready_in,
  input  [7:0] sel,
  input  [15:0] in_0,
  input  [15:0] in_1,
  input  [15:0] in_2,
  input  [15:0] in_3,
  input  [15:0] in_4,
  input  [15:0] in_5,
  input  [15:0] in_6,
  input  [15:0] in_7,
  output [15:0] data_out,
  output valid_out,
  output [7:0] addr_out,
  output ready_out
);

  wire active_eq;
  wire [15:0] multiplexer_1_out;

  Comparator #(.Bits(5)) active (.a(addr_in[7:3]), .b(sel[7:3]), .eq(active_eq));  // open: gt, lt
  Multiplexer #(.Selector_Bits(3), .Bits(16)) multiplexer_1 (
    .sel(addr_in[2:0]), .in_0(in_0), .in_1(in_1), .in_2(in_2), .in_3(in_3), .in_4(in_4), .in_5(in_5),
    .in_6(in_6), .in_7(in_7), .out(multiplexer_1_out));
  Multiplexer #(.Bits(16)) multiplexer_2 (.sel(active_eq), .in_0(data_in), .in_1(multiplexer_1_out), .out(data_out));
  or or_1 (valid_out, active_eq, valid_in);

  assign addr_out = addr_in;
  assign ready_out = ready_in;
endmodule
