// Digital circuit debugreg.dig as structural Verilog
module debugreg (
  input  [38:0] i,
  input  [4:0] s_0,
  input  [38:0] o,
  input  [4:0] s_1,
  input  [4:0] s_2,
  input  [4:0] s_3,
  input  [4:0] s_4,
  input  [4:0] s_5,
  output [15:0] v_0,
  output [15:0] v_1,
  output [15:0] v_2,
  output [15:0] v_3,
  output [15:0] v_4,
  output [15:0] v_5
);

  wire and_1_out, and_2_out, and_3_out, and_4_out, and_5_out, and_6_out, comparator_1_eq, comparator_2_eq,
       comparator_3_eq, comparator_4_eq, comparator_5_eq, comparator_6_eq;
  wire [15:0] register_1_q, register_2_q, register_3_q, register_4_q, register_5_q, register_6_q;

  Comparator #(.Bits(4)) comparator_1 (.a(i[19:16]), .b(s_0[3:0]), .eq(comparator_1_eq));  // open: gt, lt
  Comparator #(.Bits(4)) comparator_2 (.a(i[19:16]), .b(s_1[3:0]), .eq(comparator_2_eq));  // open: gt, lt
  Comparator #(.Bits(4)) comparator_3 (.a(i[19:16]), .b(s_2[3:0]), .eq(comparator_3_eq));  // open: gt, lt
  Comparator #(.Bits(4)) comparator_4 (.a(i[19:16]), .b(s_3[3:0]), .eq(comparator_4_eq));  // open: gt, lt
  Comparator #(.Bits(4)) comparator_5 (.a(i[19:16]), .b(s_4[3:0]), .eq(comparator_5_eq));  // open: gt, lt
  Comparator #(.Bits(4)) comparator_6 (.a(i[19:16]), .b(s_5[3:0]), .eq(comparator_6_eq));  // open: gt, lt
  and and_1 (and_1_out, i[21], i[20], comparator_1_eq);
  and and_2 (and_2_out, i[21], i[20], comparator_2_eq);
  and and_3 (and_3_out, i[21], i[20], comparator_3_eq);
  and and_4 (and_4_out, i[21], i[20], comparator_4_eq);
  and and_5 (and_5_out, i[21], i[20], comparator_5_eq);
  and and_6 (and_6_out, i[21], i[20], comparator_6_eq);
  Register #(.Bits(16)) register_1 (.D(i[15:0]), .C(i[38]), .en(and_1_out), .Q(register_1_q));
  Register #(.Bits(16)) register_2 (.D(i[15:0]), .C(i[38]), .en(and_2_out), .Q(register_2_q));
  Register #(.Bits(16)) register_3 (.D(i[15:0]), .C(i[38]), .en(and_3_out), .Q(register_3_q));
  Register #(.Bits(16)) register_4 (.D(i[15:0]), .C(i[38]), .en(and_4_out), .Q(register_4_q));
  Register #(.Bits(16)) register_5 (.D(i[15:0]), .C(i[38]), .en(and_5_out), .Q(register_5_q));
  Register #(.Bits(16)) register_6 (.D(i[15:0]), .C(i[38]), .en(and_6_out), .Q(register_6_q));
  Multiplexer #(.Bits(16)) multiplexer_1 (.sel(s_0[4]), .in_0(register_1_q), .in_1(i[37:22]), .out(v_0));
  Multiplexer #(.Bits(16)) multiplexer_2 (.sel(s_1[4]), .in_0(register_2_q), .in_1(i[37:22]), .out(v_1));
  Multiplexer #(.Bits(16)) multiplexer_3 (.sel(s_2[4]), .in_0(register_3_q), .in_1(i[37:22]), .out(v_2));
  Multiplexer #(.Bits(16)) multiplexer_4 (.sel(s_3[4]), .in_0(register_4_q), .in_1(i[37:22]), .out(v_3));
  Multiplexer #(.Bits(16)) multiplexer_5 (.sel(s_4[4]), .in_0(register_5_q), .in_1(i[37:22]), .out(v_4));
  Multiplexer #(.Bits(16)) multiplexer_6 (.sel(s_5[4]), .in_0(register_6_q), .in_1(i[37:22]), .out(v_5));

  assign o = i;

  // Other names for the same wires on the sheet: wrval_t[15:0] = i[15:0]; rd_t[3:0] = i[19:16]; en = i[20];
  //   write_t = i[21]; PC_t[15:0] = i[37:22]; C = i[38]
endmodule
