// Digital circuit debugregcopy.dig as structural Verilog
module debugregcopy (
  input  [25:0] db,
  input  [4:0] b,
  input  e,
  output [15:0] o0,
  output [15:0] o1,
  output [15:0] o2,
  output [15:0] o3,
  output [15:0] o4,
  output [15:0] o5,
  output [15:0] o6,
  output [15:0] o7
);

  wire and_1_out, comparator_1_eq, demultiplexer_1_out_0, demultiplexer_1_out_1, demultiplexer_1_out_2,
       demultiplexer_1_out_3, demultiplexer_1_out_4, demultiplexer_1_out_5, demultiplexer_1_out_6,
       demultiplexer_1_out_7;
  wire [15:0] register_1_q, register_2_q, register_3_q, register_4_q, register_5_q, register_6_q,
       register_7_q, register_8_q;

  Comparator #(.Bits(5)) comparator_1 (.a(db[24:20]), .b(b), .eq(comparator_1_eq));  // open: gt, lt
  and and_1 (and_1_out, comparator_1_eq, db[16]);
  Demultiplexer #(.Selector_Bits(3)) demultiplexer_1 (
    .sel(db[19:17]), .in(and_1_out), .out_0(demultiplexer_1_out_0), .out_1(demultiplexer_1_out_1),
    .out_2(demultiplexer_1_out_2), .out_3(demultiplexer_1_out_3), .out_4(demultiplexer_1_out_4),
    .out_5(demultiplexer_1_out_5), .out_6(demultiplexer_1_out_6), .out_7(demultiplexer_1_out_7));
  Register #(.Bits(16)) register_1 (.D(db[15:0]), .C(db[25]), .en(demultiplexer_1_out_0), .Q(register_1_q));
  Register #(.Bits(16)) register_2 (.D(db[15:0]), .C(db[25]), .en(demultiplexer_1_out_1), .Q(register_2_q));
  Register #(.Bits(16)) register_3 (.D(db[15:0]), .C(db[25]), .en(demultiplexer_1_out_2), .Q(register_3_q));
  Register #(.Bits(16)) register_4 (.D(db[15:0]), .C(db[25]), .en(demultiplexer_1_out_3), .Q(register_4_q));
  Register #(.Bits(16)) register_5 (.D(db[15:0]), .C(db[25]), .en(demultiplexer_1_out_4), .Q(register_5_q));
  Register #(.Bits(16)) register_6 (.D(db[15:0]), .C(db[25]), .en(demultiplexer_1_out_5), .Q(register_6_q));
  Register #(.Bits(16)) register_7 (.D(db[15:0]), .C(db[25]), .en(demultiplexer_1_out_6), .Q(register_7_q));
  Register #(.Bits(16)) register_8 (.D(db[15:0]), .C(db[25]), .en(demultiplexer_1_out_7), .Q(register_8_q));
  Register #(.Bits(16)) register_9 (.D(register_1_q), .C(db[25]), .en(e), .Q(o0));
  Register #(.Bits(16)) register_10 (.D(register_2_q), .C(db[25]), .en(e), .Q(o1));
  Register #(.Bits(16)) register_11 (.D(register_3_q), .C(db[25]), .en(e), .Q(o2));
  Register #(.Bits(16)) register_12 (.D(register_4_q), .C(db[25]), .en(e), .Q(o3));
  Register #(.Bits(16)) register_13 (.D(register_5_q), .C(db[25]), .en(e), .Q(o4));
  Register #(.Bits(16)) register_14 (.D(register_6_q), .C(db[25]), .en(e), .Q(o5));
  Register #(.Bits(16)) register_15 (.D(register_7_q), .C(db[25]), .en(e), .Q(o6));
  Register #(.Bits(16)) register_16 (.D(register_8_q), .C(db[25]), .en(e), .Q(o7));

  // Other names for the same wires on the sheet: C = db[25]
endmodule
