// Digital circuit debugregs.dig as structural Verilog
module debugregs (
  input  [15:0] data_in,
  input  valid_in,
  input  [7:0] addr_in,
  input  ready_in,
  input  write,
  input  en,
  input  clock,
  input  [3:0] rd,
  input  [15:0] wrval,
  input  [7:0] sel,
  output [15:0] data_out,
  output valid_out,
  output [7:0] addr_out,
  output ready_out
);

  wire active_eq, and_1_out;
  wire [15:0] ramdualaccess_1_d2;

  and and_1 (and_1_out, en, write);
  RAMDualAccess #(.AddrBits(4), .Bits(16)) ramdualaccess_1 (
    .str(and_1_out), .C(clock), .ld(1'b0), .A1(rd), .Din1(wrval), .A2(addr_in[3:0]), .D2(ramdualaccess_1_d2));  // open: D1
  Comparator #(.Bits(4)) active (.a(addr_in[7:4]), .b(sel[7:4]), .eq(active_eq));  // open: gt, lt
  Multiplexer #(.Bits(16)) multiplexer_1 (.sel(active_eq), .in_0(data_in), .in_1(ramdualaccess_1_d2), .out(data_out));
  or or_1 (valid_out, active_eq, valid_in);

  assign addr_out = addr_in;
  assign ready_out = ready_in;
endmodule
