// Digital circuit debugrender.dig as structural Verilog
module debugrender (
  input  [21:0] db,
  input  clock,
  input  hex,
  input  \signed ,
  output fb_valid,
  output [8:0] fb_A,
  output [7:0] fb_D,
  output rdy
);

  wire and_1_out, and_2_out, and_3_out, comparator_1_eq, not_1_out, num_eq, or_1_out, register_5_q;
  wire [1:0] register_3_q, Type_d, wait_out;
  wire [2:0] digit_out, Length_d, register_2_q;
  wire [6:0] multiplexer_1_out, num2ascii_1_char, vga_opdisp_1_char, vga_regdisp_1_char;
  wire [8:0] add_1_s, Offset_d, register_4_q;
  wire [15:0] register_1_q;

  ROM #(.AddrBits(5), .Bits(2)) Type (.A(db[21:17]), .sel(1'b1), .D(Type_d));
  ROM #(.AddrBits(5), .Bits(9)) Offset (.A(db[21:17]), .sel(1'b1), .D(Offset_d));
  Comparator #(.Bits(2)) num (.a(2'b00), .b(Type_d), .eq(num_eq));  // open: gt, lt
  ROM #(.Bits(3)) Length (.A(Type_d), .sel(1'b1), .D(Length_d));
  and and_1 (and_1_out, ~hex, num_eq);  // And
  or or_1 (or_1_out, ~and_1_out, and_2_out);  // Or
  Counter #(.Bits(2)) \wait  (.en(~and_2_out), .C(clock), .clr(rdy), .out(wait_out));  // open: ovf
  and and_2 (and_2_out, wait_out[0], wait_out[1]);
  Register #(.Bits(16)) register_1 (.D(db[15:0]), .C(clock), .en(rdy), .Q(register_1_q));
  Counter #(.Bits(3)) digit (.en(or_1_out), .C(clock), .clr(rdy), .out(digit_out));  // open: ovf
  Register #(.Bits(3)) register_2 (.D(Length_d), .C(clock), .en(rdy), .Q(register_2_q));
  Register #(.Bits(2)) register_3 (.D(Type_d), .C(clock), .en(rdy), .Q(register_3_q));
  Register #(.Bits(9)) register_4 (.D(Offset_d), .C(clock), .en(rdy), .Q(register_4_q));
  Register register_5 (.D(db[16]), .C(clock), .en(1'b1), .Q(register_5_q));
  Comparator #(.Bits(3)) Done (.a(digit_out), .b(register_2_q), .eq(rdy));  // open: gt, lt
  Comparator #(.Bits(9)) comparator_1 (.a(register_4_q), .b({9{1'b0}}), .eq(comparator_1_eq));  // open: gt, lt
  not not_1 (not_1_out, comparator_1_eq);
  Add #(.Bits(9)) add_1 (.a({{6{1'b0}}, digit_out}), .b(register_4_q), .c_i(1'b0), .s(add_1_s));  // open: c_o
  and and_3 (and_3_out, not_1_out, register_5_q);
  num2ascii num2ascii_1 (
    .num(register_1_q), .s(\signed ), .hex(hex), .clock(clock), .digit(digit_out), .char(num2ascii_1_char));
  vga_opdisp vga_opdisp_1 (.fullop(register_1_q), .digit(digit_out), .char(vga_opdisp_1_char));
  vga_regdisp vga_regdisp_1 (.\reg (register_1_q), .digit(digit_out), .char(vga_regdisp_1_char));
  Multiplexer #(.Selector_Bits(2), .Bits(7)) multiplexer_1 (
    .sel(register_3_q), .in_0(num2ascii_1_char), .in_1(vga_opdisp_1_char), .in_2(vga_regdisp_1_char),
    .in_3({7{1'b0}}), .out(multiplexer_1_out));
  Register #(.Bits(7)) register_6 (.D(multiplexer_1_out), .C(clock), .en(1'b1), .Q(fb_D[6:0]));
  Register #(.Bits(9)) register_7 (.D(add_1_s), .C(clock), .en(1'b1), .Q(fb_A));
  Register register_8 (.D(and_3_out), .C(clock), .en(1'b1), .Q(fb_valid));

  assign fb_D[7] = 1'b0;

  // Other names for the same wires on the sheet: C = clock; db_data[15:0] = db[15:0]; db_valid = db[16];
  //   db_addr[4:0] = db[21:17]

  // Notes on the sheet:
  //   contents of Type (hex, n*v repeats v):
  //   0,0,0,0,0,0,0,0,0,0,0,0,0,0,0,0,1,0,0,0,0,0,0,0,2,2
  //   contents of Offset (hex, n*v repeats v):
  //   21,41,61,81,29,49,69,89,31,51,71,91,39,59,79,99,c1,0,111,119,109,0,d9,141,cc,d4
  //   contents of Length (hex, n*v repeats v):
  //   5,7,2,1
endmodule
