// Digital circuit debugval.dig as structural Verilog
module debugval (
  input  [25:0] db_i,
  input  [7:0] sel,
  output [25:0] db_o,
  output [15:0] Q
);

  wire and_1_out, comparator_1_eq;

  Comparator #(.Bits(8)) comparator_1 (.a(db_i[24:17]), .b(sel), .eq(comparator_1_eq));  // open: gt, lt
  and and_1 (and_1_out, db_i[16], comparator_1_eq);
  Register #(.Bits(16)) register_1 (.D(db_i[15:0]), .C(db_i[25]), .en(and_1_out), .Q(Q));

  assign db_o = db_i;
endmodule
