// Digital circuit decodedec.dig as structural Verilog
module decodedec (
  input  [15:0] D,
  output [4:0] op,
  output [2:0] cond,
  output [3:0] rs,
  output [3:0] rd
);


  assign cond = D[15:13];
  assign op = D[12:8];
  assign rd = D[3:0];
  assign rs = D[7:4];
endmodule
