// Digital circuit decoder.dig as structural Verilog
module decoder (
  input  [15:0] rdval,
  input  [15:0] rsval,
  input  [15:0] instr,
  output [1:0] rs,
  output [1:0] rd,
  output [15:0] L,
  output [15:0] R,
  output [2:0] cond,
  output [4:0] op,
  output rs_valid,
  output rd_valid
);

  wire cond_valid, imm_valid, mem;
  wire [3:2] multiplexer_6_out, multiplexer_7_out;
  wire [15:0] imm5, imm6, imm8, imm12, multiplexer_2_out, multiplexer_3_out;

  BitExtender #(.inputBits(5)) bitextender_1 (.in(instr[11:7]), .out(imm5));
  BitExtender #(.inputBits(6)) bitextender_2 (.in(instr[11:6]), .out(imm6));
  BitExtender bitextender_3 (.in(instr[11:4]), .out(imm8));
  BitExtender #(.inputBits(12)) bitextender_4 (.in(instr[15:4]), .out(imm12));
  Multiplexer #(.Bits(3)) multiplexer_1 (.sel(cond_valid), .in_0(3'b000), .in_1(instr[6:4]), .out(cond));
  Multiplexer #(.Selector_Bits(3), .Bits(16)) multiplexer_2 (
    .sel(instr[2:0]), .in_0({16{1'b0}}), .in_1(imm6), .in_2({16{1'b0}}), .in_3(imm5), .in_4(imm8),
    .in_5(imm12), .in_6({{11{1'b0}}, instr[7:3]}), .in_7({{11{1'b0}}, instr[7:3]}), .out(multiplexer_2_out));
  instdecoder instdecoder_1 (
    .fmt(instr[2:0]), .op0(instr[7:3]), .op(op), .rd_valid(rd_valid), .rs_valid(rs_valid),
    .imm_valid(imm_valid), .mem(mem), .cond_valid(cond_valid));
  Multiplexer #(.Bits(16)) multiplexer_3 (.sel(rs_valid), .in_0({16{1'b0}}), .in_1(rsval), .out(multiplexer_3_out));
  Multiplexer #(.Bits(16)) multiplexer_4 (.sel(imm_valid), .in_0(multiplexer_3_out), .in_1(multiplexer_2_out), .out(R));
  Multiplexer #(.Bits(16)) multiplexer_5 (.sel(mem), .in_0(rdval), .in_1(multiplexer_2_out), .out(L));
  Multiplexer #(.Bits(4)) multiplexer_6 (
    .sel(rs_valid), .in_0(4'b0000), .in_1(instr[11:8]), .out({multiplexer_6_out, rs}));
  Multiplexer #(.Bits(4)) multiplexer_7 (
    .sel(rd_valid), .in_0(4'b0000), .in_1(instr[15:12]), .out({multiplexer_7_out, rd}));

  // Other names for the same wires on the sheet: fmt[2:0] = instr[2:0]; off5[4:0] = instr[7:3]; op0[4:0] = instr[7:3];
  //   rs_i[3:0] = instr[11:8]; rd_i[3:0] = instr[15:12]
endmodule

/* Test case ls:
instr               rsval rs rdval rd L       R  op       
0b0000000010101110  2     0  2     0  0b10101 2  0b11110  
0b0000000000000111  3     0  2     0  0b00000 3  0b11111  
0b1111000010001110  4     0  2     3  0b10001 4  0b11110  
0b0000111110001111  5     3  2     0  0b10001 5  0b11111  
   
*/

/* Test case rr:
instr               rsval rs rdval rd L R op 
0b0000000000000000  5     0  2     0  2 5 0  
0b0011000011111000  5     0  2     3  2 5 31 
0b0011001110000000  5     3  2     3  2 5 16 
*/

/* Test case ri8:
instr               rsval rs rdval rd L R      op       
0b0000000000000100  5     0  1     0  1 0      0b11010  
0b1111000011111100  5     0  2     3  2 0xf    0b11011  
0b0011111100010100  5     0  3     3  3 0xfff1 0b11010  
0b0010011110110100  5     0  4     2  4 0x7b   0b11010  
*/

/* Test case i12:
instr               rsval rs rdval rd L R      op       
0b0000000000000101  5     0  2     0  2 0      0b11100   
0b0000000000011101  5     0  2     0  2 1      0b11101  
0b0100000000011101  5     0  2     0  2 0x401  0b11101   
0b1111111111011101  5     0  2     0  2 0xFFFD 0b11101  
 
*/

/* Test case ri6:
instr               rsval rs rdval rd L R      op       
0b0000000000000001  5     0  1     0  1 0      0b10000  
0b1111000011111001  5     0  2     3  2 3      0b10111  
0b0011110001010001  5     0  3     3  3 0xfff1 0b10010  
0b0010000101110001  5     0  4     2  4 5      0b10110  
*/

/* Test case ric:
instr               rsval rs rdval rd L R      op       cond
0b0000000000000011  5     0  1     0  1 0      0b11000  0b000
0b1111000111101011  5     0  2     3  2 3      0b11001  0b110
0b0011100010010011  5     0  3     3  3 0xfff1 0b11000  0b001
0b0010001011110011  5     0  4     2  4 5      0b11000  0b111
*/

/* Test case rrc:
instr               rsval rs rdval rd L R op       cond
0b0000000000000010  5     0  1     0  1 5 0b11000  0
0b0011000011111010  4     0  2     3  2 4 0b11001  7
0b0011001111010010  3     3  3     3  3 3 0b11000  5
*/
