// Digital circuit digit2ascii.dig as structural Verilog
module digit2ascii (
  input  [3:0] D,
  output [6:0] A
);

  Multiplexer #(.Selector_Bits(4), .Bits(7)) multiplexer_1 (
    .sel(D), .in_0(7'b0110000), .in_1(7'b0110001), .in_2(7'b0110010), .in_3(7'b0110011), .in_4(7'b0110100),
    .in_5(7'b0110101), .in_6(7'b0110110), .in_7(7'b0110111), .in_8(7'b0111000), .in_9(7'b0111001),
    .in_10(7'b1000001), .in_11(7'b1000010), .in_12(7'b1000011), .in_13(7'b1000100), .in_14(7'b1000101),
    .in_15(7'b1000110), .out(A));
endmodule
