// Digital circuit digit2asciiskip.dig as structural Verilog
module digit2asciiskip (
  input  [3:0] i,
  input  s_i,
  output [6:0] a,
  output s_o
);

  wire [6:0] digit2ascii_1_a;

  or or_1 (s_o, s_i, i[0], i[1], i[2], i[3]);
  digit2ascii digit2ascii_1 (.D(i), .A(digit2ascii_1_a));
  Multiplexer #(.Bits(7)) multiplexer_1 (.sel(s_o), .in_0(7'b0100000), .in_1(digit2ascii_1_a), .out(a));
endmodule
