// Digital circuit div10.dig as structural Verilog
module div10 (
  input  [15:0] N,
  output [12:0] Q,
  output [3:0] R
);

  wire not_1_out, sub_2_c_o;
  wire [4:0] sub_2_s;
  wire [7:0] add_3_s, add_3_s_2;
  wire [15:0] add_1_s, add_2_s, sub_1_s;
  wire [15:1] add_4_s;
  wire [15:15] add_4_s_2;

  Add #(.Bits(16)) add_1 (.a({1'b0, N[15:1]}), .b({2'b00, N[15:2]}), .c_i(1'b0), .s(add_1_s));  // open: c_o
  Add #(.Bits(16)) add_2 (.a({add_3_s_2, add_3_s}), .b({{8{1'b0}}, add_3_s_2}), .c_i(1'b0), .s(add_2_s));  // open: c_o
  Sub #(.Bits(16)) sub_1 (.a(N), .b({add_4_s, 1'b0}), .c_i(1'b0), .s(sub_1_s));  // open: c_o
  Add #(.Bits(16)) add_3 (
    .a(add_1_s), .b({4'b0000, add_1_s[15:4]}), .c_i(1'b0), .s({add_3_s_2, add_3_s}));  // open: c_o
  Sub #(.Bits(5)) sub_2 (.a(sub_1_s[4:0]), .b(5'b01010), .c_i(1'b0), .s(sub_2_s), .c_o(sub_2_c_o));
  Add #(.Bits(16)) add_4 (
    .a({3'b000, add_2_s[15:3]}), .b({1'b0, add_2_s[15:3], 2'b00}), .c_i(1'b0), .s({add_4_s_2[15], add_4_s}));  // open: c_o
  not not_1 (not_1_out, sub_2_c_o);
  Add #(.Bits(13)) add_5 (.a(add_2_s[15:3]), .b({13{1'b0}}), .c_i(not_1_out), .s(Q));  // open: c_o
  Multiplexer #(.Bits(4)) multiplexer_1 (.sel(sub_2_c_o), .in_0(sub_2_s[3:0]), .in_1(sub_1_s[3:0]), .out(R));

  // Notes on the sheet:
  //   N: default 58581
endmodule
