// Digital circuit execute.dig as structural Verilog
module execute (
  input  [15:0] L,
  input  [15:0] R,
  input  [2:0] cond,
  input  [2:0] op,
  output [15:0] result,
  output skip_n
);

  wire add_1_c_o, and_3_out, and_4_out, and_5_out, and_6_out, and_7_out, and_8_out, and_9_out, eq, ge, hs,
       lo, lt, ne, not_2_out, not_3_out, or_1_out, signed_eq, signed_gt, signed_lt;
  wire [1:0] and_2_out;
  wire [3:0] and_1_out;
  wire [7:0] nor_1_out;
  wire [15:0] add_1_s, multiplexer_1_out, not_1_out, xor_1_out;

  Decoder #(.Selector_Bits(3)) decoder_1 (
    .sel(cond), .out_1(eq), .out_2(ne), .out_3(lt), .out_4(ge), .out_5(lo), .out_6(hs));  // open: out_0, out_7
  assign xor_1_out = L ^ R;  // XOr xor_1, 16 bits wide
  Multiplexer #(.Bits(16)) multiplexer_1 (.sel(op[2]), .in_0(R), .in_1(not_1_out), .out(multiplexer_1_out));
  assign not_1_out = ~R;  // Not not_1, 16 bits wide
  assign nor_1_out = ~(xor_1_out[7:0] | xor_1_out[15:8]);  // NOr nor_1, 8 bits wide
  Add #(.Bits(16)) add_1 (.a(L), .b(multiplexer_1_out), .c_i(op[2]), .s(add_1_s), .c_o(add_1_c_o));
  assign and_1_out = nor_1_out[3:0] & nor_1_out[7:4];  // And and_1, 4 bits wide
  assign and_2_out = and_1_out[1:0] & and_1_out[3:2];  // And and_2, 2 bits wide
  Comparator #(.Signed("true"), .Bits(16)) \signed  (.a(L), .b(R), .gt(signed_gt), .eq(signed_eq), .lt(signed_lt));
  and and_3 (and_3_out, and_2_out[0], and_2_out[1]);
  or or_1 (or_1_out, signed_gt, signed_eq);
  not not_2 (not_2_out, add_1_c_o);
  not not_3 (not_3_out, and_3_out);
  Multiplexer #(.Selector_Bits(2), .Bits(16)) multiplexer_2 (
    .sel(op[1:0]), .in_0(L), .in_1(add_1_s), .in_2({16{1'b0}}), .in_3(multiplexer_1_out), .out(result));
  and and_4 (and_4_out, lt, or_1_out);
  and and_5 (and_5_out, ge, signed_lt);
  and and_6 (and_6_out, lo, add_1_c_o);
  and and_7 (and_7_out, hs, not_2_out);
  and and_8 (and_8_out, ne, and_3_out);
  and and_9 (and_9_out, eq, not_3_out);
  or or_2 (skip_n, and_4_out, and_5_out, and_6_out, and_7_out, and_8_out, and_9_out);

  // Notes on the sheet:
  //   Equal / Zero Detector
endmodule
