// Digital circuit fetch.dig as structural Verilog
module fetch (
  input  [15:0] instr_i,
  input  clock,
  input  fetch,
  input  jump,
  input  [15:0] value,
  input  en,
  output [15:0] instr_o,
  output [7:0] pc
);

  wire and_1_out, and_2_out;
  wire [15:0] multiplexer_1_out;

  and and_1 (and_1_out, jump, en);
  Multiplexer #(.Bits(16)) multiplexer_1 (.sel(and_1_out), .in_0(instr_i), .in_1({16{1'b0}}), .out(multiplexer_1_out));
  and and_2 (and_2_out, fetch, and_1_out);
  Register #(.Bits(16)) IR (.D(multiplexer_1_out), .C(clock), .en(fetch), .Q(instr_o));
  CounterPreset #(.Bits(8), .isProgramCounter("true")) u_PC (
    .en(fetch), .C(clock), .dir(1'b0), .in(value[7:0]), .ld(and_2_out), .clr(1'b0), .out(pc));  // open: ovf
endmodule
