// Digital circuit frontpanel.dig as structural Verilog
module frontpanel (
  input  clock,
  input  erun,
  output [15:0] PC,
  output halt,
  output error
);

  wire aluopdisplay_1_p1, aluopdisplay_1_p2, busdisplay_1_p3, busdisplay_1_p6, busdisplay_1_p9,
       busdisplay_1_p11, busdisplay_1_p14, busdisplay_2_p1, busdisplay_2_p2, busdisplay_2_p3,
       busdisplay_2_p4, busdisplay_2_p5, busdisplay_3_p3, busdisplay_3_p6, busdisplay_3_p10,
       busdisplay_3_p12, busdisplay_3_p15, busdisplay_4_p1, busdisplay_4_p2, busdisplay_4_p3,
       busdisplay_4_p4, busdisplay_4_p5, comparator_1_eq, datamemio_1_ack, hex, instrdisplay_1_p1,
       instrdisplay_1_p2, instrdisplay_1_p3, instrdisplay_1_p4, instrdisplay_1_p5, instrdisplay_1_p6, MC,
       rddisplay_1_p3, rddisplay_1_p6, rddisplay_1_p8, rddisplay_1_p9, rddisplay_2_p1, rddisplay_2_p2,
       rddisplay_2_p3, rddisplay_3_p5, rddisplay_3_p8, rddisplay_3_p10, rddisplay_3_p11, rj32_1_req,
       rj32_1_w_en, run_t, skip, slow_t, stalled_t, step_t;
  wire [3:0] busdisplay_1_p2, busdisplay_1_p5, busdisplay_1_p7, busdisplay_1_p10, busdisplay_1_p13,
       busdisplay_2_d1, busdisplay_2_d2, busdisplay_2_d3, busdisplay_2_d4, busdisplay_2_d5, busdisplay_3_p2,
       busdisplay_3_p5, busdisplay_3_p8, busdisplay_3_p11, busdisplay_3_p14, busdisplay_4_d1,
       busdisplay_4_d2, busdisplay_4_d3, busdisplay_4_d4, busdisplay_4_d5;
  wire [9:0] rj32_1_a_prog;
  wire [15:0] aluopdisplay_1_d1, aluopdisplay_1_d2, datamemio_1_d_out, debugreg_1_v_1, debugreg_1_v_2,
       debugreg_1_v_3, debugreg_1_v_4, debugreg_2_v_0, debugreg_2_v_1, debugreg_2_v_2, debugreg_2_v_3,
       debugreg_2_v_4, debugreg_2_v_5, debugreg_3_v_0, debugreg_3_v_1, debugreg_3_v_2, debugreg_3_v_3,
       debugreg_3_v_4, debugreg_3_v_5, instrdisplay_1_d1, instrdisplay_1_d2, instrdisplay_1_d3,
       instrdisplay_1_d4, instrdisplay_1_d5, instrdisplay_1_d6, Program_d, rddisplay_1_p2, rddisplay_1_p4,
       rddisplay_1_p7, rddisplay_2_d1, rddisplay_2_d2, rddisplay_2_d3, rddisplay_3_p4, rddisplay_3_p6,
       rddisplay_3_p9, rj32_1_a_data, rj32_1_d_out;
  wire [25:0] ctrl, instrdisplay_1_o, rddisplay_2_o;
  wire [33:0] busdisplay_1_p15, busdisplay_2_o, busdisplay_3_p7;
  wire [38:0] \reg ;
  wire [63:0] bus;

  Comparator #(.Bits(16)) comparator_1 (.a(PC), .b(16'hea), .eq(comparator_1_eq));  // open: gt, lt
  BlockRAMDualPort #(.AddrBits(10), .isProgramMemory("true"), .Bits(16)) Program (
    .A(rj32_1_a_prog), .Din({16{1'b0}}), .str(1'b0), .C(MC), .D(Program_d));
  Break #(.Cycles(1000000)) break_1 (.brk(comparator_1_eq));
  Button step (.out(step_t));
  Button slow (.out(slow_t));
  Button run (.out(run_t));
  LED stalled (.in(stalled_t));
  SixteenSeg sixteenseg_1 (.led(rddisplay_1_p2), .dp(rddisplay_1_p3));
  // rddisplay rddisplay_1: pin names not known; wires that end beside it: ctrl, rddisplay_1_p2, rddisplay_1_p3, rddisplay_1_p4, 1'b0, rddisplay_1_p6, rddisplay_1_p7, rddisplay_1_p8, rddisplay_1_p9
  rj32 rj32_1 (
    .erun(erun), .run_faster(1'b1), .run_fast(run_t), .run_slow(slow_t), .step(step_t), .clock(clock),
    .\reg (\reg ), .A_prog(rj32_1_a_prog), .D_prog(Program_d), .clock_m(MC), .w_en(rj32_1_w_en),
    .D_out(rj32_1_d_out), .A_data(rj32_1_a_data), .D_in(datamemio_1_d_out), .req(rj32_1_req),
    .ack(datamemio_1_ack));  // open: stall, skip, halt, error, db, bus, ctrl
  datamemio datamemio_1 (
    .we(rj32_1_w_en), .D_in(rj32_1_d_out), .A(rj32_1_a_data), .D_out(datamemio_1_d_out), .req(rj32_1_req),
    .ack(datamemio_1_ack), .clk(clock));
  SixteenSeg sixteenseg_2 (.led(instrdisplay_1_d1), .dp(instrdisplay_1_p1));
  SixteenSeg sixteenseg_3 (.led(instrdisplay_1_d2), .dp(instrdisplay_1_p2));
  instrdisplay instrdisplay_1 (
    .D1(instrdisplay_1_d1), .P1(instrdisplay_1_p1), .D2(instrdisplay_1_d2), .P2(instrdisplay_1_p2),
    .D3(instrdisplay_1_d3), .P3(instrdisplay_1_p3), .D4(instrdisplay_1_d4), .P4(instrdisplay_1_p4),
    .D5(instrdisplay_1_d5), .P5(instrdisplay_1_p5), .D6(instrdisplay_1_d6), .P6(instrdisplay_1_p6), .i(ctrl),
    .o(instrdisplay_1_o));
  SixteenSeg sixteenseg_4 (.led(rddisplay_1_p4), .dp(rddisplay_1_p6));
  SixteenSeg sixteenseg_5 (.led(rddisplay_1_p7), .dp(rddisplay_1_p8));
  SixteenSeg sixteenseg_6 (.led(instrdisplay_1_d3), .dp(instrdisplay_1_p3));
  SixteenSeg sixteenseg_7 (.led(instrdisplay_1_d4), .dp(instrdisplay_1_p4));
  Seven_Seg_Hex seven_seg_hex_1 (.d(busdisplay_1_p2), .dp(busdisplay_1_p3));
  // busdisplay busdisplay_1: pin names not known; wires that end beside it: rddisplay_1_p9, busdisplay_1_p2, busdisplay_1_p3, bus, busdisplay_1_p5, busdisplay_1_p6, busdisplay_1_p7, 2'b11, busdisplay_1_p9, busdisplay_1_p10, busdisplay_1_p11, hex, busdisplay_1_p13, busdisplay_1_p14, busdisplay_1_p15
  SixteenSeg sixteenseg_8 (.led(instrdisplay_1_d5), .dp(instrdisplay_1_p5));
  SixteenSeg sixteenseg_9 (.led(instrdisplay_1_d6), .dp(instrdisplay_1_p6));
  Seven_Seg_Hex seven_seg_hex_2 (.d(busdisplay_1_p5), .dp(busdisplay_1_p6));
  Seven_Seg_Hex seven_seg_hex_3 (.d(busdisplay_1_p7), .dp(busdisplay_1_p9));
  SixteenSeg sixteenseg_10 (.led(rddisplay_2_d1), .dp(rddisplay_2_p1));
  Seven_Seg_Hex seven_seg_hex_4 (.d(busdisplay_1_p10), .dp(busdisplay_1_p11));
  Seven_Seg_Hex seven_seg_hex_5 (.d(busdisplay_1_p13), .dp(busdisplay_1_p14));
  SixteenSeg sixteenseg_11 (.led(rddisplay_2_d2), .dp(rddisplay_2_p2));
  SixteenSeg sixteenseg_12 (.led(rddisplay_2_d3), .dp(rddisplay_2_p3));
  rddisplay rddisplay_2 (
    .D1(rddisplay_2_d1), .P1(rddisplay_2_p1), .D2(rddisplay_2_d2), .P2(rddisplay_2_p2), .D3(rddisplay_2_d3),
    .P3(rddisplay_2_p3), .i(instrdisplay_1_o), .o(rddisplay_2_o), .C(1'b1));
  Seven_Seg_Hex seven_seg_hex_6 (.d(busdisplay_2_d1), .dp(busdisplay_2_p1));
  busdisplay busdisplay_2 (
    .D1(busdisplay_2_d1), .P1(busdisplay_2_p1), .D2(busdisplay_2_d2), .P2(busdisplay_2_p2),
    .D3(busdisplay_2_d3), .P3(busdisplay_2_p3), .D4(busdisplay_2_d4), .P4(busdisplay_2_p4),
    .D5(busdisplay_2_d5), .P5(busdisplay_2_p5), .i(busdisplay_1_p15), .o(busdisplay_2_o), .B(bus), .S(2'b01),
    .H(hex));
  SixteenSeg sixteenseg_13 (.led(rddisplay_3_p4), .dp(rddisplay_3_p5));
  Seven_Seg_Hex seven_seg_hex_7 (.d(busdisplay_2_d2), .dp(busdisplay_2_p2));
  Seven_Seg_Hex seven_seg_hex_8 (.d(busdisplay_2_d3), .dp(busdisplay_2_p3));
  debugreg debugreg_1 (
    .i(\reg ), .s_0(5'b10001), .s_1({5{1'b0}}), .s_2(5'b01101), .s_3(5'b01110), .s_4(5'b01111),
    .s_5({5{1'b0}}), .v_0(PC), .v_1(debugreg_1_v_1), .v_2(debugreg_1_v_2), .v_3(debugreg_1_v_3),
    .v_4(debugreg_1_v_4));  // open: v_5, o
  SixteenSeg sixteenseg_14 (.led(rddisplay_3_p6), .dp(rddisplay_3_p8));
  SixteenSeg sixteenseg_15 (.led(rddisplay_3_p9), .dp(rddisplay_3_p10));
  // rddisplay rddisplay_3: pin names not known; wires that end beside it: bus, ctrl, rddisplay_2_o, rddisplay_3_p4, rddisplay_3_p5, rddisplay_3_p6, 1'b0, rddisplay_3_p8, rddisplay_3_p9, rddisplay_3_p10, rddisplay_3_p11, busdisplay_2_o
  Seven_Seg_Hex seven_seg_hex_9 (.d(busdisplay_2_d4), .dp(busdisplay_2_p4));
  Seven_Seg_Hex seven_seg_hex_10 (.d(busdisplay_2_d5), .dp(busdisplay_2_p5));
  // Probe RA on debugreg_1_v_1
  // Probe FP on debugreg_1_v_2
  // Probe BP on debugreg_1_v_3
  // Probe SP on debugreg_1_v_4
  Seven_Seg_Hex seven_seg_hex_11 (.d(busdisplay_3_p2), .dp(busdisplay_3_p3));
  SixteenSeg sixteenseg_16 (.led(aluopdisplay_1_d1), .dp(aluopdisplay_1_p1));
  aluopdisplay aluopdisplay_1 (
    .D1(aluopdisplay_1_d1), .P1(aluopdisplay_1_p1), .D2(aluopdisplay_1_d2), .P2(aluopdisplay_1_p2));  // open: I, Q, R, L
  Seven_Seg_Hex seven_seg_hex_12 (.d(busdisplay_3_p5), .dp(busdisplay_3_p6));
  Seven_Seg_Hex seven_seg_hex_13 (.d(busdisplay_3_p8), .dp(busdisplay_3_p10));
  // busdisplay busdisplay_3: pin names not known; wires that end beside it: rddisplay_3_p11, busdisplay_3_p2, busdisplay_3_p3, bus, busdisplay_3_p5, busdisplay_3_p6, busdisplay_3_p7, busdisplay_3_p8, 2'b00, busdisplay_3_p10, busdisplay_3_p11, busdisplay_3_p12, hex, busdisplay_3_p14, busdisplay_3_p15
  SixteenSeg sixteenseg_17 (.led(aluopdisplay_1_d2), .dp(aluopdisplay_1_p2));
  debugreg debugreg_2 (
    .i(\reg ), .s_0(5'b00001), .s_1(5'b00010), .s_2(5'b00011), .s_3(5'b00100), .s_4(5'b00101),
    .s_5(5'b00110), .v_0(debugreg_2_v_0), .v_1(debugreg_2_v_1), .v_2(debugreg_2_v_2), .v_3(debugreg_2_v_3),
    .v_4(debugreg_2_v_4), .v_5(debugreg_2_v_5));  // open: o
  Seven_Seg_Hex seven_seg_hex_14 (.d(busdisplay_3_p11), .dp(busdisplay_3_p12));
  Seven_Seg_Hex seven_seg_hex_15 (.d(busdisplay_3_p14), .dp(busdisplay_3_p15));
  Seven_Seg_Hex seven_seg_hex_16 (.d(busdisplay_4_d1), .dp(busdisplay_4_p1));
  Seven_Seg_Hex seven_seg_hex_17 (.d(busdisplay_4_d2), .dp(busdisplay_4_p2));
  busdisplay busdisplay_4 (
    .D1(busdisplay_4_d1), .P1(busdisplay_4_p1), .D2(busdisplay_4_d2), .P2(busdisplay_4_p2),
    .D3(busdisplay_4_d3), .P3(busdisplay_4_p3), .D4(busdisplay_4_d4), .P4(busdisplay_4_p4),
    .D5(busdisplay_4_d5), .P5(busdisplay_4_p5), .i(busdisplay_3_p7), .B(bus), .S(2'b10), .H(hex));  // open: o
  // Probe R1_a0 on debugreg_2_v_0
  // Probe R2_a1 on debugreg_2_v_1
  // Probe R3_a2 on debugreg_2_v_2
  // Probe R4_s0 on debugreg_2_v_3
  // Probe R5_s1 on debugreg_2_v_4
  // Probe R6_s2 on debugreg_2_v_5
  Seven_Seg_Hex seven_seg_hex_18 (.d(busdisplay_4_d3), .dp(busdisplay_4_p3));
  Seven_Seg_Hex seven_seg_hex_19 (.d(busdisplay_4_d4), .dp(busdisplay_4_p4));
  Seven_Seg_Hex seven_seg_hex_20 (.d(busdisplay_4_d5), .dp(busdisplay_4_p5));
  debugreg debugreg_3 (
    .i(\reg ), .s_0(5'b00111), .s_1(5'b01000), .s_2(5'b01001), .s_3(5'b01010), .s_4(5'b01011),
    .s_5(5'b01100), .v_0(debugreg_3_v_0), .v_1(debugreg_3_v_1), .v_2(debugreg_3_v_2), .v_3(debugreg_3_v_3),
    .v_4(debugreg_3_v_4), .v_5(debugreg_3_v_5));  // open: o
  // Probe R7_s3 on debugreg_3_v_0
  // Probe R8_t0 on debugreg_3_v_1
  // Probe R9_t1 on debugreg_3_v_2
  // Probe R10_t2 on debugreg_3_v_3
  // Probe R11_t3 on debugreg_3_v_4
  // Probe R12_t4 on debugreg_3_v_5
  DipSwitch u_hex (.out(hex));
  LED u_skip (.in(skip));

  // Other names for the same wires on the sheet: C = clock

  // Notes on the sheet:
  //   clock: Hz: 5
  //   rj45 Creates
  //   =
endmodule
