// Digital circuit funnelshifter.dig as structural Verilog
module funnelshifter (
  input  [15:0] I,
  input  [3:0] amt,
  input  dir,
  input  arith,
  output [15:0] O
);

  wire add_1_c_o;
  wire [3:0] add_1_s, multiplexer_4_out, not_1_out;
  wire [15:0] bitextender_1_out, multiplexer_1_out, multiplexer_2_out, multiplexer_3_out, multiplexer_6_out;
  wire [18:0] multiplexer_5_out;

  BitExtender #(.inputBits(1)) bitextender_1 (.in(I[15]), .out(bitextender_1_out));
  Multiplexer #(.Bits(16)) multiplexer_1 (
    .sel(arith), .in_0({16{1'b0}}), .in_1(bitextender_1_out), .out(multiplexer_1_out));
  Multiplexer #(.Bits(16)) multiplexer_2 (.sel(dir), .in_0(I), .in_1(multiplexer_1_out), .out(multiplexer_2_out));
  Multiplexer #(.Bits(16)) multiplexer_3 (.sel(dir), .in_0(multiplexer_1_out), .in_1(I), .out(multiplexer_3_out));
  Multiplexer #(.Bits(4)) multiplexer_4 (.sel(dir), .in_0(amt), .in_1(not_1_out), .out(multiplexer_4_out));
  assign not_1_out = ~amt;  // Not not_1, 4 bits wide
  Add #(.Bits(4)) add_1 (.a(4'b0000), .b(multiplexer_4_out), .c_i(dir), .s(add_1_s), .c_o(add_1_c_o));
  Multiplexer #(.Selector_Bits(2), .Bits(19)) multiplexer_5 (
    .sel(add_1_s[3:2]), .in_0({multiplexer_3_out[2:0], multiplexer_2_out}),
    .in_1({multiplexer_3_out[6:0], multiplexer_2_out[15:4]}),
    .in_2({multiplexer_3_out[10:0], multiplexer_2_out[15:8]}),
    .in_3({multiplexer_3_out[14:0], multiplexer_2_out[15:12]}), .out(multiplexer_5_out));
  Multiplexer #(.Selector_Bits(2), .Bits(16)) multiplexer_6 (
    .sel(add_1_s[1:0]), .in_0(multiplexer_5_out[15:0]), .in_1(multiplexer_5_out[16:1]),
    .in_2(multiplexer_5_out[17:2]), .in_3(multiplexer_5_out[18:3]), .out(multiplexer_6_out));
  Multiplexer #(.Bits(16)) multiplexer_7 (.sel(add_1_c_o), .in_0(multiplexer_6_out), .in_1(multiplexer_3_out), .out(O));
endmodule
