// Digital circuit gt4add3.dig as structural Verilog
module gt4add3 (
  input  [3:0] I,
  output [3:0] O
);

  wire nand_1_out, nand_2_out, nand_3_out, nand_4_out, nand_5_out, nand_6_out, nand_7_out, nand_8_out,
       nand_9_out, nand_10_out, nand_11_out, nand_12_out, nand_13_out, not_1_out, not_2_out, not_3_out,
       not_4_out;

  not not_1 (not_1_out, I[3]);
  not not_2 (not_2_out, I[2]);
  not not_3 (not_3_out, I[1]);
  not not_4 (not_4_out, I[0]);
  nand nand_1 (nand_1_out, I[0], I[2], not_1_out);
  nand nand_2 (nand_2_out, not_4_out, not_3_out, I[3]);
  nand nand_3 (nand_3_out, I[1], I[2], not_1_out);
  nand nand_4 (nand_4_out, not_2_out, I[3]);
  nand nand_5 (nand_5_out, not_4_out, not_3_out, I[2]);
  nand nand_6 (nand_6_out, I[0], not_2_out, I[3]);
  nand nand_7 (nand_7_out, I[1], not_2_out, I[3]);
  nand nand_8 (nand_8_out, I[0], I[1]);
  nand nand_9 (nand_9_out, not_4_out, not_3_out, I[3]);
  nand nand_10 (nand_10_out, I[1], not_2_out, not_1_out);
  nand nand_11 (nand_11_out, I[0], not_2_out, not_1_out);
  nand nand_12 (nand_12_out, not_4_out, I[1], I[2]);
  nand nand_13 (nand_13_out, not_4_out, I[3]);
  nand nand_14 (O[3], nand_1_out, nand_2_out, nand_3_out, nand_4_out);
  nand nand_15 (O[2], nand_5_out, nand_6_out, nand_7_out);
  nand nand_16 (O[1], nand_8_out, nand_9_out, nand_10_out);
  nand nand_17 (O[0], nand_11_out, nand_12_out, nand_13_out);

  // Other names for the same wires on the sheet: I_0 = I[0]; I_1 = I[1]; I_2 = I[2]; I_3 = I[3]; O_0 = O[0];
  //   O_1 = O[1]; O_2 = O[2]; O_3 = O[3]
endmodule
