// Digital circuit hexdisplay.dig as structural Verilog
module hexdisplay (
  input  E,
  input  [31:0] V,
  output [3:0] D1,
  output P1,
  output [3:0] D2,
  output P2,
  output [3:0] D3,
  output P3,
  output [3:0] D4,
  output P4,
  output [3:0] D5,
  output P5,
  output [3:0] D6,
  output P6,
  output [3:0] D7,
  output P7,
  output [3:0] D8,
  output P8
);

  wire and_1_out, and_2_out, and_3_out, and_4_out, and_5_out, and_6_out, and_7_out, comparator_1_gt,
       comparator_2_gt, comparator_3_gt, comparator_4_gt, comparator_5_gt, comparator_6_gt, comparator_7_gt,
       or_1_out, or_2_out, or_3_out, or_4_out, or_5_out, or_6_out, or_7_out;
  wire [2:0] priorityencoder_1_num;

  Comparator #(.Bits(3)) comparator_1 (.a(priorityencoder_1_num), .b(3'b110), .gt(comparator_1_gt));  // open: eq, lt
  and and_1 (and_1_out, comparator_1_gt, E);
  assign D1 = and_1_out ? V[31:28] : 4'bz;  // Driver driver_1
  or or_1 (or_1_out, V[28], V[29], V[30], V[31]);
  Comparator #(.Bits(3)) comparator_2 (.a(priorityencoder_1_num), .b(3'b101), .gt(comparator_2_gt));  // open: eq, lt
  and and_2 (and_2_out, comparator_2_gt, E);
  assign D2 = and_2_out ? V[27:24] : 4'bz;  // Driver driver_2
  or or_2 (or_2_out, V[24], V[25], V[26], V[27]);
  Comparator #(.Bits(3)) comparator_3 (.a(priorityencoder_1_num), .b(3'b100), .gt(comparator_3_gt));  // open: eq, lt
  and and_3 (and_3_out, comparator_3_gt, E);
  assign D3 = and_3_out ? V[23:20] : 4'bz;  // Driver driver_3
  or or_3 (or_3_out, V[20], V[21], V[22], V[23]);
  Comparator #(.Bits(3)) comparator_4 (.a(priorityencoder_1_num), .b(3'b011), .gt(comparator_4_gt));  // open: eq, lt
  and and_4 (and_4_out, comparator_4_gt, E);
  assign D4 = and_4_out ? V[19:16] : 4'bz;  // Driver driver_4
  or or_4 (or_4_out, V[16], V[17], V[18], V[19]);
  Comparator #(.Bits(3)) comparator_5 (.a(priorityencoder_1_num), .b(3'b010), .gt(comparator_5_gt));  // open: eq, lt
  and and_5 (and_5_out, comparator_5_gt, E);
  assign D5 = and_5_out ? V[15:12] : 4'bz;  // Driver driver_5
  or or_5 (or_5_out, V[12], V[13], V[14], V[15]);
  Comparator #(.Bits(3)) comparator_6 (.a(priorityencoder_1_num), .b(3'b001), .gt(comparator_6_gt));  // open: eq, lt
  and and_6 (and_6_out, comparator_6_gt, E);
  assign D6 = and_6_out ? V[11:8] : 4'bz;  // Driver driver_6
  or or_6 (or_6_out, V[8], V[9], V[10], V[11]);
  Comparator #(.Bits(3)) comparator_7 (.a(priorityencoder_1_num), .b(3'b000), .gt(comparator_7_gt));  // open: eq, lt
  and and_7 (and_7_out, comparator_7_gt, E);
  assign D7 = and_7_out ? V[7:4] : 4'bz;  // Driver driver_7
  or or_7 (or_7_out, V[4], V[5], V[6], V[7]);
  assign D8 = E ? V[3:0] : 4'bz;  // Driver driver_8
  PriorityEncoder #(.Selector_Bits(3)) priorityencoder_1 (
    .in0(1'b0), .in1(or_7_out), .in2(or_6_out), .in3(or_5_out), .in4(or_4_out), .in5(or_3_out),
    .in6(or_2_out), .in7(or_1_out), .num(priorityencoder_1_num));  // open: any

  assign P1 = 1'b0;
  assign P2 = 1'b0;
  assign P3 = 1'b0;
  assign P4 = 1'b0;
  assign P5 = 1'b0;
  assign P6 = 1'b0;
  assign P7 = 1'b0;
  assign P8 = 1'b0;
endmodule
