// Digital circuit instdecoder.dig as structural Verilog
module instdecoder (
  input  [2:0] fmt,
  input  [4:0] op0,
  output [4:0] op,
  output rd_valid,
  output rs_valid,
  output imm_valid,
  output mem,
  output cond_valid
);

  wire decoder_1_out_6, decoder_1_out_7, i12, ri6, ri8, ric, rr, rrc;

  Decoder #(.Selector_Bits(3)) decoder_1 (
    .sel(fmt), .out_0(rr), .out_1(ri6), .out_2(rrc), .out_3(ric), .out_4(ri8), .out_5(i12),
    .out_6(decoder_1_out_6), .out_7(decoder_1_out_7));
  or or_1 (mem, decoder_1_out_6, decoder_1_out_7);
  Multiplexer #(.Selector_Bits(3), .Bits(5)) multiplexer_1 (
    .sel(fmt), .in_0(op0), .in_1({2'b10, op0[2:0]}), .in_2({4'b1100, op0[0]}), .in_3({4'b1100, op0[0]}),
    .in_4({4'b1101, op0[0]}), .in_5({4'b1110, op0[0]}), .in_6({4'b1111, fmt[0]}), .in_7({4'b1111, fmt[0]}),
    .out(op));
  or or_2 (rs_valid, mem, rrc, rr);
  not not_1 (rd_valid, i12);
  nor nor_1 (imm_valid, rr, rrc, mem);
  or or_3 (cond_valid, ric, rrc);

  // Other names for the same wires on the sheet: ls = mem
endmodule
