// Digital circuit mcsequencer.dig as structural Verilog
module mcsequencer (
  input  [4:0] op,
  input  clock,
  input  en,
  input  [2:0] flags,
  input  [2:0] fmask,
  input  [4:0] next_t,
  input  [4:0] next_f,
  output [5:0] uop,
  output nnbusy,
  output busy
);

  wire nnbusy_eq, not_1_out, op_eq, true_eq;
  wire [2:0] and_1_out;
  wire [4:0] multiplexer_1_out, step_q;

  assign and_1_out = flags & fmask;  // And and_1, 3 bits wide
  Multiplexer #(.Bits(5)) multiplexer_1 (.sel(true_eq), .in_0(next_f), .in_1(next_t), .out(multiplexer_1_out));
  Comparator #(.Bits(3)) true (.a(and_1_out), .b(fmask), .eq(true_eq));  // open: gt, lt
  Comparator #(.Bits(5)) u_nnbusy (.a(multiplexer_1_out), .b({5{1'b0}}), .eq(nnbusy_eq));  // open: gt, lt
  Register #(.Bits(5)) step (.D(multiplexer_1_out), .C(clock), .en(en), .Q(step_q));
  or or_1 (nnbusy, nnbusy_eq, ~en);  // Or
  not not_1 (not_1_out, nnbusy);
  Comparator #(.Bits(5)) u_op (.a(step_q), .b({5{1'b0}}), .eq(op_eq));  // open: gt, lt
  Register u_busy (.D(not_1_out), .C(clock), .en(en), .Q(busy));
  not not_2 (uop[5], op_eq);
  Multiplexer #(.Bits(5)) multiplexer_2 (.sel(op_eq), .in_0(step_q), .in_1(op), .out(uop[4:0]));

  // Other names for the same wires on the sheet: C = clock; en_t = en
endmodule
