// Digital circuit memaccess.dig as structural Verilog
module memaccess (
  input  [15:0] result,
  input  [15:0] rdval,
  input  store,
  input  en,
  input  mem,
  input  clk,
  output [15:0] A,
  output str,
  output [15:0] D_in,
  output req
);

  wire and_1_out, d_ff_1_nq;

  and and_1 (and_1_out, en, mem);
  and and_2 (str, store, en);
  D_FF d_ff_1 (.D(and_1_out), .C(clk), .nQ(d_ff_1_nq));  // open: Q
  and and_3 (req, and_1_out, d_ff_1_nq);
  // Pins of 14 and 16 bits meet at result

  assign A = result;
  assign D_in = rdval;

  // Other names for the same wires on the sheet: C = clk
endmodule
