// Digital circuit num2ascii.dig as structural Verilog
module num2ascii (
  input  [15:0] num,
  input  s,
  input  hex,
  input  clock,
  input  [2:0] digit,
  output [6:0] char
);

  wire unsign_1_s;
  wire [6:0] bcd2ascii_1_p4, bcd2ascii_1_p5, bcd2ascii_1_p6, bcd2ascii_1_p7, bcd2ascii_1_p8, bcd2ascii_1_p9;
  wire [15:0] unsign_1_o;
  wire [19:0] bin2bcdpiped_1_o, multiplexer_1_out;

  unsign unsign_1 (.i(num), .sgn(s), .o(unsign_1_o), .s(unsign_1_s));
  bin2bcdpiped bin2bcdpiped_1 (.I(unsign_1_o), .clock(clock), .O(bin2bcdpiped_1_o));
  Multiplexer #(.Bits(20)) multiplexer_1 (
    .sel(hex), .in_0(bin2bcdpiped_1_o), .in_1({4'b0000, unsign_1_o}), .out(multiplexer_1_out));
  // bcd2ascii bcd2ascii_1: pin names not known; wires that end beside it: multiplexer_1_out, unsign_1_s, 1'b1, bcd2ascii_1_p4, bcd2ascii_1_p5, bcd2ascii_1_p6, bcd2ascii_1_p7, bcd2ascii_1_p8, bcd2ascii_1_p9
  Multiplexer #(.Selector_Bits(3), .Bits(7)) multiplexer_2 (
    .sel(digit), .in_0(bcd2ascii_1_p4), .in_1(bcd2ascii_1_p5), .in_2(bcd2ascii_1_p6), .in_3(bcd2ascii_1_p7),
    .in_4(bcd2ascii_1_p8), .in_5(bcd2ascii_1_p9), .in_6({7{1'b0}}), .in_7({7{1'b0}}), .out(char));
endmodule
