// Digital circuit op2ascii.dig as structural Verilog
module op2ascii (
  input  [4:0] I,
  input  [2:0] C,
  output [6:0] L0,
  output [6:0] L1,
  output [6:0] L2,
  output [6:0] L3,
  output [6:0] L4,
  output [6:0] L5
);

  wire and_1_out;
  wire [6:0] multiplexer_5_out, multiplexer_6_out, multiplexer_8_out, multiplexer_9_out;

  Multiplexer #(.Selector_Bits(5), .Bits(7)) multiplexer_1 (
    .sel(I), .in_0(7'b0100000), .in_1(7'b0100000), .in_2(7'b0100000), .in_3(7'b0100000), .in_4(7'b0100000),
    .in_5(7'b0100000), .in_6(7'b0100000), .in_7(7'b0100000), .in_8(7'b0100000), .in_9(7'b0100000),
    .in_10(7'b0100000), .in_11(7'b0100000), .in_12(7'b0100000), .in_13(7'b0100000), .in_14(7'b0100000),
    .in_15(7'b0100000), .in_16(7'b0100000), .in_17(7'b0100000), .in_18(7'b0100000), .in_19(7'b0100000),
    .in_20(7'b0100000), .in_21(7'b0100000), .in_22(7'b0100000), .in_23(7'b0100000), .in_24(7'b0100000),
    .in_25(7'b1001001), .in_26(7'b0100000), .in_27(7'b0100000), .in_28(7'b0100000), .in_29(7'b0100000),
    .in_30(7'b0100000), .in_31(7'b0100000), .out(L0));
  Multiplexer #(.Selector_Bits(5), .Bits(7)) multiplexer_2 (
    .sel(I), .in_0(7'b0100000), .in_1(7'b0100000), .in_2(7'b1000101), .in_3(7'b0100000), .in_4(7'b0100000),
    .in_5(7'b0100000), .in_6(7'b0100000), .in_7(7'b0100000), .in_8(7'b0100000), .in_9(7'b0100000),
    .in_10(7'b0100000), .in_11(7'b0100000), .in_12(7'b0100000), .in_13(7'b0100000), .in_14(7'b0100000),
    .in_15(7'b0100000), .in_16(7'b0100000), .in_17(7'b0100000), .in_18(7'b0100000), .in_19(7'b0100000),
    .in_20(7'b0100000), .in_21(7'b0100000), .in_22(7'b0100000), .in_23(7'b0100000), .in_24(7'b1001001),
    .in_25(7'b1000110), .in_26(7'b0100000), .in_27(7'b0100000), .in_28(7'b0100000), .in_29(7'b0100000),
    .in_30(7'b0100000), .in_31(7'b1010011), .out(L1));
  Multiplexer #(.Selector_Bits(5), .Bits(7)) multiplexer_3 (
    .sel(I), .in_0(7'b0100000), .in_1(7'b0100000), .in_2(7'b1010010), .in_3(7'b1001000), .in_4(7'b0100000),
    .in_5(7'b0100000), .in_6(7'b0100000), .in_7(7'b0100000), .in_8(7'b0100000), .in_9(7'b0100000),
    .in_10(7'b0100000), .in_11(7'b0100000), .in_12(7'b0100000), .in_13(7'b0100000), .in_14(7'b0100000),
    .in_15(7'b0100000), .in_16(7'b0100000), .in_17(7'b0100000), .in_18(7'b0100000), .in_19(7'b0100000),
    .in_20(7'b0100000), .in_21(7'b0100000), .in_22(7'b1001101), .in_23(7'b0100000), .in_24(7'b1000110),
    .in_25(7'b1000011), .in_26(7'b0100000), .in_27(7'b0100000), .in_28(7'b1001010), .in_29(7'b0100000),
    .in_30(7'b1001100), .in_31(7'b1010100), .out(L2));
  Multiplexer #(.Selector_Bits(5), .Bits(7)) multiplexer_4 (
    .sel(I), .in_0(7'b1001110), .in_1(7'b0100000), .in_2(7'b1010010), .in_3(7'b1000001), .in_4(7'b0100000),
    .in_5(7'b0100000), .in_6(7'b0100000), .in_7(7'b0100000), .in_8(7'b0100000), .in_9(7'b0100000),
    .in_10(7'b0100000), .in_11(7'b0100000), .in_12(7'b0100000), .in_13(7'b0100000), .in_14(7'b0100000),
    .in_15(7'b0100000), .in_16(7'b1000001), .in_17(7'b0100000), .in_18(7'b0100000), .in_19(7'b0100000),
    .in_20(7'b0100000), .in_21(7'b0100000), .in_22(7'b1001111), .in_23(7'b0100000), .in_24(7'b0100000),
    .in_25(7'b0100000), .in_26(7'b0100000), .in_27(7'b0100000), .in_28(7'b1010101), .in_29(7'b0100000),
    .in_30(7'b1001111), .in_31(7'b1001111), .out(L3));
  Multiplexer #(.Selector_Bits(5), .Bits(7)) multiplexer_5 (
    .sel(I), .in_0(7'b1001111), .in_1(7'b0100000), .in_2(7'b1001111), .in_3(7'b1001100), .in_4(7'b0100000),
    .in_5(7'b0100000), .in_6(7'b0100000), .in_7(7'b0100000), .in_8(7'b0100000), .in_9(7'b0100000),
    .in_10(7'b0100000), .in_11(7'b0100000), .in_12(7'b0100000), .in_13(7'b0100000), .in_14(7'b0100000),
    .in_15(7'b0100000), .in_16(7'b1000100), .in_17(7'b0100000), .in_18(7'b0100000), .in_19(7'b0100000),
    .in_20(7'b1000101), .in_21(7'b0100000), .in_22(7'b1010110), .in_23(7'b0100000), .in_24(7'b0100000),
    .in_25(7'b0100000), .in_26(7'b0100000), .in_27(7'b0100000), .in_28(7'b1001101), .in_29(7'b0100000),
    .in_30(7'b1000001), .in_31(7'b1010010), .out(multiplexer_5_out));
  Multiplexer #(.Selector_Bits(3), .Bits(7)) multiplexer_6 (
    .sel(C), .in_0(7'b0100000), .in_1(7'b1000101), .in_2(7'b1001110), .in_3(7'b1001100), .in_4(7'b1000111),
    .in_5(7'b1001100), .in_6(7'b1001000), .in_7(7'b0100000), .out(multiplexer_6_out));
  Multiplexer #(.Bits(7)) multiplexer_7 (.sel(and_1_out), .in_0(multiplexer_5_out), .in_1(multiplexer_6_out), .out(L4));
  Multiplexer #(.Selector_Bits(5), .Bits(7)) multiplexer_8 (
    .sel(I), .in_0(7'b1010000), .in_1(7'b0100000), .in_2(7'b1010010), .in_3(7'b1010100), .in_4(7'b0100000),
    .in_5(7'b0100000), .in_6(7'b0100000), .in_7(7'b0100000), .in_8(7'b0100000), .in_9(7'b0100000),
    .in_10(7'b0100000), .in_11(7'b0100000), .in_12(7'b0100000), .in_13(7'b0100000), .in_14(7'b0100000),
    .in_15(7'b0100000), .in_16(7'b1000100), .in_17(7'b0100000), .in_18(7'b0100000), .in_19(7'b0100000),
    .in_20(7'b1010001), .in_21(7'b0100000), .in_22(7'b1000101), .in_23(7'b0100000), .in_24(7'b0100000),
    .in_25(7'b0100000), .in_26(7'b0100000), .in_27(7'b0100000), .in_28(7'b1010000), .in_29(7'b0100000),
    .in_30(7'b1000100), .in_31(7'b1000101), .out(multiplexer_8_out));
  Multiplexer #(.Selector_Bits(3), .Bits(7)) multiplexer_9 (
    .sel(C), .in_0(7'b0100000), .in_1(7'b1010001), .in_2(7'b1000101), .in_3(7'b1010100), .in_4(7'b1000101),
    .in_5(7'b1001111), .in_6(7'b1010011), .in_7(7'b0100000), .out(multiplexer_9_out));
  Multiplexer #(.Bits(7)) multiplexer_10 (
    .sel(and_1_out), .in_0(multiplexer_8_out), .in_1(multiplexer_9_out), .out(L5));
  and and_1 (and_1_out, ~I[1], ~I[2], I[3], I[4]);  // And
  // Pins of 1 and 7 bits meet at L0
  // Pins of 1 and 7 bits meet at L1
  // Pins of 1 and 7 bits meet at L2
  // Pins of 1 and 7 bits meet at L3
  // Pins of 1 and 7 bits meet at L4
  // Pins of 1 and 7 bits meet at L5
endmodule
