// Digital circuit pixgen.dig as structural Verilog
module pixgen (
  input  H_i,
  input  V_i,
  input  [3:0] col,
  input  [4:0] row,
  input  valid,
  input  [15:0] char,
  input  [15:0] bg,
  input  clk,
  input  [15:0] pix,
  output H_o,
  output V_o,
  output [10:0] A,
  output [15:0] colour
);

  wire sub_1_c_o;
  wire [1:0] PValid_q;
  wire [3:0] PCol_q;
  wire [6:0] sub_1_s;
  wire [6:6] multiplexer_1_out;
  wire [8:0] not_1_out, PColour_q;

  Sub #(.Bits(7)) sub_1 (.a(char[6:0]), .b(7'b0100000), .c_i(1'b0), .s(sub_1_s), .c_o(sub_1_c_o));
  Multiplexer #(.Bits(7)) multiplexer_1 (
    .sel(sub_1_c_o), .in_0(sub_1_s), .in_1({7{1'b0}}), .out({multiplexer_1_out[6], A[10:5]}));
  assign not_1_out = ~char[15:7];  // Not not_1, 9 bits wide
  Register register_1 (.D(H_i), .C(clk), .en(1'b1), .Q(H_o));
  Register register_2 (.D(V_i), .C(clk), .en(1'b1), .Q(V_o));
  Register #(.Bits(4)) PCol (.D(col), .C(clk), .en(1'b1), .Q(PCol_q));
  Register PValid (.D(valid), .C(clk), .en(1'b1), .Q(PValid_q[1]));
  Register #(.Bits(9)) PColour (.D(not_1_out), .C(clk), .en(1'b1), .Q(PColour_q));
  Multiplexer #(.Selector_Bits(4)) multiplexer_2 (
    .sel(PCol_q), .in_0(pix[15]), .in_1(pix[14]), .in_2(pix[13]), .in_3(pix[12]), .in_4(pix[11]),
    .in_5(pix[10]), .in_6(pix[9]), .in_7(pix[8]), .in_8(pix[7]), .in_9(pix[6]), .in_10(pix[5]),
    .in_11(pix[4]), .in_12(pix[3]), .in_13(pix[2]), .in_14(pix[1]), .in_15(pix[0]), .out(PValid_q[0]));
  Multiplexer #(.Selector_Bits(2), .Bits(16)) multiplexer_3 (
    .sel(PValid_q), .in_0({16{1'b0}}), .in_1({16{1'b0}}), .in_2(bg),
    .in_3({4'b0000, PColour_q[8:6], 1'b0, PColour_q[5:3], 1'b0, PColour_q[2:0], 1'b0}), .out(colour));

  assign A[4:0] = row;

  // Other names for the same wires on the sheet: C = clk

  // Notes on the sheet:
  //   bg: default 546
endmodule
