// Digital circuit posgen.dig as structural Verilog
module posgen (
  input  H_i,
  input  V_i,
  input  [15:0] X,
  input  [15:0] Y,
  input  clk,
  output H_o,
  output V_o,
  output [3:0] col,
  output [4:0] row,
  output valid,
  output [8:0] A
);

  wire comparator_1_lt;
  wire [15:0] sub_1_s;

  Sub #(.Bits(16)) sub_1 (.a(X), .b(16'h40), .c_i(1'b0), .s({sub_1_s[15:9], A[4:0], sub_1_s[3:0]}));  // open: c_o
  Comparator #(.Bits(16)) comparator_1 (
    .a({sub_1_s[15:9], A[4:0], sub_1_s[3:0]}), .b(16'h200), .lt(comparator_1_lt));  // open: gt, eq
  Register register_1 (.D(H_i), .C(clk), .en(1'b1), .Q(H_o));
  Register register_2 (.D(V_i), .C(clk), .en(1'b1), .Q(V_o));
  Register #(.Bits(4)) CCol (.D(sub_1_s[3:0]), .C(clk), .en(1'b1), .Q(col));
  Register #(.Bits(5)) CRow (.D(Y[4:0]), .C(clk), .en(1'b1), .Q(row));
  Register CValid (.D(comparator_1_lt), .C(clk), .en(1'b1), .Q(valid));

  assign A[8:5] = Y[8:5];

  // Other names for the same wires on the sheet: C = clk
endmodule
