// Digital circuit rddisplay.dig as structural Verilog
module rddisplay (
  input  [25:0] i,
  input  C,
  output [15:0] D1,
  output P1,
  output [15:0] D2,
  output P2,
  output [25:0] o,
  output [15:0] D3,
  output P3
);

  wire aluop2ascii_1_p2, ctrldec_1_p2, ctrldec_1_p4, multiplexer_1_out;
  wire [2:0] ctrldec_1_p3;
  wire [3:0] decodedec_1_p2;
  wire [15:0] debugval_1_q, debugval_2_q;
  wire [25:0] debugval_1_db_o;

  debugval debugval_1 (.db_i(i), .sel(8'h10), .db_o(debugval_1_db_o), .Q(debugval_1_q));
  // decodedec decodedec_1: pin names not known; wires that end beside it: debugval_1_q, decodedec_1_p2
  regdisplay regdisplay_1 (
    .D1(D1), .P1(P1), .D2(D2), .P2(P2), .D3(D3), .P3(P3), .R(decodedec_1_p2), .J(ctrldec_1_p2),
    .E(multiplexer_1_out));
  debugval debugval_2 (.db_i(debugval_1_db_o), .sel(8'h11), .db_o(o), .Q(debugval_2_q));
  // ctrldec ctrldec_1: pin names not known; wires that end beside it: debugval_2_q, ctrldec_1_p2, ctrldec_1_p3, ctrldec_1_p4
  // aluop2ascii aluop2ascii_1: pin names not known; wires that end beside it: {1'b0, ctrldec_1_p3}, aluop2ascii_1_p2
  Multiplexer multiplexer_1 (.sel(C), .in_0(aluop2ascii_1_p2), .in_1(ctrldec_1_p4), .out(multiplexer_1_out));
endmodule
