// Digital circuit reg2ascii.dig as structural Verilog
module reg2ascii (
  input  [3:0] R,
  input  J,
  input  E,
  output [6:0] D_0,
  output [6:0] D_1,
  output [6:0] D_2
);

  wire [6:0] multiplexer_1_out, multiplexer_3_out, multiplexer_5_out;

  Multiplexer #(.Selector_Bits(4), .Bits(7)) multiplexer_1 (
    .sel(R), .in_0(7'b0100000), .in_1(7'b0100000), .in_2(7'b0100000), .in_3(7'b0100000), .in_4(7'b0100000),
    .in_5(7'b0100000), .in_6(7'b0100000), .in_7(7'b0100000), .in_8(7'b0100000), .in_9(7'b0100000),
    .in_10(7'b1010010), .in_11(7'b1010010), .in_12(7'b1010010), .in_13(7'b1010010), .in_14(7'b1010010),
    .in_15(7'b1010010), .out(multiplexer_1_out));
  Multiplexer #(.Selector_Bits(2), .Bits(7)) multiplexer_2 (
    .sel({E, J}), .in_0(7'b0100000), .in_1(7'b0100000), .in_2(multiplexer_1_out), .in_3(7'b0100000), .out(D_0));
  Multiplexer #(.Selector_Bits(4), .Bits(7)) multiplexer_3 (
    .sel(R), .in_0(7'b1010010), .in_1(7'b1010010), .in_2(7'b1010010), .in_3(7'b1010010), .in_4(7'b1010010),
    .in_5(7'b1010010), .in_6(7'b1010010), .in_7(7'b1010010), .in_8(7'b1010010), .in_9(7'b1010010),
    .in_10(7'b0110001), .in_11(7'b0110001), .in_12(7'b0110001), .in_13(7'b0110001), .in_14(7'b0110001),
    .in_15(7'b0110001), .out(multiplexer_3_out));
  Multiplexer #(.Selector_Bits(2), .Bits(7)) multiplexer_4 (
    .sel({E, J}), .in_0(7'b0100000), .in_1(7'b0100000), .in_2(multiplexer_3_out), .in_3(7'b1010000), .out(D_1));
  Multiplexer #(.Selector_Bits(4), .Bits(7)) multiplexer_5 (
    .sel(R), .in_0(7'b0110000), .in_1(7'b0110001), .in_2(7'b0110010), .in_3(7'b0110011), .in_4(7'b0110100),
    .in_5(7'b0110101), .in_6(7'b0110110), .in_7(7'b0110111), .in_8(7'b0111000), .in_9(7'b0111001),
    .in_10(7'b0110000), .in_11(7'b0110001), .in_12(7'b0110010), .in_13(7'b0110011), .in_14(7'b0110100),
    .in_15(7'b0110101), .out(multiplexer_5_out));
  Multiplexer #(.Selector_Bits(2), .Bits(7)) multiplexer_6 (
    .sel({E, J}), .in_0(7'b0100000), .in_1(7'b0100000), .in_2(multiplexer_5_out), .in_3(7'b1000011), .out(D_2));
endmodule
