// Digital circuit regfile.dig as structural Verilog
module regfile (
  input  [3:0] rs,
  input  [3:0] rd,
  input  [15:0] result,
  input  clock,
  input  en,
  input  wr,
  output [15:0] rdval,
  output [15:0] rsval,
  output [15:0] R0,
  output [15:0] R1,
  output [15:0] R2,
  output [15:0] R3
);

  wire decoder_1_out_4, decoder_1_out_5, decoder_1_out_6, decoder_1_out_7;
  wire [2:2] and_1_out;
  wire [15:0] demultiplexer_1_out_0, demultiplexer_1_out_1, demultiplexer_1_out_2, demultiplexer_1_out_3;

  and and_1 (and_1_out[2], en, wr);
  Demultiplexer #(.Selector_Bits(2), .Bits(16)) demultiplexer_1 (
    .sel(rd[1:0]), .in(result), .out_0(demultiplexer_1_out_0), .out_1(demultiplexer_1_out_1),
    .out_2(demultiplexer_1_out_2), .out_3(demultiplexer_1_out_3));
  Decoder #(.Selector_Bits(3)) decoder_1 (
    .sel({and_1_out[2], rd[1:0]}), .out_4(decoder_1_out_4), .out_5(decoder_1_out_5), .out_6(decoder_1_out_6),
    .out_7(decoder_1_out_7));  // open: out_0, out_1, out_2, out_3
  Register #(.Bits(16)) u_R0 (.D(demultiplexer_1_out_0), .C(clock), .en(decoder_1_out_4), .Q(R0));
  Register #(.Bits(16)) u_R1 (.D(demultiplexer_1_out_1), .C(clock), .en(decoder_1_out_5), .Q(R1));
  Register #(.Bits(16)) u_R2 (.D(demultiplexer_1_out_2), .C(clock), .en(decoder_1_out_6), .Q(R2));
  Register #(.Bits(16)) u_R3 (.D(demultiplexer_1_out_3), .C(clock), .en(decoder_1_out_7), .Q(R3));
  Multiplexer #(.Selector_Bits(2), .Bits(16)) multiplexer_1 (
    .sel(rs[1:0]), .in_0(R0), .in_1(R1), .in_2(R2), .in_3(R3), .out(rsval));
  Multiplexer #(.Selector_Bits(2), .Bits(16)) multiplexer_2 (
    .sel(rd[1:0]), .in_0(R0), .in_1(R1), .in_2(R2), .in_3(R3), .out(rdval));
endmodule
