// Digital circuit renderdelay.dig as structural Verilog
module renderdelay (
  input  clk,
  input  [15:0] I,
  output [15:0] O
);

  wire [15:0] register_1_q, register_2_q, register_3_q;

  Register #(.Bits(16)) register_1 (.D(I), .C(clk), .en(1'b1), .Q(register_1_q));
  Register #(.Bits(16)) register_2 (.D(register_1_q), .C(clk), .en(1'b1), .Q(register_2_q));
  Register #(.Bits(16)) register_3 (.D(register_2_q), .C(clk), .en(1'b1), .Q(register_3_q));
  Register #(.Bits(16)) register_4 (.D(register_3_q), .C(clk), .en(1'b1), .Q(O));

  // Other names for the same wires on the sheet: C = clk
endmodule
