// Digital circuit rj32.dig as structural Verilog
module rj32 (
  input  clock,
  input  step,
  input  run_slow,
  input  [15:0] D_prog,
  input  [15:0] D_in,
  input  run_fast,
  input  run_faster,
  input  erun,
  input  ack,
  output halt,
  output error,
  output skip,
  output stall,
  output [9:0] A_prog,
  output clock_m,
  output [15:0] A_data,
  output [15:0] D_out,
  output w_en,
  output [25:0] db,
  output req,
  output [33:0] ctrl,
  output [63:0] bus,
  output [38:0] \reg 
);

  wire skip_n;
  wire [15:0] execute_1_l_out, execute_1_r_out, fetch_1_instr_o, regfile_1_rdval, regfile_1_rsval,
       writeback_1_rdval_out, writeback_1_result_out;

  not not_1 (clock_m, clock);
  fetch fetch_1 (
    .result(bus[47:32]), .instr_i(D_prog), .clock(clock), .fetch(ctrl[11]), .jump(ctrl[4]), .en(ctrl[12]),
    .instr_o(fetch_1_instr_o), .pc({\reg [37:32], A_prog}));
  decoder decoder_1 (
    .rdval(regfile_1_rdval), .rsval(regfile_1_rsval), .instr(fetch_1_instr_o), .pc({\reg [37:32], A_prog}),
    .jump(ctrl[4]), .clk(clock), .en(ctrl[11]), .rs(ctrl[33:30]), .rd(ctrl[28:25]), .L(bus[15:0]),
    .R(bus[31:16]), .op(ctrl[20:16]), .rs_valid(ctrl[29]), .rd_valid(ctrl[24]), .imm(bus[63:48]),
    .immv(ctrl[15]));
  clockctrl clockctrl_1 (
    .clock(clock), .step(step), .slow(run_slow), .fast(run_fast), .faster(run_faster), .efast(erun),
    .stall(ctrl[0]));
  control control_1 (
    .op(ctrl[20:16]), .stall(ctrl[0]), .clock(clock), .skip_n(skip_n), .ack(ack), .aluop(ctrl[7:5]),
    .cond(ctrl[23:21]), .skip(ctrl[1]), .halt(ctrl[2]), .error(ctrl[3]), .en_write(ctrl[12]), .mem(ctrl[8]),
    .store(ctrl[9]), .en_fetch(ctrl[11]), .jump(ctrl[4]), .write(ctrl[10]), .wrmux(ctrl[14:13]));
  execute execute_1 (
    .L(bus[15:0]), .R(bus[31:16]), .op(ctrl[7:5]), .cond(ctrl[23:21]), .L_out(execute_1_l_out),
    .R_out(execute_1_r_out), .result(bus[47:32]), .skip_n(skip_n));
  writeback writeback_1 (
    .L(execute_1_l_out), .R(execute_1_r_out), .result(bus[47:32]), .rdval(regfile_1_rdval), .D(D_in),
    .wrmux(ctrl[14:13]), .wrval(\reg [15:0]), .result_out(writeback_1_result_out),
    .rdval_out(writeback_1_rdval_out));
  debugbus debugbus_1 (
    .db_ready(1'b1), .clock(clock), .ctrl(ctrl[15:0]), .wrval(\reg [15:0]), .result(bus[47:32]),
    .L(bus[15:0]), .R(bus[31:16]), .imm(bus[63:48]), .pc({\reg [37:32], A_prog}),
    .fullop({{8{1'b0}}, ctrl[23:16]}), .rdf({{10{1'b0}}, ctrl[24], ctrl[4], ctrl[28:25]}),
    .rsf({{10{1'b0}}, ctrl[29], 1'b0, ctrl[33:30]}), .db(db));
  // memaccess memaccess_1: pin names not known; wires that end beside it: writeback_1_result_out, writeback_1_rdval_out, ctrl[9], ctrl[12], ctrl[8], clock, A_data, w_en, D_out, req
  regfile regfile_1 (
    .rs(ctrl[33:30]), .rd(ctrl[28:25]), .wrval(\reg [15:0]), .clock(clock), .en(ctrl[12]), .wr(ctrl[10]),
    .rdval(regfile_1_rdval), .rsval(regfile_1_rsval));

  assign error = ctrl[3];
  assign halt = ctrl[2];
  assign {\reg [38], \reg [31:16]} = {clock, A_prog, ctrl[10], ctrl[12], ctrl[28:25]};
  assign skip = ctrl[1];
  assign stall = ctrl[0];

  // Other names for the same wires on the sheet: A_data_t[15:0] = A_data; ack_t = ack; aluop_t[2:0] = ctrl[7:5];
  //   ctrl_t[15:0] = ctrl[15:0]; C = clock; cond_t[2:0] = ctrl[23:21]; fullop_t[7:0] = ctrl[23:16];
  //   D_in_t[15:0] = D_in; D_out_t[15:0] = D_out; D_prog_t[15:0] = D_prog; en = ctrl[12]; en_fetch = ctrl[11];
  //   error_t = ctrl[3]; halt_t = ctrl[2]; imm_t[15:0] = bus[63:48]; immv_t = ctrl[15]; jump_t = ctrl[4];
  //   rdf_t[5:0] = {ctrl[24], ctrl[4], ctrl[28:25]}; L_t[15:0] = bus[15:0]; mem_t = ctrl[8]; op_t[4:0] = ctrl[20:16];
  //   A_prog_t[15:0] = {\reg [37:32], A_prog}; PC_t[15:0] = {\reg [37:32], A_prog}; R_t[15:0] = bus[31:16];
  //   rd_t[3:0] = ctrl[28:25]; rdvalid_t = ctrl[24]; req_t = req; result_t[15:0] = bus[47:32];
  //   rs_t[3:0] = ctrl[33:30]; rsf_t (some bits) = {ctrl[29], ctrl[33:30]}; rsvalid_t = ctrl[29]; skip_t = ctrl[1];
  //   stall_t = ctrl[0]; store_t = ctrl[9]; W_en_t = w_en; write_t = ctrl[10]; wrmux_t[1:0] = ctrl[14:13];
  //   wrval_t[15:0] = \reg [15:0]

  // Notes on the sheet:
  //   clock: Hz: 10
  //   rj45 Creates
endmodule
