// Digital circuit rsdisplay.dig as structural Verilog
module rsdisplay (
  input  [25:0] i,
  output [15:0] D1,
  output P1,
  output [15:0] D2,
  output P2,
  output [25:0] o,
  output [15:0] D3,
  output P3
);

  wire decodedec_1_p2, regdisplay_1_p8;
  wire [15:0] debugval_1_q, debugval_2_q;
  wire [25:0] debugval_1_db_o;

  debugval debugval_1 (.db_i(i), .sel(8'h10), .db_o(debugval_1_db_o), .Q(debugval_1_q));
  // decodedec decodedec_1: pin names not known; wires that end beside it: debugval_1_q, decodedec_1_p2
  // regdisplay regdisplay_1: pin names not known; wires that end beside it: D1, decodedec_1_p2, P1, D2, 1'b0, P2, D3, regdisplay_1_p8, P3
  debugval debugval_2 (.db_i(debugval_1_db_o), .sel(8'h11), .db_o(o), .Q(debugval_2_q));
  // ctrldec ctrldec_1: pin names not known; wires that end beside it: debugval_2_q, regdisplay_1_p8
endmodule
