// Digital circuit strgen.dig as structural Verilog
module strgen (
  input  [8:0] A_i,
  input  [15:0] D_i,
  input  [1:0] X,
  input  [3:0] Y,
  input  [8:0] C,
  input  [6:0] L0,
  input  [6:0] L1,
  input  [6:0] L2,
  input  [6:0] L3,
  input  [6:0] L4,
  input  [6:0] L5,
  input  [6:0] L6,
  input  [6:0] L7,
  input  en,
  output [8:0] A_o,
  output [15:0] D_o
);

  wire nor_1_out;
  wire [5:0] xor_1_out;
  wire [6:0] multiplexer_1_out;

  assign xor_1_out = A_i[8:3] ^ {Y, X};  // XOr xor_1, 6 bits wide
  Multiplexer #(.Selector_Bits(3), .Bits(7)) multiplexer_1 (
    .sel(A_i[2:0]), .in_0(L0), .in_1(L1), .in_2(L2), .in_3(L3), .in_4(L4), .in_5(L5), .in_6(L6), .in_7(L7),
    .out(multiplexer_1_out));
  nor nor_1 (nor_1_out, xor_1_out[0], xor_1_out[1], xor_1_out[2], xor_1_out[3], xor_1_out[4], xor_1_out[5], ~en);  // NOr
  Multiplexer #(.Bits(16)) multiplexer_2 (.sel(nor_1_out), .in_0(D_i), .in_1({C, multiplexer_1_out}), .out(D_o));

  assign A_o = A_i;
endmodule
