// Digital circuit syncpulse.dig as structural Verilog
module syncpulse (
  input  en,
  input  clk,
  input  [15:0] res,
  input  [15:0] fp,
  input  [15:0] sync,
  input  [15:0] bp,
  input  neg,
  output [15:0] V,
  output pulse,
  output valid,
  output C
);

  wire and_1_out, comparator_1_lt, comparator_2_lt, comparator_3_eq, comparator_3_gt, or_1_out;
  wire [15:0] sub_1_s, sub_2_s, sub_3_s;

  Comparator #(.Signed("true"), .Bits(16)) comparator_1 (.a(V), .b(res), .lt(comparator_1_lt));  // open: gt, eq
  Sub #(.Bits(16)) sub_1 (.a({16{1'b0}}), .b(bp), .c_i(1'b0), .s(sub_1_s));  // open: c_o
  Sub #(.Bits(16)) sub_2 (.a(sub_1_s), .b(sync), .c_i(1'b0), .s(sub_2_s));  // open: c_o
  Sub #(.Bits(16)) sub_3 (.a(sub_2_s), .b(fp), .c_i(1'b0), .s(sub_3_s));  // open: c_o
  not not_1 (C, comparator_1_lt);
  Comparator #(.Signed("true"), .Bits(16)) comparator_2 (.a(V), .b(sub_1_s), .lt(comparator_2_lt));  // open: gt, eq
  Comparator #(.Signed("true"), .Bits(16)) comparator_3 (
    .a(V), .b(sub_2_s), .gt(comparator_3_gt), .eq(comparator_3_eq));  // open: lt
  Comparator #(.Signed("true"), .Bits(16)) comparator_4 (.a(V), .b({16{1'b1}}), .gt(valid));  // open: eq, lt
  CounterPreset #(.Bits(16)) counterpreset_1 (
    .en(en), .C(clk), .dir(1'b0), .in(sub_3_s), .ld(C), .clr(1'b0), .out(V));  // open: ovf
  or or_1 (or_1_out, comparator_3_gt, comparator_3_eq);
  and and_1 (and_1_out, comparator_2_lt, or_1_out);
  xor xor_1 (pulse, and_1_out, neg);

  // Notes on the sheet:
  //   res: default 639
  //   fp: default 16
  //   sync: default 96
  //   bp: default 48
endmodule
