// Digital circuit unsign.dig as structural Verilog
module unsign (
  input  [15:0] i,
  input  sgn,
  output [15:0] o,
  output s
);

  wire [15:0] neg_1_out;

  Neg #(.Bits(16)) neg_1 (.in(i), .out(neg_1_out));
  and and_1 (s, i[15], sgn);
  Multiplexer #(.Bits(16)) multiplexer_1 (.sel(s), .in_0(i), .in_1(neg_1_out), .out(o));
endmodule
