// Digital circuit engine.dig as structural Verilog
module engine (
  input  clk,
  input  rst,
  input  [11:0] x_i,
  input  [11:0] y_i,
  input  line_i,
  input  frame_i,
  input  hsync_i,
  input  vsync_i,
  input  en_disp_i,
  output [11:0] x_o,
  output [11:0] y_o,
  output line_o,
  output frame_o,
  output [7:0] r,
  output [7:0] g,
  output [7:0] b,
  output hsync_o,
  output vsync_o,
  output en_disp_o
);

  wire [7:0] demultiplexer_1_out_0, demultiplexer_1_out_1, demultiplexer_1_out_2, demultiplexer_1_out_3,
       or_1_out, or_2_out, or_3_out;

  Demultiplexer #(.Selector_Bits(2), .Bits(8)) demultiplexer_1 (
    .sel(y_i[7:6]), .in(x_i[8:1]), .out_0(demultiplexer_1_out_0), .out_1(demultiplexer_1_out_1),
    .out_2(demultiplexer_1_out_2), .out_3(demultiplexer_1_out_3));
  assign or_1_out = demultiplexer_1_out_0 | demultiplexer_1_out_3;  // Or or_1, 8 bits wide
  assign or_2_out = demultiplexer_1_out_1 | demultiplexer_1_out_3;  // Or or_2, 8 bits wide
  assign or_3_out = demultiplexer_1_out_2 | demultiplexer_1_out_3;  // Or or_3, 8 bits wide
  Multiplexer #(.Bits(8)) multiplexer_1 (.sel(en_disp_i), .in_0({8{1'b0}}), .in_1(or_1_out), .out(r));
  Multiplexer #(.Bits(8)) multiplexer_2 (.sel(en_disp_i), .in_0({8{1'b0}}), .in_1(or_2_out), .out(g));
  Multiplexer #(.Bits(8)) multiplexer_3 (.sel(en_disp_i), .in_0({8{1'b0}}), .in_1(or_3_out), .out(b));

  assign en_disp_o = en_disp_i;
  assign frame_o = frame_i;
  assign hsync_o = hsync_i;
  assign line_o = line_i;
  assign vsync_o = vsync_i;
  assign x_o = x_i;
  assign y_o = y_i;
endmodule
