// Digital circuit framebuffer.dig as structural Verilog
module framebuffer (
  input  clk,
  input  [11:0] X,
  input  [11:0] Y,
  input  [7:0] R,
  input  [7:0] G,
  input  [7:0] B
);

  wire [15:15] Frame_Buffer_d;
  wire [18:0] add_1_s, bitextender_1_out;
  wire [23:0] mul_1_mul;

  BitExtender #(.inputBits(12), .outputBits(19)) bitextender_1 (.in(X), .out(bitextender_1_out));
  Mul #(.Bits(12)) mul_1 (.a(Y), .b(12'h280), .mul(mul_1_mul));
  Add #(.Bits(19)) add_1 (.a(bitextender_1_out), .b(mul_1_mul[18:0]), .c_i(1'b0), .s(add_1_s));  // open: c_o
  GraphicCard #(.graphicHeight(360), .graphicWidth(640), .Bits(16)) Frame_Buffer (
    .A(add_1_s), .str(1'b1), .C(clk), .ld(1'b0), .B(1'b0), .D({Frame_Buffer_d[15], B[7:3], G[7:3], R[7:3]}));
  // also tied to VCC on the sheet: Frame_Buffer_d[15]

  // Notes on the sheet:
  //   8:8:8 RGB -> 5:5:5 RGB
endmodule
