// Digital circuit palettebram.dig as structural Verilog
module palettebram (
  input  [8:0] pixel,
  input  clk,
  input  pal_we,
  input  [9:0] pal_adr,
  input  [15:0] pal_dat,
  output [23:0] colour
);

  wire and_1_out, and_2_out, counter_1_ovf, or_1_out, or_2_out, rs_ff_1_nq, rs_ff_1_q;
  wire [8:0] counter_1_out, driver_2_out;
  wire [23:0] driver_1_out, PalBRAM1_d2;

  Counter #(.Bits(9)) counter_1 (.en(rs_ff_1_nq), .C(clk), .clr(1'b0), .out(counter_1_out), .ovf(counter_1_ovf));
  RS_FF rs_ff_1 (.S(counter_1_ovf), .C(clk), .R(1'b0), .Q(rs_ff_1_q), .nQ(rs_ff_1_nq));
  and and_1 (and_1_out, pal_we, ~pal_adr[0]);  // And
  and and_2 (and_2_out, pal_we, pal_adr[0]);
  assign driver_1_out = rs_ff_1_q ? {pal_dat[7:0], pal_dat} : 24'bz;  // Driver driver_1
  assign driver_2_out = rs_ff_1_q ? pal_adr[9:1] : 9'bz;  // Driver driver_2
  ROM #(.AddrBits(9), .Bits(24)) Palette (.A(counter_1_out), .sel(rs_ff_1_nq), .D(driver_1_out));
  assign driver_2_out = rs_ff_1_nq ? counter_1_out : 9'bz;  // Driver driver_3
  or or_1 (or_1_out, rs_ff_1_nq, and_1_out);
  or or_2 (or_2_out, rs_ff_1_nq, and_2_out);
  RAMDualAccess #(.AddrBits(9), .Bits(16)) PalBRAM1 (
    .str(or_1_out), .C(clk), .ld(1'b0), .A1(driver_2_out), .Din1(driver_1_out[15:0]), .A2(pixel),
    .D2(PalBRAM1_d2[15:0]));  // open: D1
  RAMDualAccess #(.AddrBits(9), .Bits(8)) PalBRAM2 (
    .str(or_2_out), .C(clk), .ld(1'b0), .A1(driver_2_out), .Din1(driver_1_out[23:16]), .A2(pixel),
    .D2(PalBRAM1_d2[23:16]));  // open: D1
  D_FF #(.Bits(24)) d_ff_1 (.D(PalBRAM1_d2), .C(clk), .Q(colour));  // open: nQ

  // Other names for the same wires on the sheet: C = clk

  // Notes on the sheet:
  //   clk: Hz: 50
  //   contents of Palette (hex, n*v repeats v):
  //   150e11,7b7d7d,452923,3f4527,303b2a,4d4a2b,2f361a,3a3a25,303923,555040,aea9b2,3e4b35,
  //   31452f,23351e,463826,7c7312,3b5c1c,f39f13,965529,bfa19f,77493f,db7512,dcc9c0,6c418a,
  //   99757d,6f2918,80583f,8d5c48,c2705e,f8fbf5,784831,7f584d,ff00ff,0,e2b604,866d09,9b8577,
  //   d6b42a,e9c223,c3ac4d,f5c402,ad9e62,f7ca12,fdcd0b,cdb03c,a5860a,fecb00,f9cc1d,504643,
  //   cfc18e,93838f,ebe3a6,837940,d4bfc7,b4a1a3,c67c5a,f9f3f3,cdb7b3,c9a8a4,87716f,e4cfcf,
  //   f2e1dc,ab8f91,dfc0b5,1b1d23,555b2f,99a776,575f3b,42513e,576d43,3e4f20,495d2a,667445,
  //   495f3b,53652d,576145,424f30,5d6830,c8e3a4,496045,25361e,54808c,3a513e,b7808d,4c5f45,
  //   3b522e,9d8a55,74c69e,2e4722,d3f4d1,435942,566f49,465730,31492d,5fccd5,d3baa5,9091d,
  //   1a87d9,233a61,d7c2c7,32262e,665366,907f7b,84160a,202b2e,303633,195e9f,794ca7,a297b5,
  //   674e47,3c572a,fcfcfc,3e5c2a,76a23b,55b0a1,607f33,4d784d,b4da0f,618756,8bbf93,72a665,
  //   2788a2,708937,a7bb65,4d7528,d2de97,7e8d54,3ec1e9,f30dfc,878f2d,1d7ecb,24324b,552a1a,
  //   d5cad0,6c536e,14260f,fbcb01,9f8fa1,a1110c,155795,a1d08,f6f2f5,1d2226,40410,3d632e,
  //   e2671e,89af54,efeca1,7dc59d,448468,c1c36e,688a3a,6aac7c,e7d487,f7fcee,6f9169,7acfc0,
  //   89b97d,6b593b,c8c88f,39502d,ba9609,862612,a69556,7c6749,ecd35a,836710,610f11,f1dca7,
  //   e6bc14,9d7408,927182,baa782,635326,977a4c,864a15,405f1d,a3af1c,5d6a2e,8da55d,62703e,
  //   4a632d,d6e062,677d44,51693e,cdd112,4e6322,617431,729b50,53682d,d6e599,b0b65c,32520c,
  //   b85607,436219,94bd61,4d672d,6e8f3c,251b23,a29762,cad9b4,52704c,355222,c9cf68,728f60,
  //   395d10,466323,3a5f1e,11260d,1373bb,223325,272c41,e5d4d4,790e3,2b3b29,1b3113,d457d,
  //   353f2d,87d3b2,7f7574,3a493f,273818,5d546a,9b9998,3d5f1f,8ebd0e,76b267,72931a,b6d571,
  //   619653,5a7c1f,d5e9b9,8cb342,88c587,779531,7d9b54,597e41,eadb6d,96bb62,b6c342,3d5d2b,
  //   75a062,577d45,c9ce6e,48653f,548667,70a386,566942,d4e4b8,698344,86bc97,6b8d67,5a7345,
  //   94ad5b,516b2c,436c54,161f3f,1c70c3,16447f,20a3f3,767b83,9d2410,7fbbc9,1c89e6,1f5a9a,
  //   3d5f45,4476c2,5ad8f8,3b6c92,8f50e9,28cbf8,97b194,2a2247,ecd7cf,b2a8ac,f7ebe9,da522a,
  //   bcc0b0,998693,fdfcfc,cec2ca,eedfe1,ceaeab,6e6f60,b99695,e1c0b6,fcf5f0,e1c9cb,70405,
  //   c00e04,cd8f85,6d0d07,c54b17,6a5b3b,d56b24,ee2407,9e0e04,e6d1d8,945748,f64c08,fb740c,
  //   380c08,a22e09,c6250a,1a3405,80994c,273b24,334923,233b18,3a4754,2b4119,24394e,a8bd68,
  //   3c552b,2b4609,364518,2b4325,e0d7bc,263a09,33482d,34471c,9c9659,d8c306,e2c751,85960d,
  //   f3dc88,d6bb2b,d0b254,a5b90d,f7d105,f3d76c,f4e7b5,f7d52d,b38c21,fadc4f,d0b67d,19241b,
  //   2d434b,48412c,8cd6ca,56452a,79654d,575436,575345,474f27,534736,615955,655739,85706b,
  //   4a4d35,5c4a37,655745,322d2e,b66507,e7ad03,d08e02,3c79c5,e79b02,fabd05,bd97bf,8b4b1a,
  //   f14a07,d8d3d6,d89d02,f4a104,f8af04,62d1f6,fdd009,b0411,676168,9d0d06,dac8dc,620c07,
  //   f8740e,cb1a0d,6e4337,a03314,bb745f,2e2e50,f53c0b,f9a172,7c0f07,ca3f13,3e0d09,29251e,
  //   b77404,904a06,e89704,c27c4f,945732,54356f,d18e04,fbc80a,a07304,673516,864c73,bd8904,
  //   354f23,f3aa08,d69d06,60719,594d30,755140,543c28,907a7a,60513c,674130,bc822c,6b5540,
  //   7b594c,665230,554234,cdb498,442223,5e5350,765e3f,180207,523a7c,991009,5d2e1c,ca1f10,
  //   55090b,9b8a95,3f5e1f,9d462b,db5820,483155,6f6d9b,32133d,740b08,a6a2c0,f0240a,f0925,
  //   bda7ab,6e834d,64594f,5888a1,efe2e0,9e90a2,31526f,907f7e,72626e,d7c6c5,394832,91cec6,
  //   63817d,66b2b4,fefdfc,100525,5e3ba9,412474,9058d7,435530,7951b7,5b3e90,9f83c2,7d47d3,
  //   2c1757,683ac2,4f4259,9d5ef1,4b2b8d,b180ed,6b568a,ff00ff,ad7a0b,50503,f6af02,a89257,
  //   3a401d,fecb00,dea603,f9d64e,88511a,d7b33c,e6b905,f9bf02,fdd603,dcbe7a,f3c430,303e26,
  //   a3a021,6d593c,8ddee5,5d592a,f1610c,d0d41a,606430,806942,515528,5e5837,e0d96b,535736,
  //   6c673a,9c9761,60653c,29480d,748c50,334a2c,2f4a20,96c39f,475930,3d5720,78190c,6b5a69,
  //   36530e,e5ebdb,b6ac53,345320,9d3a1c,39552d,4a5c3c
endmodule
