// Digital circuit pixel2colour.dig as structural Verilog
module pixel2colour (
  input  [11:0] x_i,
  input  [11:0] y_i,
  input  hsync_i,
  input  vsync_i,
  input  en_disp_i,
  input  clk,
  input  rst,
  output [11:0] x_o,
  output [11:0] y_o,
  output [7:0] r,
  output [7:0] g,
  output [7:0] b,
  output hsync_o,
  output vsync_o,
  output en_disp_o
);

  wire [23:0] palettebram_1_colour;

  pipelineregs #(.generic("bits := [12,12,1,1,1];")) pipelineregs_1 ();
  palettebram palettebram_1 (
    .pixel(x_i[8:0]), .pal_we(1'b0), .pal_adr({10{1'b0}}), .pal_dat({16{1'b0}}), .clk(clk), .rst(rst),
    .colour(palettebram_1_colour));
  Multiplexer #(.Bits(8)) multiplexer_1 (
    .sel(en_disp_o), .in_0({8{1'b0}}), .in_1(palettebram_1_colour[23:16]), .out(r));
  Multiplexer #(.Bits(8)) multiplexer_2 (.sel(en_disp_o), .in_0({8{1'b0}}), .in_1(palettebram_1_colour[15:8]), .out(g));
  Multiplexer #(.Bits(8)) multiplexer_3 (.sel(en_disp_o), .in_0({8{1'b0}}), .in_1(palettebram_1_colour[7:0]), .out(b));

  // Other names for the same wires on the sheet: C = clk; R_t = rst
endmodule
