// Digital circuit plusone.dig as structural Verilog
module plusone (
  input  A,
  output Y
);

  Add #(.generic("this.Bits = args.bitWidth;")) plus_1 (.a(A), .b(1'b0), .c_i(1'b1), .s(Y));  // open: c_o
endmodule

/* Code that sets the parameters or builds the circuit:
bitWidth := 8;
*/
