// Digital circuit rsff.dig as structural Verilog
module rsff (
  input  S,
  input  C,
  input  R,
  output Q,
  output nQ
);

  wire and_1_out, or_1_out;

  or or_1 (or_1_out, Q, S);
  and and_1 (and_1_out, or_1_out, ~R);  // And
  D_FF d_ff_1 (.D(and_1_out), .C(C), .Q(Q), .nQ(nQ));
endmodule
