// Digital circuit scanout.dig as structural Verilog
module scanout (
  input  [11:0] x_i,
  input  [11:0] y_i,
  input  hsync_i,
  input  vsync_i,
  input  en_disp_i,
  input  clk,
  input  rst,
  output [11:0] x_o,
  output [11:0] y_o,
  output [7:0] r,
  output [7:0] g,
  output [7:0] b,
  output hsync_o,
  output vsync_o,
  output en_disp_o
);

  pixel2colour pixel2colour_1 (
    .x_i(x_i), .y_i(y_i), .hsync_i(hsync_i), .vsync_i(vsync_i), .en_disp_i(en_disp_i), .clk(clk), .rst(rst),
    .x_o(x_o), .y_o(y_o), .r(r), .g(g), .b(b), .hsync_o(hsync_o), .vsync_o(vsync_o), .en_disp_o(en_disp_o));

  // Other names for the same wires on the sheet: C = clk; R_t = rst
endmodule
