// Digital circuit scanxy.dig as structural Verilog
module scanxy (
  input  C,
  input  rst,
  input  en,
  input  [11:0] h_total,
  input  [11:0] v_total,
  output [11:0] x_next,
  output [11:0] y_next,
  output [11:0] x,
  output [11:0] y,
  output line,
  output frame
);

  wire X_ovf, Y_ovf;

  and and_1 (line, X_ovf, en);
  maxcounter #(.generic("bitWidth := 12;")) u_X (
    .en(en), .C(C), .max(h_total), .rst(rst), .Q(x), .ovf(X_ovf), .N(x_next));
  maxcounter #(.generic("bitWidth := 12;")) u_Y (
    .en(line), .C(C), .max(v_total), .rst(rst), .Q(y), .ovf(Y_ovf), .N(y_next));
  and and_2 (frame, line, Y_ovf);

  // Other names for the same wires on the sheet: R = rst

  // Notes on the sheet:
  //   h_total: default 5
  //   v_total: default 3
endmodule
