// Digital circuit sync.dig as structural Verilog
module sync (
  input  clk,
  input  rst,
  input  en,
  input  [11:0] v,
  input  [11:0] fp,
  input  [11:0] sync,
  input  [11:0] bp,
  input  n,
  input  neg,
  output blank,
  output pulse
);

  wire and_1_out, and_2_out, and_3_out, equals_1_q, equals_2_q, equals_3_q, or_1_out, or_2_out, rsff_2_nq,
       rsff_2_q;

  equals #(.generic("bitWidth := 12;")) equals_1 (.A(v), .B(fp), .Q(equals_1_q));
  equals #(.generic("bitWidth := 12;")) equals_2 (.A(v), .B(sync), .Q(equals_2_q));
  equals #(.generic("bitWidth := 12;")) equals_3 (.A(v), .B(bp), .Q(equals_3_q));
  and and_1 (and_1_out, en, equals_1_q);
  and and_2 (and_2_out, en, equals_2_q);
  and and_3 (and_3_out, en, equals_3_q);
  or or_1 (or_1_out, rst, n);
  or or_2 (or_2_out, rst, and_3_out);
  rsff rsff_1 (.S(and_1_out), .C(clk), .R(or_1_out), .Q(blank));  // open: nQ
  rsff rsff_2 (.S(and_2_out), .C(clk), .R(or_2_out), .Q(rsff_2_q), .nQ(rsff_2_nq));
  Multiplexer multiplexer_1 (.sel(neg), .in_0(rsff_2_q), .in_1(rsff_2_nq), .out(pulse));

  // Other names for the same wires on the sheet: C = clk; R = rst

  // Notes on the sheet:
  //   fp: default 3
  //   sync: default 5
  //   bp: default 7
endmodule
