// Digital circuit syncstate.dig as structural Verilog
module syncstate (
  input  blank_end,
  input  blank_bgn,
  input  sync_bgn,
  input  sync_end,
  input  neg,
  input  clk,
  input  rst,
  output blank,
  output sync
);

  wire or_1_out, or_2_out, rsff_2_nq, rsff_2_q;

  or or_1 (or_1_out, blank_end, rst);
  or or_2 (or_2_out, sync_end, rst);
  rsff rsff_1 (.S(blank_bgn), .C(clk), .R(or_1_out), .Q(blank));  // open: nQ
  rsff rsff_2 (.S(sync_bgn), .C(clk), .R(or_2_out), .Q(rsff_2_q), .nQ(rsff_2_nq));
  Multiplexer multiplexer_1 (.sel(neg), .in_0(rsff_2_q), .in_1(rsff_2_nq), .out(sync));

  // Other names for the same wires on the sheet: C = clk; R = rst
endmodule
