// Digital circuit top_simfb.dig as structural Verilog
module top_simfb (
  input  clk,
  input  rst
);

  wire scanxy_1_nf, scanxy_1_nl;
  wire [7:0] engine_1_b, engine_1_g, engine_1_r;
  wire [11:0] engine_1_x_o, engine_1_y_o, scanxy_1_x, scanxy_1_y;

  scanxy scanxy_1 (
    .C(clk), .rst(rst), .en(1'b1), .hr(12'h280), .vr(12'h168), .x(scanxy_1_x), .y(scanxy_1_y),
    .nl(scanxy_1_nl), .nf(scanxy_1_nf));  // open: nx, ny
  engine engine_1 (
    .clk(clk), .rst(rst), .X_i(scanxy_1_x), .Y_i(scanxy_1_y), .nl_i(scanxy_1_nl), .nf_i(scanxy_1_nf),
    .hs_i(1'b0), .vs_i(1'b0), .de_i(1'b1), .X_o(engine_1_x_o), .Y_o(engine_1_y_o), .R(engine_1_r),
    .G(engine_1_g), .B(engine_1_b));  // open: nl_o, nf_o, hs_o, vs_o, de_o
  framebuffer framebuffer_1 (
    .clk(clk), .X(engine_1_x_o), .Y(engine_1_y_o), .R(engine_1_r), .G(engine_1_g), .B(engine_1_b));

  // Other names for the same wires on the sheet: C = clk; R = rst

  // Notes on the sheet:
  //   clk: Hz: 2147483647
  //   Legend:
  //   clk, C: clock
  //   rst, R: reset
  //   en: enable
  //   hr: horizontal resolution
  //   vr: vertical resolution
  //   nx: next x position
  //   ny: next y position
  //   nl: next line
  //   nf: next frame
  //   hs: horizontal sync
  //   vs: vertical sync
  //   de: display enable
  //   r: red colour channel
  //   g: green colour channel
  //   b: blue colour channel
endmodule
