// Digital circuit top_simvga.dig as structural Verilog
module top_simvga (
  input  clk,
  input  rst
);

  wire vdp_1_hsync, vdp_1_vsync;
  wire [7:0] vdp_1_b, vdp_1_g, vdp_1_r;

  vdp vdp_1 (
    .clk(clk), .rst(rst), .h_fp(12'h280), .h_sync(12'h290), .h_bp(12'h2f0), .h_total(12'h320), .h_neg(1'b1),
    .v_fp(12'h168), .v_sync(12'h19c), .v_bp(12'h19e), .v_total(12'h1c1), .v_neg(1'b0), .r(vdp_1_r),
    .g(vdp_1_g), .b(vdp_1_b), .hsync(vdp_1_hsync), .vsync(vdp_1_vsync));  // open: en_disp, x, y, line, frame
  VGA vga_1 (.R(vdp_1_r), .G(vdp_1_g), .B(vdp_1_b), .H(vdp_1_hsync), .V(vdp_1_vsync), .C(clk));

  // Other names for the same wires on the sheet: C = clk; R = rst

  // Notes on the sheet:
  //   clk: Hz: 2147483647
endmodule
