// Digital circuit vgasync.dig as structural Verilog
module vgasync (
  input  [11:0] x_i,
  input  [11:0] y_i,
  input  line_i,
  input  frame_i,
  input  [11:0] h_fp,
  input  [11:0] h_sync,
  input  [11:0] h_bp,
  input  h_neg,
  input  [11:0] v_fp,
  input  [11:0] v_sync,
  input  [11:0] v_bp,
  input  v_neg,
  input  clk,
  input  rst,
  output [11:0] x_o,
  output [11:0] y_o,
  output line_o,
  output frame_o,
  output hsync,
  output vsync,
  output en_disp
);

  wire H_2_blank, H_blank_bgn, H_sync_bgn, H_sync_end, V_2_blank, V_blank_bgn, V_sync_bgn, V_sync_end;

  sync H (
    .en(1'b1), .v(x_i), .fp(h_fp), .sync(h_sync), .bp(h_bp), .blank_bgn(H_blank_bgn), .sync_bgn(H_sync_bgn),
    .sync_end(H_sync_end));
  sync V (
    .en(line_i), .v(y_i), .fp(v_fp), .sync(v_sync), .bp(v_bp), .blank_bgn(V_blank_bgn),
    .sync_bgn(V_sync_bgn), .sync_end(V_sync_end));
  syncstate H_2 (
    .blank_end(line_i), .blank_bgn(H_blank_bgn), .sync_bgn(H_sync_bgn), .sync_end(H_sync_end), .neg(h_neg),
    .clk(clk), .rst(rst), .blank(H_2_blank), .sync(hsync));
  syncstate V_2 (
    .blank_end(frame_i), .blank_bgn(V_blank_bgn), .sync_bgn(V_sync_bgn), .sync_end(V_sync_end), .neg(v_neg),
    .clk(clk), .rst(rst), .blank(V_2_blank), .sync(vsync));
  nor nor_1 (en_disp, H_2_blank, V_2_blank);

  assign frame_o = frame_i;
  assign line_o = line_i;
  assign x_o = x_i;
  assign y_o = y_i;

  // Other names for the same wires on the sheet: C = clk; frame_t = frame_i; line_t = line_i; R = rst;
  //   x_t[11:0] = x_i; y_t[11:0] = y_i

  // Notes on the sheet:
  //   h_fp: default 3
  //   h_sync: default 5
  //   h_bp: default 5
  //   v_fp: default 3
  //   v_sync: default 5
  //   v_bp: default 5
endmodule
