// Digital circuit vga.dig as structural Verilog
module vga (
  input  clk,
  input  [15:0] H_res,
  input  [15:0] H_fp,
  input  [15:0] H_sync,
  input  [15:0] H_bp,
  input  H_neg,
  input  [15:0] V_res,
  input  [15:0] V_fp,
  input  [15:0] V_sync,
  input  [15:0] V_bp,
  input  V_neg,
  input  [15:0] colour,
  output [3:0] R,
  output [3:0] G,
  output [3:0] B,
  output H,
  output V,
  output [15:0] X,
  output [15:0] Y
);

  wire and_1_out, syncpulse_1_c, syncpulse_1_valid, syncpulse_2_valid;

  syncpulse syncpulse_1 (
    .en(1'b1), .clk(clk), .res(H_res), .fp(H_fp), .sync(H_sync), .bp(H_bp), .neg(H_neg), .V(X), .pulse(H),
    .valid(syncpulse_1_valid), .C(syncpulse_1_c));
  syncpulse syncpulse_2 (
    .en(syncpulse_1_c), .clk(clk), .res(V_res), .fp(V_fp), .sync(V_sync), .bp(V_bp), .neg(V_neg), .V(Y),
    .pulse(V), .valid(syncpulse_2_valid));  // open: C
  and and_1 (and_1_out, syncpulse_1_valid, syncpulse_2_valid);
  Multiplexer #(.Bits(4)) multiplexer_1 (.sel(and_1_out), .in_0(4'b0000), .in_1(colour[11:8]), .out(R));
  Multiplexer #(.Bits(4)) multiplexer_2 (.sel(and_1_out), .in_0(4'b0000), .in_1(colour[7:4]), .out(G));
  Multiplexer #(.Bits(4)) multiplexer_3 (.sel(and_1_out), .in_0(4'b0000), .in_1(colour[3:0]), .out(B));

  // Other names for the same wires on the sheet: C = clk

  // Notes on the sheet:
  //   clk: Hz: 2147483647
  //   H_res: default 639
  //   H_fp: default 16
  //   H_sync: default 96
  //   H_bp: default 48
  //   H_neg: default 1
  //   V_res: default 479
  //   V_fp: default 11
  //   V_sync: default 2
  //   V_bp: default 33
  //   V_neg: default 1
endmodule
