// Digital circuit vga_blinkenlights.dig as structural Verilog
module vga_blinkenlights (
  input  clock,
  input  [15:0] PC,
  input  [15:0] R0,
  input  [15:0] R1,
  input  [15:0] R2,
  input  [15:0] R3,
  input  [15:0] L_b,
  input  [15:0] R_b,
  input  [15:0] result,
  input  skip,
  input  jump,
  input  [4:0] op,
  input  [2:0] cond,
  input  [3:0] rd,
  input  [3:0] rs,
  input  rdv,
  input  rsv,
  input  halt,
  input  error,
  input  [15:0] imm,
  input  immv,
  input  [2:0] aluop,
  input  clock_slow,
  input  [15:0] CD,
  output [3:0] R,
  output [3:0] G,
  output [3:0] B,
  output hs,
  output vs,
  output de,
  output [10:0] CA
);

  wire error_t, halt_t, immv_t, jump_t, L_v, R_v, rdv_t, register_9_q, register_23_q, register_28_q,
       register_29_q, register_30_q, register_31_q, register_32_q, res_v, rsv_t, skip_t, vb;
  wire [2:0] aluop_t, cond_t, register_11_q, register_25_q;
  wire [3:0] rd_t, register_26_q, register_27_q, rs_t;
  wire [4:0] op_t, register_24_q;
  wire [6:0] aluop_c_o, error_c_o, halt_c_o, jump_c_o, L_c_o, Op_c_o, PC_c_o, R0_c_o, R1_c_o, R2_c_o, R3_c_o,
       R_c_o, rd_2_c_o, rd_c_o, result_c_o, rs_c_o, skip_c_o, vga_display_1_p12;
  wire [7:0] aluop_cx_o, aluop_cy_o, error_cx_o, error_cy_o, halt_cx_o, halt_cy_o, jump_cx_o, jump_cy_o,
       L_cx_o, L_cy_o, Op_cx_o, Op_cy_o, PC_cx_o, PC_cy_o, R0_cx_o, R0_cy_o, R1_cx_o, R1_cy_o, R2_cx_o,
       R2_cy_o, R3_cx_o, R3_cy_o, R_cx_o, R_cy_o, rd_2_cx_o, rd_2_cy_o, rd_cx_o, rd_cy_o, result_cx_o,
       result_cy_o, rs_cx_o, rs_cy_o, skip_cx_o, skip_cy_o, vga_display_1_p22, vga_display_1_p23;
  wire [11:0] aluop_bg_o, aluop_fg_o, error_bg_o, error_fg_o, halt_bg_o, halt_fg_o, jump_bg_o, jump_fg_o,
       L_bg_o, L_fg_o, Op_bg_o, Op_fg_o, PC_bg_o, PC_fg_o, R0_bg_o, R0_fg_o, R1_bg_o, R1_fg_o, R2_bg_o,
       R2_fg_o, R3_bg_o, R3_fg_o, R_bg_o, R_fg_o, rd_2_bg_o, rd_2_fg_o, rd_bg_o, rd_fg_o, result_bg_o,
       result_fg_o, rs_bg_o, rs_fg_o, skip_bg_o, skip_fg_o, vga_display_1_p13, vga_display_1_p14;
  wire [15:0] imm_t, L_t, PC_t, R0_t, R1_t, R2_t, R3_t, R_t, register_1_q, register_2_q, register_3_q,
       register_4_q, register_5_q, register_6_q, register_7_q, register_8_q, register_10_q, result_t;

  Register #(.Bits(16)) register_1 (.D(PC), .C(clock_slow), .en(1'b1), .Q(register_1_q));
  Register #(.Bits(16)) register_2 (.D(R0), .C(clock_slow), .en(1'b1), .Q(register_2_q));
  Register #(.Bits(16)) register_3 (.D(R1), .C(clock_slow), .en(1'b1), .Q(register_3_q));
  Register #(.Bits(16)) register_4 (.D(R2), .C(clock_slow), .en(1'b1), .Q(register_4_q));
  Register #(.Bits(16)) register_5 (.D(R3), .C(clock_slow), .en(1'b1), .Q(register_5_q));
  Register #(.Bits(16)) register_6 (.D(L_b), .C(clock_slow), .en(1'b1), .Q(register_6_q));
  Register #(.Bits(16)) register_7 (.D(R_b), .C(clock_slow), .en(1'b1), .Q(register_7_q));
  Register #(.Bits(16)) register_8 (.D(result), .C(clock_slow), .en(1'b1), .Q(register_8_q));
  Register register_9 (.D(skip), .C(clock_slow), .en(1'b1), .Q(register_9_q));
  Register #(.Bits(16)) register_10 (.D(imm), .C(clock_slow), .en(1'b1), .Q(register_10_q));
  Register #(.Bits(3)) register_11 (.D(aluop), .C(clock_slow), .en(1'b1), .Q(register_11_q));
  Register #(.Bits(16)) register_12 (.D(register_1_q), .C(clock), .en(vb), .Q(PC_t));
  Register #(.Bits(16)) register_13 (.D(register_2_q), .C(clock), .en(vb), .Q(R0_t));
  Register #(.Bits(16)) register_14 (.D(register_3_q), .C(clock), .en(vb), .Q(R1_t));
  Register #(.Bits(16)) register_15 (.D(register_4_q), .C(clock), .en(vb), .Q(R2_t));
  Register #(.Bits(16)) register_16 (.D(register_5_q), .C(clock), .en(vb), .Q(R3_t));
  Register #(.Bits(16)) register_17 (.D(register_6_q), .C(clock), .en(vb), .Q(L_t));
  Register #(.Bits(16)) register_18 (.D(register_7_q), .C(clock), .en(vb), .Q(R_t));
  Register #(.Bits(16)) register_19 (.D(register_8_q), .C(clock), .en(vb), .Q(result_t));
  Register register_20 (.D(register_9_q), .C(clock), .en(vb), .Q(skip_t));
  Register #(.Bits(16)) register_21 (.D(register_10_q), .C(clock), .en(vb), .Q(imm_t));
  Register #(.Bits(3)) register_22 (.D(register_11_q), .C(clock), .en(vb), .Q(aluop_t));
  Register register_23 (.D(jump), .C(clock_slow), .en(1'b1), .Q(register_23_q));
  Register #(.Bits(5)) register_24 (.D(op), .C(clock_slow), .en(1'b1), .Q(register_24_q));
  Register #(.Bits(3)) register_25 (.D(cond), .C(clock_slow), .en(1'b1), .Q(register_25_q));
  Register #(.Bits(4)) register_26 (.D(rd), .C(clock_slow), .en(1'b1), .Q(register_26_q));
  Register #(.Bits(4)) register_27 (.D(rs), .C(clock_slow), .en(1'b1), .Q(register_27_q));
  Register register_28 (.D(rdv), .C(clock_slow), .en(1'b1), .Q(register_28_q));
  Register register_29 (.D(rsv), .C(clock_slow), .en(1'b1), .Q(register_29_q));
  Register register_30 (.D(halt), .C(clock_slow), .en(1'b1), .Q(register_30_q));
  Register register_31 (.D(error), .C(clock_slow), .en(1'b1), .Q(register_31_q));
  Register register_32 (.D(immv), .C(clock_slow), .en(1'b1), .Q(register_32_q));
  Register register_33 (.D(register_23_q), .C(clock), .en(vb), .Q(jump_t));
  Register #(.Bits(5)) register_34 (.D(register_24_q), .C(clock), .en(vb), .Q(op_t));
  Register #(.Bits(3)) register_35 (.D(register_25_q), .C(clock), .en(vb), .Q(cond_t));
  Register #(.Bits(4)) register_36 (.D(register_26_q), .C(clock), .en(vb), .Q(rd_t));
  Register #(.Bits(4)) register_37 (.D(register_27_q), .C(clock), .en(vb), .Q(rs_t));
  Register register_38 (.D(register_28_q), .C(clock), .en(vb), .Q(rdv_t));
  Register register_39 (.D(register_29_q), .C(clock), .en(vb), .Q(rsv_t));
  Register register_40 (.D(register_30_q), .C(clock), .en(vb), .Q(halt_t));
  Register register_41 (.D(register_31_q), .C(clock), .en(vb), .Q(error_t));
  Register register_42 (.D(register_32_q), .C(clock), .en(vb), .Q(immv_t));
  // vga_display vga_display_1: pin names not known; wires that end beside it: clock, 12'h280, 12'h10, 12'h60, 12'h30, 1'b1, 12'h1e0, 12'ha, 12'h2, 12'h22, 1'b1, vga_display_1_p12, vga_display_1_p13, vga_display_1_p14, CD, R, G, B, hs, vs, de, vga_display_1_p22, vga_display_1_p23, CA, vb
  vga_labelnum L (
    .CX_i(aluop_cx_o), .CY_i(aluop_cy_o), .C_i(aluop_c_o), .fg_i(aluop_fg_o), .bg_i(aluop_bg_o),
    .fg_lab(12'h1be), .fg_num(12'he07), .bg_c(12'h112), .CX_c(5'b00010), .CY_c(8'hc), .en(L_v),
    .L_0(7'b0100000), .L_1(7'b0111101), .L_2(7'b0100000), .N(L_t), .CX_o(L_cx_o), .CY_o(L_cy_o), .C_o(L_c_o),
    .fg_o(L_fg_o), .bg_o(L_bg_o));  // open: busy
  vga_opdisp u_Op (
    .CX_i(L_cx_o), .CY_i(L_cy_o), .C_i(L_c_o), .fg_i(L_fg_o), .bg_i(L_bg_o), .fg_c(12'h1e3), .bg_c(12'h112),
    .CX_c(5'b00001), .CY_c(8'hb), .en(1'b1), .op(op_t), .cond(cond_t), .CX_o(Op_cx_o), .CY_o(Op_cy_o),
    .C_o(Op_c_o), .fg_o(Op_fg_o), .bg_o(Op_bg_o));  // open: busy
  vga_labelnum u_PC (
    .CX_i(vga_display_1_p22), .CY_i(vga_display_1_p23), .C_i({7{1'b0}}), .fg_i({12{1'b0}}),
    .bg_i({12{1'b0}}), .fg_lab(12'h1be), .fg_num(12'he07), .bg_c(12'h112), .CX_c(5'b00001), .CY_c(8'h8),
    .en(1'b1), .L_0(7'b0100000), .L_1(7'b1010000), .L_2(7'b1000011), .N(PC_t), .CX_o(PC_cx_o),
    .CY_o(PC_cy_o), .C_o(PC_c_o), .fg_o(PC_fg_o), .bg_o(PC_bg_o));  // open: busy
  vga_hex u_R (
    .CX_i(Op_cx_o), .CY_i(Op_cy_o), .C_i(Op_c_o), .fg_i(Op_fg_o), .bg_i(Op_bg_o), .fg_c(12'he07),
    .bg_c(12'h112), .CX_c(6'b000111), .CY_c(8'hc), .N(R_t), .en(R_v), .CX_o(R_cx_o), .CY_o(R_cy_o),
    .C_o(R_c_o), .fg_o(R_fg_o), .bg_o(R_bg_o));  // open: busy
  vga_labelnum u_R0 (
    .CX_i(PC_cx_o), .CY_i(PC_cy_o), .C_i(PC_c_o), .fg_i(PC_fg_o), .bg_i(PC_bg_o), .fg_lab(12'h1be),
    .fg_num(12'he07), .bg_c(12'h112), .CX_c(5'b00011), .CY_c(8'h2), .en(1'b1), .L_0(7'b0100000),
    .L_1(7'b1010010), .L_2(7'b0110000), .N(R0_t), .CX_o(R0_cx_o), .CY_o(R0_cy_o), .C_o(R0_c_o),
    .fg_o(R0_fg_o), .bg_o(R0_bg_o));  // open: busy
  vga_hex u_result (
    .CX_i(R_cx_o), .CY_i(R_cy_o), .C_i(R_c_o), .fg_i(R_fg_o), .bg_i(R_bg_o), .fg_c(12'he07), .bg_c(12'h112),
    .CX_c(6'b000011), .CY_c(8'hc), .N(result_t), .en(res_v), .CX_o(result_cx_o), .CY_o(result_cy_o),
    .C_o(result_c_o), .fg_o(result_fg_o), .bg_o(result_bg_o));  // open: busy
  vga_labelnum u_R1 (
    .CX_i(R0_cx_o), .CY_i(R0_cy_o), .C_i(R0_c_o), .fg_i(R0_fg_o), .bg_i(R0_bg_o), .fg_lab(12'h1be),
    .fg_num(12'he07), .bg_c(12'h112), .CX_c(5'b00011), .CY_c(8'h3), .en(1'b1), .L_0(7'b0100000),
    .L_1(7'b1010010), .L_2(7'b0110001), .N(R1_t), .CX_o(R1_cx_o), .CY_o(R1_cy_o), .C_o(R1_c_o),
    .fg_o(R1_fg_o), .bg_o(R1_bg_o));  // open: busy
  vga_string u_jump (
    .CX_i(result_cx_o), .CY_i(result_cy_o), .C_i(result_c_o), .fg_i(result_fg_o), .bg_i(result_bg_o),
    .fg_c(12'h1be), .bg_c(12'h112), .CX_c(6'b000010), .CY_c(8'h7), .C_0(7'b1001010), .C_1(7'b1010101),
    .C_2(7'b1001101), .C_3(7'b1010000), .en(jump_t), .CX_o(jump_cx_o), .CY_o(jump_cy_o), .C_o(jump_c_o),
    .fg_o(jump_fg_o), .bg_o(jump_bg_o));
  vga_labelnum u_R2 (
    .CX_i(R1_cx_o), .CY_i(R1_cy_o), .C_i(R1_c_o), .fg_i(R1_fg_o), .bg_i(R1_bg_o), .fg_lab(12'h1be),
    .fg_num(12'he07), .bg_c(12'h112), .CX_c(5'b00011), .CY_c(8'h4), .en(1'b1), .L_0(7'b0100000),
    .L_1(7'b1010010), .L_2(7'b0110010), .N(R2_t), .CX_o(R2_cx_o), .CY_o(R2_cy_o), .C_o(R2_c_o),
    .fg_o(R2_fg_o), .bg_o(R2_bg_o));  // open: busy
  vga_string u_skip (
    .CX_i(jump_cx_o), .CY_i(jump_cy_o), .C_i(jump_c_o), .fg_i(jump_fg_o), .bg_i(jump_bg_o), .fg_c(12'he81),
    .bg_c(12'h112), .CX_c(6'b000011), .CY_c(8'h7), .C_0(7'b1010011), .C_1(7'b1001011), .C_2(7'b1001001),
    .C_3(7'b1010000), .en(skip_t), .CX_o(skip_cx_o), .CY_o(skip_cy_o), .C_o(skip_c_o), .fg_o(skip_fg_o),
    .bg_o(skip_bg_o));
  vga_labelnum u_R3 (
    .CX_i(R2_cx_o), .CY_i(R2_cy_o), .C_i(R2_c_o), .fg_i(R2_fg_o), .bg_i(R2_bg_o), .fg_lab(12'h1be),
    .fg_num(12'he07), .bg_c(12'h112), .CX_c(5'b00011), .CY_c(8'h5), .en(1'b1), .L_0(7'b0100000),
    .L_1(7'b1010010), .L_2(7'b0110011), .N(R3_t), .CX_o(R3_cx_o), .CY_o(R3_cy_o), .C_o(R3_c_o),
    .fg_o(R3_fg_o), .bg_o(R3_bg_o));  // open: busy
  vga_string u_halt (
    .CX_i(skip_cx_o), .CY_i(skip_cy_o), .C_i(skip_c_o), .fg_i(skip_fg_o), .bg_i(skip_bg_o), .fg_c(12'h2e3),
    .bg_c(12'h112), .CX_c(6'b000010), .CY_c(8'h2), .C_0(7'b1001000), .C_1(7'b1000001), .C_2(7'b1001100),
    .C_3(7'b1010100), .en(halt_t), .CX_o(halt_cx_o), .CY_o(halt_cy_o), .C_o(halt_c_o), .fg_o(halt_fg_o),
    .bg_o(halt_bg_o));
  vga_regdisp u_rd (
    .CX_i(R3_cx_o), .CY_i(R3_cy_o), .C_i(R3_c_o), .fg_i(R3_fg_o), .bg_i(R3_bg_o), .fg_c(12'h1be),
    .bg_c(12'h112), .CX_c(6'b000101), .CY_c(8'hb), .en(rdv_t), .R(rd_t), .J(jump_t), .sep(7'b0101100),
    .CX_o(rd_cx_o), .CY_o(rd_cy_o), .C_o(rd_c_o), .fg_o(rd_fg_o), .bg_o(rd_bg_o));  // open: busy
  vga_string u_error (
    .CX_i(halt_cx_o), .CY_i(halt_cy_o), .C_i(halt_c_o), .fg_i(halt_fg_o), .bg_i(halt_bg_o), .fg_c(12'he07),
    .bg_c(12'h112), .CX_c(6'b000011), .CY_c(8'h2), .C_0(7'b1000101), .C_1(7'b1010010), .C_2(7'b1010010),
    .C_3(7'b1000100), .en(error_t), .CX_o(error_cx_o), .CY_o(error_cy_o), .C_o(error_c_o), .fg_o(error_fg_o),
    .bg_o(error_bg_o));
  vga_regdisp u_rs (
    .CX_i(rd_cx_o), .CY_i(rd_cy_o), .C_i(rd_c_o), .fg_i(rd_fg_o), .bg_i(rd_bg_o), .fg_c(12'h1be),
    .bg_c(12'h112), .CX_c(6'b000110), .CY_c(8'hb), .en(rsv_t), .R(rs_t), .J(1'b0), .sep(7'b0100000),
    .CX_o(rs_cx_o), .CY_o(rs_cy_o), .C_o(rs_c_o), .fg_o(rs_fg_o), .bg_o(rs_bg_o));  // open: busy
  vga_regdisp rd_2 (
    .CX_i(error_cx_o), .CY_i(error_cy_o), .C_i(error_c_o), .fg_i(error_fg_o), .bg_i(error_bg_o),
    .fg_c(12'h1be), .bg_c(12'h112), .CX_c(6'b000010), .CY_c(8'hc), .en(res_v), .R(rd_t), .J(jump_t),
    .sep(7'b0111101), .CX_o(rd_2_cx_o), .CY_o(rd_2_cy_o), .C_o(rd_2_c_o), .fg_o(rd_2_fg_o), .bg_o(rd_2_bg_o));  // open: busy
  vga_aluopdisp u_aluop (
    .CX_i(rs_cx_o), .CY_i(rs_cy_o), .C_i(rs_c_o), .fg_i(rs_fg_o), .bg_i(rs_bg_o), .fg_c(12'he81),
    .bg_c(12'h112), .CX_c(6'b000110), .CY_c(8'hc), .en(1'b1), .aop(aluop_t), .CX_o(aluop_cx_o),
    .CY_o(aluop_cy_o), .C_o(aluop_c_o), .fg_o(aluop_fg_o), .bg_o(aluop_bg_o), .L_v(L_v), .R_v(R_v),
    .res_v(res_v));  // open: busy
  vga_hex result_2 (
    .CX_i(rd_2_cx_o), .CY_i(rd_2_cy_o), .C_i(rd_2_c_o), .fg_i(rd_2_fg_o), .bg_i(rd_2_bg_o), .fg_c(12'he07),
    .bg_c(12'h112), .CX_c(6'b000111), .CY_c(8'hb), .N(imm_t), .en(immv_t), .C_o(vga_display_1_p12),
    .fg_o(vga_display_1_p13), .bg_o(vga_display_1_p14));  // open: CX_o, CY_o, busy

  // Other names for the same wires on the sheet: C = clock; RC = clock_slow

  // Notes on the sheet:
  //   clock: Hz: 2147483647
endmodule
