// Digital circuit vga_charpos.dig as structural Verilog
module vga_charpos (
  input  [15:0] X,
  input  [15:0] Y,
  output [4:0] row,
  output [3:0] col,
  output [7:0] CX,
  output [7:0] CY
);

  // Pins of 4 and 5 bits meet at Y[4:0]

  assign col = X[3:0];
  assign CX = X[11:4];
  assign CY = Y[12:5];
  assign row = Y[4:0];
endmodule
