// Digital circuit vga_debugrender.dig as structural Verilog
module vga_debugrender (
  input  [15:0] db_D,
  input  clock,
  input  \signed ,
  input  hex,
  output [8:0] fb_A,
  output [6:0] fb_D,
  output fb_wen,
  output [3:0] colour,
  output [4:0] db_A
);

  wire and_1_out, call, colr, d_ff_1_q, dba, nop, plot, pos, ret, typ, write;
  wire [2:0] offset, type_q;
  wire [3:0] colour_q;
  wire [6:0] multiplexer_2_out, multiplexer_3_out, num2ascii_1_char, vga_aluopdisp_1_char, vga_opdisp_1_char,
       vga_regdisp_1_char;
  wire [7:0] d_ff_2_q_2, DispPC_out, multiplexer_1_out, plus_1_s, RA_q;
  wire [8:0] add_1_s, pos_q;
  wire [15:0] code_d, d_ff_2_q, value_q;

  D_FF d_ff_1 (.D(dba), .C(clock), .Q(d_ff_1_q));  // open: nQ
  Multiplexer #(.Bits(8)) multiplexer_1 (.sel(ret), .in_0(d_ff_2_q_2), .in_1(plus_1_s), .out(multiplexer_1_out));
  Register #(.Bits(16)) value (.D(db_D), .C(clock), .en(d_ff_1_q), .Q(value_q));
  CounterPreset #(.Bits(8)) DispPC (
    .en(1'b1), .C(clock), .dir(1'b0), .in(multiplexer_1_out), .ld(call), .clr(1'b0), .out(DispPC_out));  // open: ovf
  and and_1 (and_1_out, call, ~ret);  // And
  num2ascii num2ascii_1 (
    .num(value_q), .s(\signed ), .hex(hex), .clock(clock), .digit(offset), .char(num2ascii_1_char));
  vga_opdisp vga_opdisp_1 (.fullop(value_q), .digit(offset), .char(vga_opdisp_1_char));
  vga_regdisp vga_regdisp_1 (.\reg (value_q), .digit(offset), .char(vga_regdisp_1_char));
  vga_aluopdisp vga_aluopdisp_1 (.aluop(value_q), .digit(offset), .char(vga_aluopdisp_1_char));
  ROM #(.AddrBits(8), .Bits(16)) code (.A(DispPC_out), .sel(1'b1), .D(code_d));
  Register #(.Bits(8)) RA (.D(DispPC_out), .C(clock), .en(and_1_out), .Q(RA_q));
  Multiplexer #(.Selector_Bits(3), .Bits(7)) multiplexer_2 (
    .sel(offset), .in_0(7'b0111101), .in_1(7'b0100000), .in_2(7'b0100000), .in_3(7'b0100000),
    .in_4(7'b0100000), .in_5(7'b0100000), .in_6(7'b0100000), .in_7(7'b0100000), .out(multiplexer_2_out));
  D_FF #(.Bits(16)) d_ff_2 (.D(code_d), .C(clock), .Q({d_ff_2_q[15:12], ret, d_ff_2_q_2, d_ff_2_q[2:0]}));  // open: nQ
  Add #(.Bits(8)) plus_1 (.a(RA_q), .b({8{1'b0}}), .c_i(1'b1), .s(plus_1_s));  // open: c_o
  Multiplexer #(.Selector_Bits(3), .Bits(7)) multiplexer_3 (
    .sel(type_q), .in_0(num2ascii_1_char), .in_1(vga_opdisp_1_char), .in_2(vga_regdisp_1_char),
    .in_3(vga_aluopdisp_1_char), .in_4({7{1'b0}}), .in_5({7{1'b0}}), .in_6({7{1'b0}}),
    .in_7(multiplexer_2_out), .out(multiplexer_3_out));
  Decoder #(.Selector_Bits(3)) decoder_1 (
    .sel(d_ff_2_q[2:0]), .out_0(nop), .out_1(plot), .out_2(call), .out_3(typ), .out_4(pos), .out_6(dba),
    .out_7(colr));  // open: out_5
  Register #(.Bits(5)) u_db_A (.D(d_ff_2_q_2[4:0]), .C(clock), .en(dba), .Q(db_A));
  Register #(.Bits(9)) u_pos (.D({ret, d_ff_2_q_2}), .C(clock), .en(pos), .Q(pos_q));
  Register #(.Bits(3)) u_Offset (.D(d_ff_2_q_2[2:0]), .C(clock), .en(plot), .Q(offset));
  Register #(.Bits(4)) u_colour (.D(d_ff_2_q_2[3:0]), .C(clock), .en(colr), .Q(colour_q));
  Register u_plot (.D(plot), .C(clock), .en(1'b1), .Q(write));
  Register #(.Bits(3)) \type  (.D(d_ff_2_q_2[2:0]), .C(clock), .en(typ), .Q(type_q));
  Register #(.Bits(7)) char (.D(multiplexer_3_out), .C(clock), .en(write), .Q(fb_D));
  Add #(.Bits(9)) add_1 (.a(pos_q), .b({{6{1'b0}}, offset}), .c_i(1'b0), .s(add_1_s));  // open: c_o
  Register #(.Bits(9)) register_1 (.D(add_1_s), .C(clock), .en(write), .Q(fb_A));
  Register #(.Bits(4)) colour_2 (.D(colour_q), .C(clock), .en(1'b1), .Q(colour));
  Register wen (.D(write), .C(clock), .en(1'b1), .Q(fb_wen));

  // Other names for the same wires on the sheet: C = clock

  // Notes on the sheet:
  //   contents of code (hex, n*v repeats v):
  //   5a,0,0,0,1,9,11,19,21,29,802,3,27,6,10c,a,26,14c,a,46,18c,a,66,1cc,a,e,20c,a,2e,24c,
  //   a,4e,28c,a,6e,2cc,a,16,30c,a,36,34c,a,56,38c,a,76,3cc,a,1e,40c,a,3e,44c,a,5e,48c,
  //   a,7e,4cc,a,b6,6cc,a,a6,84c,a,96,88c,a,9e,8cc,a,be,a0c,a,86,37,b,60c,1,0,9,0,11,0,
  //   19,0,21,0,29,0,31,0,39,17,13,ce,6a4,1,9,11,c6,664,1,9,11,80c,1,9,11,8e,1b,1f,8b4,
  //   9,11,834,3b,17,1,884,1,5a
endmodule
