// Digital circuit vga_frontpanel.dig as structural Verilog
module vga_frontpanel (
  input  clock,
  input  [15:0] PC,
  input  [15:0] R0,
  input  [15:0] R1,
  input  [15:0] R2,
  input  [15:0] R3,
  input  en,
  input  [15:0] L,
  input  [15:0] R,
  input  [4:0] op,
  input  [2:0] cond,
  input  jump,
  input  skip,
  input  [15:0] result,
  input  clock_slow,
  input  [3:0] rs,
  input  [3:0] rd,
  input  rd_valid,
  input  rs_valid,
  input  halt,
  input  error,
  input  [15:0] imm,
  input  imm_valid,
  input  [2:0] aluop
);

  wire C, vga_blinkenlights_1_p26, vga_blinkenlights_1_p27, vga_blinkenlights_1_p28, vga_blinkenlights_1_p29,
       vga_blinkenlights_1_p30;
  wire [7:0] Map_d, vga_blinkenlights_1_p25;
  wire [9:0] vga_blinkenlights_1_p32;
  wire [10:0] vga_blinkenlights_1_p31;
  wire [15:0] Char_d, Tile_d, vga_blinkenlights_1_p24;

  and and_1 (C, en, clock);
  // vga_blinkenlights vga_blinkenlights_1: pin names not known; wires that end beside it: C, PC, R0, R1, R2, R3, L, R, result, skip, jump, op, cond, rd, rs, rd_valid, rs_valid, halt, error, imm, imm_valid, aluop, clock_slow, vga_blinkenlights_1_p24, vga_blinkenlights_1_p25, vga_blinkenlights_1_p26, vga_blinkenlights_1_p27, vga_blinkenlights_1_p28, vga_blinkenlights_1_p29, vga_blinkenlights_1_p30, vga_blinkenlights_1_p31, vga_blinkenlights_1_p32
  VGA vga_1 (
    .R(vga_blinkenlights_1_p26), .G(vga_blinkenlights_1_p27), .B(vga_blinkenlights_1_p28),
    .H(vga_blinkenlights_1_p29), .V(vga_blinkenlights_1_p30), .C(C));
  ROM #(.AddrBits(11), .Bits(16)) Char (.A(vga_blinkenlights_1_p31), .sel(1'b1), .D(Char_d));
  ROM #(.AddrBits(10), .Bits(16)) Tile (.A(vga_blinkenlights_1_p31[9:0]), .sel(1'b1), .D(Tile_d));
  ROM #(.AddrBits(9), .Bits(8)) Map (.A(vga_blinkenlights_1_p32[8:0]), .sel(1'b1), .D(Map_d));
  D_FF #(.Bits(16)) d_ff_1 (.D(Char_d), .C(C), .Q(vga_blinkenlights_1_p24));  // open: nQ
  D_FF #(.Bits(16)) d_ff_2 (.D(Tile_d), .C(C));  // open: Q, nQ
  D_FF #(.Bits(8)) d_ff_3 (.D(Map_d), .C(C), .Q(vga_blinkenlights_1_p25));  // open: nQ

  // Other names for the same wires on the sheet: aluop_t[2:0] = aluop; cond_t[2:0] = cond; error_t = error;
  //   halt_t = halt; imm_t[15:0] = imm; imv_t = imm_valid; jump_t = jump; L_t[15:0] = L; op_t[4:0] = op;
  //   PC_t[15:0] = PC; R0_t[15:0] = R0; R1_t[15:0] = R1; R2_t[15:0] = R2; R3_t[15:0] = R3; R_t[15:0] = R;
  //   rd_t[3:0] = rd; rdv_t = rd_valid; result_t[15:0] = result; rs_t[3:0] = rs; rsv_t = rs_valid; SC = clock_slow;
  //   skip_t = skip

  // Notes on the sheet:
  //   clock: Hz: 2147483647
  //   contents of Char (hex, n*v repeats v):
  //   0,0,0,0,0,0,0,0,0,0,0,0,0,0,0,0,0,0,0,0,0,0,0,0,0,0,0,0,0,0,0,0,0,0,0,180,180,180,
  //   180,180,180,180,180,0,0,180,180,180,180,180,180,180,180,0,0,0,0,0,0,0,0,0,0,0,0,3e7c,
  //   1e78,0,0,0,0,0,0,0,0,0,0,0,0,0,0,0,0,0,0,0,0,0,0,0,0,0,0,0,0,0,0,3e7c,3ffc,4182,6186,
  //   6186,6186,6186,6186,6186,4182,3e7c,3e7c,4182,6186,6186,6186,6186,6186,6186,4182,3ffc,
  //   3e7c,0,0,0,0,0,0,0,0,0,0,3e7c,3ff8,4180,6180,6180,6180,6180,6180,6180,4180,3e7c,3e7c,
  //   182,186,186,186,186,186,186,182,1ffc,3e7c,0,0,0,0,0,0,0,0,0,0,3e00,3f00,4188,6188,
  //   6198,61b0,61b0,61e0,61e0,4180,3e7c,3e7c,182,786,786,d86,d86,1986,1186,1182,fc,7c,
  //   0,0,0,0,0,0,0,0,0,0,3e00,3f00,4180,6180,6180,6180,6180,6180,6180,4180,3f00,3e00,4000,
  //   6060,6060,6030,6030,6018,6008,4000,3e78,3e7c,0,0,0,0,0,0,0,0,0,0,0,0,8,8,18,30,30,
  //   60,60,0,0,0,0,0,0,0,0,0,0,0,0,0,0,0,0,0,0,0,0,0,0,0,7c,78,200,600,600,c00,800,1800,
  //   1000,0,0,0,0,1000,1800,800,c00,600,600,200,78,7c,0,0,0,0,0,0,0,0,0,0,3e00,1e00,40,
  //   60,60,30,10,18,8,0,0,0,0,8,18,10,30,60,60,40,1e00,3e00,0,0,0,0,0,0,0,0,0,0,0,0,1188,
  //   1188,1998,db0,db0,7e0,7e0,180,3e7c,3e7c,180,7e0,7e0,db0,db0,1998,1188,1188,0,0,0,
  //   0,0,0,0,0,0,0,0,0,0,0,180,180,180,180,180,180,180,180,3e7c,3e7c,180,180,180,180,180,
  //   180,180,180,0,0,0,0,0,0,0,0,0,0,0,0,0,0,0,0,0,0,0,0,0,0,0,0,0,600,600,c00,c00,1800,
  //   1000,1000,0,0,0,0,0,0,0,0,0,0,0,0,0,0,0,0,0,0,0,0,0,0,3e7c,3e7c,0,0,0,0,0,0,0,0,0,
  //   0,0,0,0,0,0,0,0,0,0,0,0,0,0,0,0,0,0,0,0,0,0,0,0,0,0,0,0,0,0,0,180,180,0,0,0,0,0,0,
  //   0,0,0,0,0,0,8,8,18,30,30,60,60,0,0,0,0,600,600,c00,c00,1800,1000,1000,0,0,0,0,0,0,
  //   0,0,0,0,0,0,3e7c,3e7c,4006,600e,601a,6032,6036,6066,6066,6006,0,0,6006,6606,6606,
  //   6c06,4c06,5806,7006,6002,3e7c,3e7c,0,0,0,0,0,0,0,0,0,0,3e00,1f00,180,180,180,180,
  //   180,180,180,180,0,0,180,180,180,180,180,180,180,180,1ff8,3e7c,0,0,0,0,0,0,0,0,0,0,
  //   3e7c,1e7c,2,6,6,6,6,6,6,2,3e7c,3e7c,4000,6000,6000,6000,6000,6000,6000,4000,3e78,
  //   3e7c,0,0,0,0,0,0,0,0,0,0,3e7c,1e7c,2,6,6,6,6,6,6,2,3e7c,3e7c,2,6,6,6,6,6,6,2,1e7c,
  //   3e7c,0,0,0,0,0,0,0,0,0,0,0,4002,6006,6006,6006,6006,6006,6006,6006,4002,3e7c,3e7c,
  //   2,6,6,6,6,6,6,6,2,0,0,0,0,0,0,0,0,0,0,0,3e7c,3e78,4000,6000,6000,6000,6000,6000,6000,
  //   4000,3e7c,3e7c,2,6,6,6,6,6,6,2,1e7c,3e7c,0,0,0,0,0,0,0,0,0,0,3e7c,3e78,4000,6000,
  //   6000,6000,6000,6000,6000,4000,3e7c,3e7c,4002,6006,6006,6006,6006,6006,6006,4002,3e7c,
  //   3e7c,0,0,0,0,0,0,0,0,0,0,3e7c,1e7c,2,6,6,6,6,6,6,6,0,0,6,6,6,6,6,6,6,6,2,0,0,0,0,
  //   0,0,0,0,0,0,0,3e7c,3e7c,4002,6006,6006,6006,6006,6006,6006,4002,3e7c,3e7c,4002,6006,
  //   6006,6006,6006,6006,6006,4002,3e7c,3e7c,0,0,0,0,0,0,0,0,0,0,3e7c,3e7c,4002,6006,6006,
  //   6006,6006,6006,6006,4002,3e7c,3e7c,2,6,6,6,6,6,6,2,1e7c,3e7c,0,0,0,0,0,0,0,0,0,0,
  //   0,0,0,0,0,180,180,0,0,0,0,0,0,0,0,180,180,0,0,0,0,0,0,0,0,0,0,0,0,0,0,0,0,0,180,180,
  //   180,180,180,180,180,180,0,0,0,600,600,c00,c00,1800,1000,1000,0,0,0,0,0,0,0,0,0,0,
  //   0,0,0,0,40,c0,c0,180,180,300,300,0,0,0,0,300,300,180,180,c0,c0,40,0,0,0,0,0,0,0,0,
  //   0,0,0,0,0,0,0,0,0,3e7c,3e7c,0,0,0,0,0,0,0,0,1e78,3e7c,0,0,0,0,0,0,0,0,0,0,0,0,0,0,
  //   0,0,0,200,300,300,180,180,c0,c0,0,0,0,0,c0,c0,180,180,300,300,200,0,0,0,0,0,0,0,0,
  //   0,0,0,0,3e7c,1e7c,2,6,6,6,6,6,6,2,7c,fc,180,180,180,180,180,180,180,180,0,0,0,0,0,
  //   0,0,0,0,0,0,0,3e7c,3ffc,4182,6186,6186,6186,6186,6186,6186,6182,fc,7c,6000,6000,6000,
  //   6000,6000,6000,6000,4000,3e78,3e7c,0,0,0,0,0,0,0,0,0,0,3e7c,3e7c,4002,6006,6006,6006,
  //   6006,6006,6006,4002,3e7c,3e7c,4002,6006,6006,6006,6006,6006,6006,6006,4002,0,0,0,
  //   0,0,0,0,0,0,0,0,3e7c,1ffc,182,186,186,186,186,186,186,182,3e7c,3e7c,182,186,186,186,
  //   186,186,186,182,1ffc,3e7c,0,0,0,0,0,0,0,0,0,0,3e7c,3e78,4000,6000,6000,6000,6000,
  //   6000,6000,6000,0,0,6000,6000,6000,6000,6000,6000,6000,4000,3e78,3e7c,0,0,0,0,0,0,
  //   0,0,0,0,3e7c,1ffc,182,186,186,186,186,186,186,186,0,0,186,186,186,186,186,186,186,
  //   182,1ffc,3e7c,0,0,0,0,0,0,0,0,0,0,3e7c,3e78,4000,6000,6000,6000,6000,6000,6000,4000,
  //   3e7c,3e7c,4000,6000,6000,6000,6000,6000,6000,4000,3e78,3e7c,0,0,0,0,0,0,0,0,0,0,3e7c,
  //   3e78,4000,6000,6000,6000,6000,6000,6000,4000,3e7c,3e7c,4000,6000,6000,6000,6000,6000,
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  //   contents of Tile (hex, n*v repeats v):
  //   0,0,0,0,0,0,0,0,0,0,4000,d000,d000,d000,d000,d000,0,0,1,7,7,7,7,7,1550,7ff0,7fd0,
  //   1540,0,0,0,0,554,ffd,7fd,154,0,0,0,0,1550,7ff4,fff4,d56d,d07d,d07d,d07d,d07d,0,0,
  //   0,340,740,7d0,1f4,1f4,0,0,0,1c0,1d0,7d0,1f40,1f40,0,0,4000,d1c0,d1d0,d7d0,ef40,ef40,
  //   0,0,1,347,747,7d7,1fb,1fb,d000,d000,d000,4000,4000,d000,d000,d000,7,7,7,1,1,7,7,7,
  //   140,1be4,2ff8,7ffd,7ffd,2ff8,1be4,140,0,140,7d0,1ff4,1ff4,7d0,140,0,d07d,d07d,d56d,
  //   fff4,7ff4,156d,7d,7d,7,7,7,1,0,14,7d,7d,7d,7d,14,0,0,0,0,0,7d,7d,14,0,0,14,7d,7d,
  //   7d00,7d00,1400,0,0,1400,7d00,7d00,fd00,fd00,e950,7ff4,7ff4,e950,fd00,fd00,7f,7f,56b,
  //   1ffd,1ffd,56b,7f,7f,d000,d000,d550,7ff4,7ff4,d550,d000,d000,7,7,557,1ffd,1ffd,557,
  //   7,7,0,0,0,0,0,1400,7d00,7d00,0,0,1550,7ff4,7ff4,1550,0,0,0,0,554,1ffd,1ffd,554,0,
  //   0,d000,d000,d000,d000,d000,4000,0,0,7,7,7,7,7,1,0,0,7d,7d,7d,7d,156d,7ff4,7ff4,1550,
  //   1f4,1f4,7d0,740,154,7fd,ffd,554,1f4,1f4,7d0,740,340,0,0,0,0,0,0,0,154,7fd,ffd,554,
  //   0,0,0,0,1540,7fd0,7ff0,1550,1f40,1f40,7d0,1d0,1c0,0,0,0,ef40,ef40,d7d0,d1d0,d1c0,
  //   4000,0,0,1fb,1fb,7d7,747,347,1,0,0,0,0,0,0,4000,d000,d000,4000,0,0,0,0,1,7,7,1,1550,
  //   7ff4,7ff4,156d,7d,7d,7d,7d,554,1ffd,1ffd,7e54,7f40,7bd0,7af4,7df4,1550,7ff0,ffd0,
  //   d540,d000,d000,d000,d000,554,1ffd,1ffd,7954,7d00,7d00,7d00,7d00,0,0,1d,7d,7d,7d,7d,
  //   7d,0,0,7400,7d00,7d00,7d00,7d00,7d00,7d,7d,7d,14,14,147d,7d7d,7d7d,7d7d,7d7d,7d14,
  //   1400,1400,7d00,7d00,7d00,0,0,1550,7ff4,7ff4,156d,7d,7d,7d00,7d00,7954,1ffd,1ffd,554,
  //   0,0,7d00,7d00,7954,1ffd,1ffd,7954,7d00,7d00,7d,7d,156d,7ff4,7ff4,1550,0,0,0,0,554,
  //   1ffd,1ffd,7954,7d00,7d00,7d,7d,156d,7ff4,7ff4,156d,7d,7d,7d00,7d00,7d00,1400,1400,
  //   7d00,7d00,7d00,d000,d000,d000,4000,0,1400,7d00,7d00,7,7,7,1,0,0,0,0,0,0,0,0,4000,
  //   d000,d000,d000,7d00,7d00,7954,1ffd,1fff,557,7,7,1f7d,1fad,7ed,1fd,15bd,7ff4,7ff4,
  //   1550,7d00,7d00,7d00,7d00,7954,1ffd,1ffd,554,d000,d000,d000,d000,e540,ffd0,7ff0,1550,
  //   7,7,7,7,15b,7ff,ffd,554,7d00,7d00,7d00,7d00,7d00,7400,0,0,1550,7ff4,fff4,e56d,d07d,
  //   d07d,d07d,d07d,554,1ffd,1fff,795b,7d07,7d07,7d07,7d07,1550,7ff0,ffd0,e540,d000,d000,
  //   d000,d000,554,ffd,7ff,15b,7,7,7,7,0,0,1d,7d,1fd,7ed,1fad,1f7d,0,0,7400,7d00,7f40,
  //   7bd0,7af4,7df4,d07d,d07d,d07d,4014,14,7d,7d,7d,7d07,7d07,7957,1fff,1ffd,554,0,0,7d07,
  //   7d07,7957,1ffd,1ffd,7957,7d07,7d07,7d,7d,7d,14,14,7d,7d,7d,7d07,7d07,7d07,1401,1401,
  //   7d07,7d07,7d07,0,0,0,0,14,7d,7d,7d,7d7d,7d7d,147d,14,4014,d07d,d07d,d07d,7d7d,7d7d,
  //   7d14,1400,1401,7d07,7d07,7d07,7d7d,7d7d,147d,14,14,7d,7d,7d,7d00,7d00,7d00,1400,1400,
  //   7d14,7d7d,7d7d,7d,7d,7d,7d,7d,1d,0,0,7d07,7d07,7d07,7d07,795b,1fff,1ffd,554,d07d,
  //   d07d,d07d,d07d,d07d,401d,0,0,7d07,7d07,7d07,7d07,7d07,7401,0,0,7df4,7af4,7bd0,7f40,
  //   7d00,7400,0,0,554,ffd,7fd,154,740,7d0,1f4,1f4,0,0,0,0,0,14,7d,7d,7d00,7d00,7d00,1400,
  //   0,14,7d,7d,7d,7d,7d,14,4014,d07d,d07d,d07d,7d00,7d00,7d00,1400,1401,7d07,7d07,7d07,
  //   7d00,7d00,1400,0,4000,d000,d000,d000,7d,7d,14,0,1,7,7,7,7d00,7d00,1400,0,0,0,0,0,
  //   7df4,7af4,7bd0,7f40,7e54,1ffd,1ffd,554,1f7d,1fad,7ed,1fd,7d,1d,0,0,d07d,d07d,d07d,
  //   d07d,e56d,fff4,7ff4,1550,1f40,1f40,7d0,1d0,1540,7fd0,7ff0,1550
  //   contents of Map (hex, n*v repeats v):
  //   0,0,0,0,0,0,1,2,a,b,1a,1b,3,4,0,0,0,0,0,0,c,0,0,0,0,0,0,d,0,0,0,0,0,0,0,0,5,2,e,f,
  //   1c,1d,0,6,0,10,0,0,6,4,11,0,1e,1f,3,7,0,12,20,21,8,9,13,14,22,23,1,2,15,16,1a,1b,
  //   0,0,17,0,21,0,0,0,18,19,0,0,0,0,0,0,24,25,0,6,17,10,21,0,26,27,2c,2d,39,3a,28,2,a,
  //   b,3b,3c,3,29,2e,2f,1c,1f,3,29,18,30,20,3a,2a,2b,31,30,0,3d,26,4,31,32,20,3a,26,4,
  //   33,32,1c,3a,3,29,0,34,0,3d,26,29,33,30,1c,3a,26,29,31,30,20,3a,24,25,0,0,24,25,1,
  //   2,35,36,21,0,0,6,0,11,0,1e,0,0,18,19,20,1f,7,0,12,0,21,0,3,29,37,38,1a,1b,3e,3f,44,
  //   45,1c,1f,26,29,33,30,4e,3d,40,3f,15,46,3b,4f,26,4,47,0,1c,1f,40,3f,a,48,3b,4f,26,
  //   4,33,19,1c,1f,26,4,33,19,4e,0,26,4,47,32,1c,3a,2a,2b,33,30,4e,3d,40,41,a,b,3b,3c,
  //   0,29,49,34,1c,3a,2a,6,33,11,4e,1e,2a,0,47,0,1c,1f,42,43,4a,4b,50,51,42,2b,4c,4d,4e,
  //   52,26,29,47,34,1c,3a,26,29,33,2f,4e,0,26,29,47,4d,1c,5b,26,29,33,55,4e,1e,26,4,31,
  //   32,20,3a,40,41,a,b,1a,1b,2a,2b,47,34,1c,3a,2a,6,2c,10,5c,0,2a,2b,56,57,5d,4f,7,6,
  //   12,11,21,1e,7,6,58,59,1a,1b,3,53,17,10,5e,1f,26,0,47,0,1c,0,7,0,5a,54,0,1e,0,29,0,
  //   34,0,3a,17,54,21,1e,0,0,0,0,0,0,20,1f
endmodule
