// Digital circuit vga_hex.dig as structural Verilog
module vga_hex (
  input  [7:0] CX_i,
  input  [7:0] CY_i,
  input  [6:0] C_i,
  input  [11:0] fg_i,
  input  [11:0] bg_i,
  input  [11:0] fg_c,
  input  [11:0] bg_c,
  input  [5:0] CX_c,
  input  [7:0] CY_c,
  input  [15:0] N,
  input  en,
  output [7:0] CX_o,
  output [7:0] CY_o,
  output [6:0] C_o,
  output [11:0] fg_o,
  output [11:0] bg_o
);

  wire [6:0] digit2ascii_1_a, digit2ascii_2_a, digit2ascii_3_a, digit2ascii_4_a;

  digit2ascii digit2ascii_1 (.D(N[15:12]), .A(digit2ascii_1_a));
  digit2ascii digit2ascii_2 (.D(N[7:4]), .A(digit2ascii_2_a));
  digit2ascii digit2ascii_3 (.D(N[11:8]), .A(digit2ascii_3_a));
  digit2ascii digit2ascii_4 (.D(N[3:0]), .A(digit2ascii_4_a));
  vga_string vga_string_1 (
    .CX_i(CX_i), .CY_i(CY_i), .C_i(C_i), .fg_i(fg_i), .bg_i(bg_i), .fg_c(fg_c), .bg_c(bg_c), .CX_c(CX_c),
    .CY_c(CY_c), .C_0(digit2ascii_1_a), .C_1(digit2ascii_3_a), .C_2(digit2ascii_2_a), .C_3(digit2ascii_4_a),
    .en(en), .CX_o(CX_o), .CY_o(CY_o), .C_o(C_o), .fg_o(fg_o), .bg_o(bg_o));
endmodule
