// Digital circuit vga_opdisp.dig as structural Verilog
module vga_opdisp (
  input  [7:0] CX_i,
  input  [7:0] CY_i,
  input  [6:0] C_i,
  input  [11:0] fg_i,
  input  [11:0] bg_i,
  input  [11:0] fg_c,
  input  [11:0] bg_c,
  input  [4:0] CX_c,
  input  [7:0] CY_c,
  input  en,
  input  [4:0] op,
  input  [2:0] cond,
  output [7:0] CX_o,
  output [7:0] CY_o,
  output [6:0] C_o,
  output [11:0] fg_o,
  output [11:0] bg_o,
  output busy
);

  wire [6:0] H1_c_o, op2ascii_1_l0, op2ascii_1_l1, op2ascii_1_l2, op2ascii_1_l3, op2ascii_1_l4, op2ascii_1_l5;
  wire [7:0] H1_cx_o, H1_cy_o;
  wire [11:0] H1_bg_o, H1_fg_o;

  op2ascii op2ascii_1 (
    .I(op), .C(cond), .L0(op2ascii_1_l0), .L1(op2ascii_1_l1), .L2(op2ascii_1_l2), .L3(op2ascii_1_l3),
    .L4(op2ascii_1_l4), .L5(op2ascii_1_l5));
  vga_string H1 (
    .CX_i(CX_i), .CY_i(CY_i), .C_i(C_i), .fg_i(fg_i), .bg_i(bg_i), .fg_c(fg_c), .bg_c(bg_c),
    .CX_c({CX_c, 1'b0}), .CY_c(CY_c), .C_0(7'b0100000), .C_1(op2ascii_1_l0), .C_2(op2ascii_1_l1),
    .C_3(op2ascii_1_l2), .en(en), .CX_o(H1_cx_o), .CY_o(H1_cy_o), .C_o(H1_c_o), .fg_o(H1_fg_o), .bg_o(H1_bg_o));
  // vga_string H2: pin names not known; wires that end beside it: H1_cx_o, H1_cy_o, H1_c_o, H1_fg_o, H1_bg_o, fg_c, bg_c, {CX_c, 1'b1}, CY_c, op2ascii_1_l3, op2ascii_1_l4, op2ascii_1_l5, 7'b0100000, en, CX_o, CY_o, C_o, fg_o, bg_o, busy
endmodule
