// Digital circuit vga_sync.dig as structural Verilog
module vga_sync (
  input  clock,
  input  [11:0] res_H,
  input  [11:0] fp_H,
  input  [11:0] sync_H,
  input  [11:0] bp_H,
  input  neg_H,
  input  [11:0] res_V,
  input  [11:0] fp_V,
  input  [11:0] sync_V,
  input  [11:0] bp_V,
  input  neg_V,
  output H,
  output V,
  output pic,
  output [11:0] X,
  output [11:0] Y,
  output vblank,
  output hblank
);

  wire comparator_1_lt, comparator_2_lt, Horiz_next;

  vga_timing Horiz (
    .en(1'b1), .clock(clock), .res(res_H), .fp(bp_H), .sync(sync_H), .bp(fp_H), .neg(neg_H), .V(X),
    .pulse(H), .next(Horiz_next));
  vga_timing Vert (
    .en(Horiz_next), .clock(clock), .res(res_V), .fp(bp_V), .sync(sync_V), .bp(fp_V), .neg(neg_V), .V(Y),
    .pulse(V));  // open: next
  Comparator #(.Bits(12)) comparator_1 (.a(X), .b(res_H), .lt(comparator_1_lt));  // open: gt, eq
  Comparator #(.Bits(12)) comparator_2 (.a(Y), .b(res_V), .lt(comparator_2_lt));  // open: gt, eq
  not not_1 (hblank, comparator_1_lt);
  not not_2 (vblank, comparator_2_lt);
  and and_1 (pic, comparator_1_lt, comparator_2_lt);

  // Other names for the same wires on the sheet: C = clock

  // Notes on the sheet:
  //   clock: Hz: 50000
  //   res_H: default 640
  //   fp_H: default 16
  //   sync_H: default 96
  //   bp_H: default 48
  //   res_V: default 640
  //   fp_V: default 16
  //   sync_V: default 96
  //   bp_V: default 48
endmodule
