// Digital circuit vga_text.dig as structural Verilog
module vga_text (
  input  H_i,
  input  V_i,
  input  pic,
  input  [4:0] row,
  input  [3:0] col,
  input  [15:0] TD,
  input  [7:0] MD,
  input  clock,
  input  [6:0] char,
  input  [3:0] fg,
  input  [11:0] bg,
  output [3:0] R,
  output [3:0] G,
  output [3:0] B,
  output hs,
  output vs,
  output de,
  output [10:0] TA,
  output [9:0] MA
);

  wire d_ff_1_q, d_ff_2_q, d_ff_5_q, d_ff_6_q, d_ff_7_q, d_ff_11_q, d_ff_14_q, d_ff_15_q, d_ff_18_q,
       d_ff_21_q, d_ff_22_q, d_ff_24_q, transparent_eq;
  wire [1:0] multiplexer_1_out;
  wire [2:0] d_ff_8_q, d_ff_9_q, d_ff_16_q, d_ff_23_q;
  wire [3:0] d_ff_3_q, d_ff_12_q, d_ff_19_q, d_ff_25_q;
  wire [4:0] d_ff_4_q;
  wire [5:5] d_ff_10_q;
  wire [11:0] d_ff_13_q, d_ff_20_q, d_ff_26_q, multiplexer_2_out, multiplexer_3_out;
  wire [15:0] Pallet_ROM_d;

  D_FF d_ff_1 (.D(H_i), .C(clock), .Q(d_ff_1_q));  // open: nQ
  D_FF d_ff_2 (.D(V_i), .C(clock), .Q(d_ff_2_q));  // open: nQ
  D_FF #(.Bits(4)) d_ff_3 (.D(col), .C(clock), .Q(d_ff_3_q));  // open: nQ
  D_FF #(.Bits(5)) d_ff_4 (.D(row), .C(clock), .Q(d_ff_4_q));  // open: nQ
  D_FF d_ff_5 (.D(pic), .C(clock), .Q(d_ff_5_q));  // open: nQ
  D_FF d_ff_6 (.D(d_ff_1_q), .C(clock), .Q(d_ff_6_q));  // open: nQ
  D_FF d_ff_7 (.D(d_ff_2_q), .C(clock), .Q(d_ff_7_q));  // open: nQ
  D_FF #(.Bits(4)) d_ff_8 (.D(d_ff_3_q), .C(clock), .Q({MA[0], d_ff_8_q}));  // open: nQ
  D_FF #(.Bits(5)) d_ff_9 (.D(d_ff_4_q), .C(clock), .Q({MA[2:1], d_ff_9_q}));  // open: nQ
  D_FF #(.Bits(7)) d_ff_10 (.D(char), .C(clock), .Q({MA[8], d_ff_10_q[5], MA[7:3]}));  // open: nQ
  D_FF d_ff_11 (.D(d_ff_5_q), .C(clock), .Q(d_ff_11_q));  // open: nQ
  D_FF #(.Bits(4)) d_ff_12 (.D(fg), .C(clock), .Q(d_ff_12_q));  // open: nQ
  D_FF #(.Bits(12)) d_ff_13 (.D(bg), .C(clock), .Q(d_ff_13_q));  // open: nQ
  D_FF d_ff_14 (.D(d_ff_6_q), .C(clock), .Q(d_ff_14_q));  // open: nQ
  D_FF d_ff_15 (.D(d_ff_7_q), .C(clock), .Q(d_ff_15_q));  // open: nQ
  D_FF #(.Bits(3)) d_ff_16 (.D(d_ff_8_q), .C(clock), .Q(d_ff_16_q));  // open: nQ
  D_FF #(.Bits(3)) d_ff_17 (.D(d_ff_9_q), .C(clock), .Q(TA[2:0]));  // open: nQ
  D_FF d_ff_18 (.D(d_ff_11_q), .C(clock), .Q(d_ff_18_q));  // open: nQ
  D_FF #(.Bits(4)) d_ff_19 (.D(d_ff_12_q), .C(clock), .Q(d_ff_19_q));  // open: nQ
  D_FF #(.Bits(12)) d_ff_20 (.D(d_ff_13_q), .C(clock), .Q(d_ff_20_q));  // open: nQ
  D_FF d_ff_21 (.D(d_ff_14_q), .C(clock), .Q(d_ff_21_q));  // open: nQ
  D_FF d_ff_22 (.D(d_ff_15_q), .C(clock), .Q(d_ff_22_q));  // open: nQ
  D_FF #(.Bits(3)) d_ff_23 (.D(d_ff_16_q), .C(clock), .Q(d_ff_23_q));  // open: nQ
  D_FF d_ff_24 (.D(d_ff_18_q), .C(clock), .Q(d_ff_24_q));  // open: nQ
  D_FF #(.Bits(4)) d_ff_25 (.D(d_ff_19_q), .C(clock), .Q(d_ff_25_q));  // open: nQ
  D_FF #(.Bits(12)) d_ff_26 (.D(d_ff_20_q), .C(clock), .Q(d_ff_26_q));  // open: nQ
  Multiplexer #(.Selector_Bits(3), .Bits(2)) multiplexer_1 (
    .sel(d_ff_23_q), .in_0(TD[1:0]), .in_1(TD[3:2]), .in_2(TD[5:4]), .in_3(TD[7:6]), .in_4(TD[9:8]),
    .in_5(TD[11:10]), .in_6(TD[13:12]), .in_7(TD[15:14]), .out(multiplexer_1_out));
  ROM #(.AddrBits(6), .Bits(16)) Pallet_ROM (.A({d_ff_25_q, multiplexer_1_out}), .sel(1'b1), .D(Pallet_ROM_d));
  Comparator #(.Bits(4)) transparent (.a(Pallet_ROM_d[15:12]), .b(4'b0000), .eq(transparent_eq));  // open: gt, lt
  Multiplexer #(.Bits(12)) multiplexer_2 (
    .sel(transparent_eq), .in_0(Pallet_ROM_d[11:0]), .in_1(d_ff_26_q), .out(multiplexer_2_out));
  Multiplexer #(.Bits(12)) multiplexer_3 (
    .sel(d_ff_24_q), .in_0({12{1'b0}}), .in_1(multiplexer_2_out), .out(multiplexer_3_out));
  D_FF d_ff_27 (.D(d_ff_21_q), .C(clock), .Q(hs));  // open: nQ
  D_FF d_ff_28 (.D(d_ff_22_q), .C(clock), .Q(vs));  // open: nQ
  D_FF d_ff_29 (.D(d_ff_24_q), .C(clock), .Q(de));  // open: nQ
  D_FF #(.Bits(4)) d_ff_30 (.D(multiplexer_3_out[3:0]), .C(clock), .Q(B));  // open: nQ
  D_FF #(.Bits(4)) d_ff_31 (.D(multiplexer_3_out[7:4]), .C(clock), .Q(G));  // open: nQ
  D_FF #(.Bits(4)) d_ff_32 (.D(multiplexer_3_out[11:8]), .C(clock), .Q(R));  // open: nQ

  assign MA[9] = 1'b0;
  assign TA[10:3] = MD;

  // Other names for the same wires on the sheet: C = clock

  // Notes on the sheet:
  //   contents of Pallet_ROM (hex, n*v repeats v):
  //   0,0,0,0,0,f144,f1aa,f0ee,0,f124,f15a,f07e,0,f420,fa50,fe70,0,f412,fa15,fe07,0,f214,
  //   f51a,f70e,0,f241,f5a1,f7e0,0,f555,fbbb,ffff
endmodule
