// Digital circuit vgafp.dig as structural Verilog
module vgafp (
  input  clk
);

  wire vga_display_1_hs, vga_display_1_vs, vga_hex_1_busy;
  wire [3:0] vga_display_1_b, vga_display_1_g, vga_display_1_r;
  wire [6:0] vga_hex_1_c_o, vga_string_1_c_o, vga_string_2_c_o, vga_string_3_c_o;
  wire [7:0] vga_display_1_cx, vga_display_1_cy, vga_string_1_cx_o, vga_string_1_cy_o, vga_string_2_cx_o,
       vga_string_2_cy_o, vga_string_3_cx_o, vga_string_3_cy_o;
  wire [10:0] vga_display_1_ca;
  wire [11:0] vga_hex_1_bg_o, vga_hex_1_fg_o, vga_string_1_bg_o, vga_string_1_fg_o, vga_string_2_bg_o,
       vga_string_2_fg_o, vga_string_3_bg_o, vga_string_3_fg_o;
  wire [15:0] Char_ROM_d, d_ff_1_q, register_1_q;
  wire [31:0] counter_1_out;

  vga_display vga_display_1 (
    .clock(clk), .res_H(12'h280), .fp_H(12'h10), .sync_H(12'h60), .bp_H(12'h30), .neg_H(1'b1),
    .res_V(12'h1e0), .fp_V(12'hb), .sync_V(12'h2), .bp_V(12'h21), .neg_V(1'b1), .char(vga_hex_1_c_o),
    .fg(vga_hex_1_fg_o), .bg(vga_hex_1_bg_o), .CD(d_ff_1_q), .R(vga_display_1_r), .G(vga_display_1_g),
    .B(vga_display_1_b), .hs(vga_display_1_hs), .vs(vga_display_1_vs), .CX(vga_display_1_cx),
    .CY(vga_display_1_cy), .CA(vga_display_1_ca));  // open: de
  VGA vga_1 (
    .R(vga_display_1_r), .G(vga_display_1_g), .B(vga_display_1_b), .H(vga_display_1_hs),
    .V(vga_display_1_vs), .C(clk));
  ROM #(.AddrBits(11), .Bits(16)) Char_ROM (.A(vga_display_1_ca), .sel(1'b1), .D(Char_ROM_d));
  D_FF #(.Bits(16)) d_ff_1 (.D(Char_ROM_d), .C(clk), .Q(d_ff_1_q));  // open: nQ
  vga_string vga_string_1 (
    .CX_i(vga_display_1_cx), .CY_i(vga_display_1_cy), .C_i({7{1'b0}}), .fg_i({12{1'b0}}), .bg_i({12{1'b0}}),
    .fg_c(12'he07), .bg_c(12'h222), .CX_c(6'b000011), .CY_c(8'h7), .C_0(7'b1001000), .C_1(7'b1000101),
    .C_2(7'b1001100), .C_3(7'b1001100), .en(1'b1), .CX_o(vga_string_1_cx_o), .CY_o(vga_string_1_cy_o),
    .C_o(vga_string_1_c_o), .fg_o(vga_string_1_fg_o), .bg_o(vga_string_1_bg_o));
  vga_string vga_string_2 (
    .CX_i(vga_string_1_cx_o), .CY_i(vga_string_1_cy_o), .C_i(vga_string_1_c_o), .fg_i(vga_string_1_fg_o),
    .bg_i(vga_string_1_bg_o), .fg_c(12'he07), .bg_c(12'h222), .CX_c(6'b000100), .CY_c(8'h7),
    .C_0(7'b1001111), .C_1(7'b0100000), .C_2(7'b1010111), .C_3(7'b1001111), .en(1'b1),
    .CX_o(vga_string_2_cx_o), .CY_o(vga_string_2_cy_o), .C_o(vga_string_2_c_o), .fg_o(vga_string_2_fg_o),
    .bg_o(vga_string_2_bg_o));
  Counter #(.Bits(32)) counter_1 (.en(1'b1), .C(clk), .clr(1'b0), .out(counter_1_out));  // open: ovf
  Register #(.Bits(16)) register_1 (.D(counter_1_out[23:8]), .C(clk), .en(~vga_hex_1_busy), .Q(register_1_q));
  vga_string vga_string_3 (
    .CX_i(vga_string_2_cx_o), .CY_i(vga_string_2_cy_o), .C_i(vga_string_2_c_o), .fg_i(vga_string_2_fg_o),
    .bg_i(vga_string_2_bg_o), .fg_c(12'he07), .bg_c(12'h222), .CX_c(6'b000101), .CY_c(8'h7),
    .C_0(7'b1010010), .C_1(7'b1001100), .C_2(7'b1000100), .C_3(7'b0100001), .en(1'b1),
    .CX_o(vga_string_3_cx_o), .CY_o(vga_string_3_cy_o), .C_o(vga_string_3_c_o), .fg_o(vga_string_3_fg_o),
    .bg_o(vga_string_3_bg_o));
  vga_hex vga_hex_1 (
    .CX_i(vga_string_3_cx_o), .CY_i(vga_string_3_cy_o), .C_i(vga_string_3_c_o), .fg_i(vga_string_3_fg_o),
    .bg_i(vga_string_3_bg_o), .fg_c(12'h1be), .bg_c(12'h222), .CX_c(6'b000100), .CY_c(8'h8),
    .N(register_1_q), .en(1'b1), .C_o(vga_hex_1_c_o), .fg_o(vga_hex_1_fg_o), .bg_o(vga_hex_1_bg_o),
    .busy(vga_hex_1_busy));  // open: CX_o, CY_o

  // Other names for the same wires on the sheet: C = clk

  // Notes on the sheet:
  //   clk: Hz: 2147483647
  //   contents of Char_ROM (hex, n*v repeats v):
  //   0,0,0,0,0,0,0,0,0,0,0,0,0,0,0,0,0,0,0,0,0,0,0,0,0,0,0,0,0,0,0,0,0,0,0,180,180,180,
  //   180,180,180,180,180,0,0,180,180,180,180,180,180,180,180,0,0,0,0,0,0,0,0,0,0,0,0,3e7c,
  //   1e78,0,0,0,0,0,0,0,0,0,0,0,0,0,0,0,0,0,0,0,0,0,0,0,0,0,0,0,0,0,0,3e7c,3ffc,4182,6186,
  //   6186,6186,6186,6186,6186,4182,3e7c,3e7c,4182,6186,6186,6186,6186,6186,6186,4182,3ffc,
  //   3e7c,0,0,0,0,0,0,0,0,0,0,3e7c,3ff8,4180,6180,6180,6180,6180,6180,6180,4180,3e7c,3e7c,
  //   182,186,186,186,186,186,186,182,1ffc,3e7c,0,0,0,0,0,0,0,0,0,0,3e00,3f00,4188,6188,
  //   6198,61b0,61b0,61e0,61e0,4180,3e7c,3e7c,182,786,786,d86,d86,1986,1186,1182,fc,7c,
  //   0,0,0,0,0,0,0,0,0,0,3e00,3f00,4180,6180,6180,6180,6180,6180,6180,4180,3f00,3e00,4000,
  //   6060,6060,6030,6030,6018,6008,4000,3e78,3e7c,0,0,0,0,0,0,0,0,0,0,0,0,8,8,18,30,30,
  //   60,60,0,0,0,0,0,0,0,0,0,0,0,0,0,0,0,0,0,0,0,0,0,0,0,7c,78,200,600,600,c00,800,1800,
  //   1000,0,0,0,0,1000,1800,800,c00,600,600,200,78,7c,0,0,0,0,0,0,0,0,0,0,3e00,1e00,40,
  //   60,60,30,10,18,8,0,0,0,0,8,18,10,30,60,60,40,1e00,3e00,0,0,0,0,0,0,0,0,0,0,0,0,1188,
  //   1188,1998,db0,db0,7e0,7e0,180,3e7c,3e7c,180,7e0,7e0,db0,db0,1998,1188,1188,0,0,0,
  //   0,0,0,0,0,0,0,0,0,0,0,180,180,180,180,180,180,180,180,3e7c,3e7c,180,180,180,180,180,
  //   180,180,180,0,0,0,0,0,0,0,0,0,0,0,0,0,0,0,0,0,0,0,0,0,0,0,0,0,600,600,c00,c00,1800,
  //   1000,1000,0,0,0,0,0,0,0,0,0,0,0,0,0,0,0,0,0,0,0,0,0,0,3e7c,3e7c,0,0,0,0,0,0,0,0,0,
  //   0,0,0,0,0,0,0,0,0,0,0,0,0,0,0,0,0,0,0,0,0,0,0,0,0,0,0,0,0,0,0,180,180,0,0,0,0,0,0,
  //   0,0,0,0,0,0,8,8,18,30,30,60,60,0,0,0,0,600,600,c00,c00,1800,1000,1000,0,0,0,0,0,0,
  //   0,0,0,0,0,0,3e7c,3e7c,4006,600e,601a,6032,6036,6066,6066,6006,0,0,6006,6606,6606,
  //   6c06,4c06,5806,7006,6002,3e7c,3e7c,0,0,0,0,0,0,0,0,0,0,3e00,1f00,180,180,180,180,
  //   180,180,180,180,0,0,180,180,180,180,180,180,180,180,1ff8,3e7c,0,0,0,0,0,0,0,0,0,0,
  //   3e7c,1e7c,2,6,6,6,6,6,6,2,3e7c,3e7c,4000,6000,6000,6000,6000,6000,6000,4000,3e78,
  //   3e7c,0,0,0,0,0,0,0,0,0,0,3e7c,1e7c,2,6,6,6,6,6,6,2,3e7c,3e7c,2,6,6,6,6,6,6,2,1e7c,
  //   3e7c,0,0,0,0,0,0,0,0,0,0,0,4002,6006,6006,6006,6006,6006,6006,6006,4002,3e7c,3e7c,
  //   2,6,6,6,6,6,6,6,2,0,0,0,0,0,0,0,0,0,0,0,3e7c,3e78,4000,6000,6000,6000,6000,6000,6000,
  //   4000,3e7c,3e7c,2,6,6,6,6,6,6,2,1e7c,3e7c,0,0,0,0,0,0,0,0,0,0,3e7c,3e78,4000,6000,
  //   6000,6000,6000,6000,6000,4000,3e7c,3e7c,4002,6006,6006,6006,6006,6006,6006,4002,3e7c,
  //   3e7c,0,0,0,0,0,0,0,0,0,0,3e7c,1e7c,2,6,6,6,6,6,6,6,0,0,6,6,6,6,6,6,6,6,2,0,0,0,0,
  //   0,0,0,0,0,0,0,3e7c,3e7c,4002,6006,6006,6006,6006,6006,6006,4002,3e7c,3e7c,4002,6006,
  //   6006,6006,6006,6006,6006,4002,3e7c,3e7c,0,0,0,0,0,0,0,0,0,0,3e7c,3e7c,4002,6006,6006,
  //   6006,6006,6006,6006,4002,3e7c,3e7c,2,6,6,6,6,6,6,2,1e7c,3e7c,0,0,0,0,0,0,0,0,0,0,
  //   0,0,0,0,0,180,180,0,0,0,0,0,0,0,0,180,180,0,0,0,0,0,0,0,0,0,0,0,0,0,0,0,0,0,180,180,
  //   180,180,180,180,180,180,0,0,0,600,600,c00,c00,1800,1000,1000,0,0,0,0,0,0,0,0,0,0,
  //   0,0,0,0,40,c0,c0,180,180,300,300,0,0,0,0,300,300,180,180,c0,c0,40,0,0,0,0,0,0,0,0,
  //   0,0,0,0,0,0,0,0,0,3e7c,3e7c,0,0,0,0,0,0,0,0,1e78,3e7c,0,0,0,0,0,0,0,0,0,0,0,0,0,0,
  //   0,0,0,200,300,300,180,180,c0,c0,0,0,0,0,c0,c0,180,180,300,300,200,0,0,0,0,0,0,0,0,
  //   0,0,0,0,3e7c,1e7c,2,6,6,6,6,6,6,2,7c,fc,180,180,180,180,180,180,180,180,0,0,0,0,0,
  //   0,0,0,0,0,0,0,3e7c,3ffc,4182,6186,6186,6186,6186,6186,6186,6182,fc,7c,6000,6000,6000,
  //   6000,6000,6000,6000,4000,3e78,3e7c,0,0,0,0,0,0,0,0,0,0,3e7c,3e7c,4002,6006,6006,6006,
  //   6006,6006,6006,4002,3e7c,3e7c,4002,6006,6006,6006,6006,6006,6006,6006,4002,0,0,0,
  //   0,0,0,0,0,0,0,0,3e7c,1ffc,182,186,186,186,186,186,186,182,3e7c,3e7c,182,186,186,186,
  //   186,186,186,182,1ffc,3e7c,0,0,0,0,0,0,0,0,0,0,3e7c,3e78,4000,6000,6000,6000,6000,
  //   6000,6000,6000,0,0,6000,6000,6000,6000,6000,6000,6000,4000,3e78,3e7c,0,0,0,0,0,0,
  //   0,0,0,0,3e7c,1ffc,182,186,186,186,186,186,186,186,0,0,186,186,186,186,186,186,186,
  //   182,1ffc,3e7c,0,0,0,0,0,0,0,0,0,0,3e7c,3e78,4000,6000,6000,6000,6000,6000,6000,4000,
  //   3e7c,3e7c,4000,6000,6000,6000,6000,6000,6000,4000,3e78,3e7c,0,0,0,0,0,0,0,0,0,0,3e7c,
  //   3e78,4000,6000,6000,6000,6000,6000,6000,4000,3e7c,3e7c,4000,6000,6000,6000,6000,6000,
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endmodule
