// Digital circuit vgatest.dig as structural Verilog
module vgatest (
  input  [15:0] H_res,
  input  [15:0] H_fp,
  input  [15:0] H_sync,
  input  [15:0] H_bp,
  input  [15:0] V_res,
  input  [15:0] V_fp,
  input  [15:0] V_sync,
  input  [15:0] V_bp,
  input  H_neg,
  input  V_neg,
  input  clk
);

  wire pixgen_1_h_o, pixgen_1_v_o, posgen_1_h_o, posgen_1_v_o, posgen_1_valid, vga_1_h, vga_1_v;
  wire [3:0] posgen_1_col, vga_1_b, vga_1_g, vga_1_r;
  wire [4:0] posgen_1_row;
  wire [8:0] posgen_1_a, strgen_1_a_o;
  wire [10:0] pixgen_1_a;
  wire [15:0] Char_q, Char_ROM_d, Pixels_q, pixgen_1_colour, strgen_1_d_o, strgen_2_d_o, vga_1_x, vga_1_y;

  vga vga_1 (
    .clk(clk), .H_res(H_res), .H_fp(H_fp), .H_sync(H_sync), .H_bp(H_bp), .H_neg(H_neg), .V_res(V_res),
    .V_fp(V_fp), .V_sync(V_sync), .V_bp(V_bp), .V_neg(V_neg), .colour(pixgen_1_colour), .R(vga_1_r),
    .G(vga_1_g), .B(vga_1_b), .H(vga_1_h), .V(vga_1_v), .X(vga_1_x), .Y(vga_1_y));
  posgen posgen_1 (
    .H_i(vga_1_h), .V_i(vga_1_v), .X(vga_1_x), .Y(vga_1_y), .clk(clk), .H_o(posgen_1_h_o),
    .V_o(posgen_1_v_o), .col(posgen_1_col), .row(posgen_1_row), .valid(posgen_1_valid), .A(posgen_1_a));
  strgen strgen_1 (
    .A_i(posgen_1_a), .D_i({16{1'b0}}), .X(2'b01), .Y(4'b0101), .C(9'h7), .L0(7'b0100000), .L1(7'b0100000),
    .L2(7'b1001000), .L3(7'b1000101), .L4(7'b1001100), .L5(7'b1001100), .L6(7'b1001111), .L7(7'b0100000),
    .en(1'b1), .A_o(strgen_1_a_o), .D_o(strgen_1_d_o));
  strgen strgen_2 (
    .A_i(strgen_1_a_o), .D_i(strgen_1_d_o), .X(2'b10), .Y(4'b0101), .C(9'h87), .L0(7'b1010111),
    .L1(7'b1001111), .L2(7'b1010010), .L3(7'b1001100), .L4(7'b1000100), .L5(7'b0100000), .L6(7'b0100000),
    .L7(7'b0100000), .en(1'b1), .D_o(strgen_2_d_o));  // open: A_o
  pixgen pixgen_1 (
    .H_i(posgen_1_h_o), .V_i(posgen_1_v_o), .col(posgen_1_col), .row(posgen_1_row), .valid(posgen_1_valid),
    .char(Char_q), .bg(16'h222), .clk(clk), .pix(Pixels_q), .H_o(pixgen_1_h_o), .V_o(pixgen_1_v_o),
    .A(pixgen_1_a), .colour(pixgen_1_colour));
  Register #(.Bits(16)) Char (.D(strgen_2_d_o), .C(clk), .en(1'b1), .Q(Char_q));
  ROM #(.AddrBits(11), .Bits(16)) Char_ROM (.A(pixgen_1_a), .sel(1'b1), .D(Char_ROM_d));
  VGA vga_2 (.R(vga_1_r), .G(vga_1_g), .B(vga_1_b), .H(pixgen_1_h_o), .V(pixgen_1_v_o), .C(clk));
  Register #(.Bits(16)) Pixels (.D(Char_ROM_d), .C(clk), .en(1'b1), .Q(Pixels_q));

  // Other names for the same wires on the sheet: C = clk

  // Notes on the sheet:
  //   H_res: default 639
  //   H_fp: default 16
  //   H_sync: default 96
  //   H_bp: default 48
  //   V_res: default 480
  //   V_fp: default 10
  //   V_sync: default 2
  //   V_bp: default 33
  //   H_neg: default 1
  //   V_neg: default 1
  //   clk: Hz: 2147483647
  //   contents of Char_ROM (hex, n*v repeats v):
  //   0,0,0,0,0,0,0,0,0,0,0,0,0,0,0,0,0,0,0,0,0,0,0,0,0,0,0,0,0,0,0,0,300,300,300,300,300,
  //   300,300,300,300,300,300,300,300,300,300,300,300,300,300,300,0,0,0,0,300,300,300,300,
  //   0,0,0,0,c30,c30,c30,c30,c30,c30,c30,c30,c30,c30,c30,c30,0,0,0,0,0,0,0,0,0,0,0,0,0,
  //   0,0,0,0,0,0,0,c30,c30,c30,c30,c30,c30,c30,c30,3ffc,3ffc,3ffc,3ffc,c30,c30,c30,c30,
  //   3ffc,3ffc,3ffc,3ffc,c30,c30,c30,c30,c30,c30,c30,c30,0,0,0,0,300,300,300,300,ff0,ff0,
  //   ff0,ff0,3300,3300,3300,3300,fc0,fc0,fc0,fc0,330,330,330,330,3fc0,3fc0,3fc0,3fc0,300,
  //   300,300,300,0,0,0,0,0,0,0,0,3c0c,3c0c,3c0c,3c0c,3c30,3c30,3c30,3c30,c0,c0,c0,c0,300,
  //   300,300,300,c3c,c3c,c3c,c3c,303c,303c,303c,303c,0,0,0,0,f00,f00,f00,f00,30c0,30c0,
  //   30c0,30c0,30c0,30c0,30c0,30c0,f00,f00,f00,f00,30cc,30cc,30cc,30cc,3030,3030,3030,
  //   3030,fcc,fcc,fcc,fcc,0,0,0,0,300,300,300,300,300,300,300,300,300,300,300,300,0,0,
  //   0,0,0,0,0,0,0,0,0,0,0,0,0,0,0,0,0,0,300,300,300,300,c00,c00,c00,c00,3000,3000,3000,
  //   3000,3000,3000,3000,3000,3000,3000,3000,3000,c00,c00,c00,c00,300,300,300,300,0,0,
  //   0,0,300,300,300,300,c0,c0,c0,c0,30,30,30,30,30,30,30,30,30,30,30,30,c0,c0,c0,c0,300,
  //   300,300,300,0,0,0,0,300,300,300,300,3330,3330,3330,3330,fc0,fc0,fc0,fc0,300,300,300,
  //   300,fc0,fc0,fc0,fc0,3330,3330,3330,3330,300,300,300,300,0,0,0,0,0,0,0,0,300,300,300,
  //   300,300,300,300,300,3ff0,3ff0,3ff0,3ff0,300,300,300,300,300,300,300,300,0,0,0,0,0,
  //   0,0,0,0,0,0,0,0,0,0,0,0,0,0,0,0,0,0,0,c0,c0,c0,c0,c0,c0,c0,c0,300,300,300,300,0,0,
  //   0,0,0,0,0,0,0,0,0,0,0,0,0,0,3ffc,3ffc,3ffc,3ffc,0,0,0,0,0,0,0,0,0,0,0,0,0,0,0,0,0,
  //   0,0,0,0,0,0,0,0,0,0,0,0,0,0,0,0,0,0,0,0,0,0,0,300,300,300,300,0,0,0,0,0,0,0,0,c,c,
  //   c,c,30,30,30,30,c0,c0,c0,c0,300,300,300,300,c00,c00,c00,c00,3000,3000,3000,3000,0,
  //   0,0,0,ff0,ff0,ff0,ff0,300c,300c,300c,300c,303c,303c,303c,303c,33cc,33cc,33cc,33cc,
  //   3c0c,3c0c,3c0c,3c0c,300c,300c,300c,300c,ff0,ff0,ff0,ff0,0,0,0,0,c0,c0,c0,c0,3c0,3c0,
  //   3c0,3c0,c0,c0,c0,c0,c0,c0,c0,c0,c0,c0,c0,c0,c0,c0,c0,c0,3f0,3f0,3f0,3f0,0,0,0,0,ff0,
  //   ff0,ff0,ff0,300c,300c,300c,300c,c,c,c,c,3f0,3f0,3f0,3f0,c00,c00,c00,c00,3000,3000,
  //   3000,3000,3ffc,3ffc,3ffc,3ffc,0,0,0,0,3ffc,3ffc,3ffc,3ffc,c,c,c,c,30,30,30,30,3f0,
  //   3f0,3f0,3f0,c,c,c,c,300c,300c,300c,300c,ff0,ff0,ff0,ff0,0,0,0,0,30,30,30,30,f0,f0,
  //   f0,f0,330,330,330,330,c30,c30,c30,c30,3ffc,3ffc,3ffc,3ffc,30,30,30,30,30,30,30,30,
  //   0,0,0,0,3ffc,3ffc,3ffc,3ffc,3000,3000,3000,3000,3ff0,3ff0,3ff0,3ff0,c,c,c,c,c,c,c,
  //   c,300c,300c,300c,300c,ff0,ff0,ff0,ff0,0,0,0,0,3fc,3fc,3fc,3fc,c00,c00,c00,c00,3000,
  //   3000,3000,3000,3ff0,3ff0,3ff0,3ff0,300c,300c,300c,300c,300c,300c,300c,300c,ff0,ff0,
  //   ff0,ff0,0,0,0,0,3ffc,3ffc,3ffc,3ffc,c,c,c,c,30,30,30,30,c0,c0,c0,c0,300,300,300,300,
  //   300,300,300,300,300,300,300,300,0,0,0,0,ff0,ff0,ff0,ff0,300c,300c,300c,300c,300c,
  //   300c,300c,300c,ff0,ff0,ff0,ff0,300c,300c,300c,300c,300c,300c,300c,300c,ff0,ff0,ff0,
  //   ff0,0,0,0,0,ff0,ff0,ff0,ff0,300c,300c,300c,300c,300c,300c,300c,300c,ffc,ffc,ffc,ffc,
  //   c,c,c,c,30,30,30,30,3fc0,3fc0,3fc0,3fc0,0,0,0,0,0,0,0,0,0,0,0,0,300,300,300,300,0,
  //   0,0,0,300,300,300,300,0,0,0,0,0,0,0,0,0,0,0,0,0,0,0,0,0,0,0,0,c0,c0,c0,c0,0,0,0,0,
  //   c0,c0,c0,c0,c0,c0,c0,c0,300,300,0,0,0,0,0,0,30,30,30,30,c0,c0,c0,c0,300,300,300,300,
  //   c00,c00,c00,c00,300,300,300,300,c0,c0,c0,c0,30,30,30,30,0,0,0,0,0,0,0,0,0,0,0,0,3ffc,
  //   3ffc,3ffc,3ffc,0,0,0,0,3ffc,3ffc,3ffc,3ffc,0,0,0,0,0,0,0,0,0,0,0,0,c00,c00,c00,c00,
  //   300,300,300,300,c0,c0,c0,c0,30,30,30,30,c0,c0,c0,c0,300,300,300,300,c00,c00,c00,c00,
  //   0,0,0,0,c00,c00,c00,c00,3000,3000,3000,3000,0,0,0,0,0,0,0,0,0,0,0,0,0,0,0,0,0,0,0,
  //   0,0,0,0,0,ff0,ff0,ff0,ff0,300c,300c,300c,300c,30cc,30cc,30cc,30cc,333c,333c,333c,
  //   333c,30f0,30f0,30f0,30f0,3000,3000,3000,3000,ffc,ffc,ffc,ffc,0,0,0,0,3c0,3c0,3c0,
  //   3c0,c30,c30,c30,c30,300c,300c,300c,300c,300c,300c,300c,300c,3ffc,3ffc,3ffc,3ffc,300c,
  //   300c,300c,300c,300c,300c,300c,300c,0,0,0,0,3ff0,3ff0,3ff0,3ff0,300c,300c,300c,300c,
  //   300c,300c,300c,300c,3ff0,3ff0,3ff0,3ff0,300c,300c,300c,300c,300c,300c,300c,300c,3ff0,
  //   3ff0,3ff0,3ff0,0,0,0,0,ff0,ff0,ff0,ff0,300c,300c,300c,300c,3000,3000,3000,3000,3000,
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endmodule
