// Digital circuit wishbone_fsm.dig as structural Verilog
module wishbone_fsm (
  input  ack,
  input  hold,
  input  mem,
  input  stall,
  input  C,
  output done,
  output req
);

  wire and_1_out, and_2_out, and_3_out, and_4_out, and_5_out, and_6_out, and_7_out, and_8_out, and_9_out,
       and_10_out, and_11_out, and_12_out, and_13_out, and_14_out, and_15_out, and_16_out, and_17_out,
       and_18_out, and_19_out, and_20_out, and_21_out, and_22_out, not_1_out, not_2_out, not_3_out,
       not_4_out, not_5_out, or_1_out, or_2_out, Z_0_n, Z_1_n;

  not not_1 (not_1_out, ack);
  not not_2 (not_2_out, hold);
  not not_3 (not_3_out, stall);
  not not_4 (not_4_out, Z_1_n);
  not not_5 (not_5_out, Z_0_n);
  and and_1 (and_1_out, Z_0_n, not_4_out, not_2_out);
  and and_2 (and_2_out, Z_0_n, not_4_out, ack);
  and and_3 (and_3_out, not_5_out, Z_1_n);
  and and_4 (and_4_out, Z_1_n, stall);
  and and_5 (and_5_out, ack, mem, not_3_out);
  and and_6 (and_6_out, not_2_out, mem, not_3_out);
  and and_7 (and_7_out, Z_0_n, Z_1_n, stall);
  and and_8 (and_8_out, Z_0_n, hold, mem);
  and and_9 (and_9_out, Z_0_n, not_4_out, hold);
  and and_10 (and_10_out, Z_0_n, not_4_out, ack);
  and and_11 (and_11_out, not_5_out, Z_1_n, ack);
  and and_12 (and_12_out, not_4_out, hold, mem, not_3_out);
  and and_13 (and_13_out, ack, mem, not_3_out);
  and and_14 (and_14_out, not_5_out, ack, mem, not_3_out);
  and and_15 (and_15_out, Z_0_n, Z_1_n, stall);
  and and_16 (and_16_out, Z_0_n, not_4_out, ack);
  and and_17 (and_17_out, not_5_out, Z_1_n, ack);
  and and_18 (and_18_out, ack, not_2_out, mem, not_3_out);
  and and_19 (and_19_out, Z_0_n, not_1_out, hold, mem, not_3_out);
  and and_20 (and_20_out, Z_0_n, Z_1_n, not_2_out, mem, not_3_out);
  and and_21 (and_21_out, not_5_out, not_4_out, mem, not_3_out);
  and and_22 (and_22_out, Z_0_n, not_4_out, not_1_out, hold);
  or or_1 (or_1_out, and_1_out, and_2_out, and_3_out, and_4_out, and_5_out, and_6_out);
  or or_2 (or_2_out, and_7_out, and_8_out, and_9_out, and_10_out, and_11_out, and_12_out, and_13_out);
  or or_3 (done, and_14_out, and_15_out, and_16_out, and_17_out, and_18_out);
  or or_4 (req, and_19_out, and_20_out, and_21_out, and_22_out);
  D_FF u_Z_1_n (.D(or_1_out), .C(C), .Q(Z_1_n));  // open: nQ
  D_FF u_Z_0_n (.D(or_2_out), .C(C), .Q(Z_0_n));  // open: nQ
  // Probe wishbone.fsm on {Z_1_n, Z_0_n}

  // Notes on the sheet:
  //   C: Hz: 2
endmodule
