// Digital circuit wishbone_fsm_test.dig as structural Verilog
module wishbone_fsm_test (
  input  clk,
  input  ack,
  input  hold,
  input  mem,
  input  stall,
  output done,
  output req
);

  wishbone_fsm wishbone_fsm_1 (.ack(ack), .hold(hold), .mem(mem), .stall(stall), .C(clk), .done(done), .req(req));
endmodule

/* Test case:
clk stall mem hold ack    req done


# same cycle ack

# no hold - no stall

# req
# clk stall mem hold ack    req done
0     0     1   0    1      1   1
1     0     0   0    1      0   0

0     0     0   0    0      0   0
1     0     0   0    0      0   0

# req req
0     0     1   0    1      1   1
1     0     1   0    1      1   1
0     0     1   0    1      1   1
1     0     0   0    1      0   0

0     0     0   0    0      0   0
1     0     0   0    0      0   0

# hold - no stall
# req
# clk stall mem hold ack    req done
0     0     1   1    0      1   0
1     0     1   1    0      1   0
0     0     1   1    0      1   0
1     0     1   1    0      1   0
0     0     0   0    1      0   1
1     0     0   0    1      0   0

0     0     0   0    0      0   0
1     0     0   0    0      0   0

# req req
0     0     1   1    0      1   0
1     0     1   1    0      1   0
0     0     1   1    0      1   0
1     0     1   1    0      1   0
0     0     1   0    1      1   1
1     0     1   0    1      1   1
0     0     0   0    1      0   1
1     0     0   0    1      0   0

0     0     0   0    0      0   0
1     0     0   0    0      0   0
*/
