// Digital circuit writeback.dig as structural Verilog
module writeback (
  input  [15:0] L,
  input  [15:0] R,
  input  [15:0] result,
  input  [15:0] rdval,
  input  [15:0] D,
  input  [1:0] wrmux,
  output [15:0] wrval,
  output [15:0] result_out,
  output [15:0] rdval_out
);

  Multiplexer #(.Selector_Bits(2), .Bits(16)) multiplexer_1 (
    .sel(wrmux), .in_0(result), .in_1(L), .in_2(D), .in_3(R), .out(wrval));

  assign rdval_out = rdval;
  assign result_out = result;
endmodule
