// Digital circuit 74185.dig as structural Verilog
module _74185 (
  input  A,
  input  B,
  input  C,
  input  D,
  input  E,
  input  NA,
  output Y3,
  output Y4,
  output Y5,
  output Y6,
  output Y2,
  output Y1
);

  ROM #(.AddrBits(5), .Bits(6)) _74185 (.A({E, D, C, B, A}), .sel(1'b1), .D({Y6, Y5, Y4, Y3, Y2, Y1}));
endmodule
