// Digital circuit bin2bcd.dig as structural Verilog
module bin2bcd (
  input  [31:0] in_1,
  input  clock_b2b
);

  wire and_1_out, button_1_out, counterpreset_1_ovf, d_ff_as_1_nq, or_1_out;
  wire [0:0] gt4add3_2_o_2;
  wire [3:0] d_ff_as_2_q, d_ff_as_2_q_2, d_ff_as_2_q_3, d_ff_as_2_q_4, d_ff_as_2_q_5, d_ff_as_2_q_6,
       d_ff_as_2_q_7, d_ff_as_2_q_8, d_ff_as_2_q_9, d_ff_as_2_q_10, gt4add3_1_o;
  wire [4:0] counterpreset_1_out;
  wire [35:0] gt4add3_2_o;

  Button button_1 (.out(button_1_out));
  D_FF_AS d_ff_as_1 (
    .Set(1'b0), .D(counterpreset_1_ovf), .C(and_1_out), .Clr(button_1_out), .nQ(d_ff_as_1_nq));  // open: Q
  and and_1 (and_1_out, d_ff_as_1_nq, clock_b2b, ~counterpreset_1_ovf);  // And
  or or_1 (or_1_out, button_1_out, and_1_out);
  BitSelector #(.Selector_Bits(5)) bitselector_1 (.in(in_1), .sel(counterpreset_1_out), .out(gt4add3_2_o[0]));
  CounterPreset #(.Bits(5)) counterpreset_1 (
    .en(1'b1), .C(or_1_out), .dir(1'b1), .in({5{1'b1}}), .ld(button_1_out), .clr(1'b0),
    .out(counterpreset_1_out), .ovf(counterpreset_1_ovf));
  LED led_1 (.in(gt4add3_2_o[0]));
  Seven_Seg_Hex seven_seg_hex_1 (.d({gt4add3_1_o[2:0], gt4add3_2_o_2[0]}), .dp(1'b0));
  gt4add3 gt4add3_1 (.I(d_ff_as_2_q_10), .O(gt4add3_1_o));
  D_FF_AS #(.Bits(40)) d_ff_as_2 (
    .Set(1'b0), .D({gt4add3_1_o[2:0], gt4add3_2_o_2[0], gt4add3_2_o}), .C(and_1_out), .Clr(button_1_out),
    .Q({d_ff_as_2_q_10, d_ff_as_2_q_9, d_ff_as_2_q_8, d_ff_as_2_q_7, d_ff_as_2_q_6, d_ff_as_2_q_5, d_ff_as_2_q_4, d_ff_as_2_q_3, d_ff_as_2_q_2, d_ff_as_2_q}));  // open: nQ
  Seven_Seg_Hex seven_seg_hex_2 (.d(gt4add3_2_o[35:32]), .dp(1'b0));
  gt4add3 gt4add3_2 (.I(d_ff_as_2_q_9), .O({gt4add3_2_o_2[0], gt4add3_2_o[35:33]}));
  Seven_Seg_Hex seven_seg_hex_3 (.d(gt4add3_2_o[31:28]), .dp(1'b0));
  gt4add3 gt4add3_3 (.I(d_ff_as_2_q_8), .O(gt4add3_2_o[32:29]));
  Seven_Seg_Hex seven_seg_hex_4 (.d(gt4add3_2_o[27:24]), .dp(1'b0));
  gt4add3 gt4add3_4 (.I(d_ff_as_2_q_7), .O(gt4add3_2_o[28:25]));
  Seven_Seg_Hex seven_seg_hex_5 (.d(gt4add3_2_o[23:20]), .dp(1'b0));
  gt4add3 gt4add3_5 (.I(d_ff_as_2_q_6), .O(gt4add3_2_o[24:21]));
  Seven_Seg_Hex seven_seg_hex_6 (.d(gt4add3_2_o[19:16]), .dp(1'b0));
  gt4add3 gt4add3_6 (.I(d_ff_as_2_q_5), .O(gt4add3_2_o[20:17]));
  Seven_Seg_Hex seven_seg_hex_7 (.d(gt4add3_2_o[15:12]), .dp(1'b0));
  gt4add3 gt4add3_7 (.I(d_ff_as_2_q_4), .O(gt4add3_2_o[16:13]));
  Seven_Seg_Hex seven_seg_hex_8 (.d(gt4add3_2_o[11:8]), .dp(1'b0));
  gt4add3 gt4add3_8 (.I(d_ff_as_2_q_3), .O(gt4add3_2_o[12:9]));
  Seven_Seg_Hex seven_seg_hex_9 (.d(gt4add3_2_o[7:4]), .dp(1'b0));
  gt4add3 gt4add3_9 (.I(d_ff_as_2_q_2), .O(gt4add3_2_o[8:5]));
  Seven_Seg_Hex seven_seg_hex_10 (.d(gt4add3_2_o[3:0]), .dp(1'b0));
  gt4add3 gt4add3_10 (.I(d_ff_as_2_q), .O(gt4add3_2_o[4:1]));

  // Notes on the sheet:
  //   in_1: default 412597816
  //   clock_b2b: Hz: 5
endmodule
