// Digital circuit bram_diagram.dig as structural Verilog
module bram_diagram (
);

  wire read_clock, read_data, read_enable, write_clock, write_enable;
  wire [7:0] read_address, write_address;
  wire [15:0] write_data, write_mask;

  bram_io _256_x_16_bits (
    .wdata(write_data), .mask(write_mask), .waddr(write_address), .store(write_enable), .wclk(write_clock),
    .rdata(read_data), .raddr(read_address), .load(read_enable), .rclk(read_clock));

  // Notes on the sheet:
  //   Block RAM
endmodule
