// Digital circuit dpram_pipeline.dig as structural Verilog
module dpram_pipeline (
  input  [1:0] S_addr,
  input  clock,
  input  S_rdy,
  input  D_vld,
  input  [1:0] D_addr,
  input  [15:0] D_data,
  output [15:0] S_data,
  output S_vld,
  output D_rdy
);

  Register register_1 (.D(S_rdy), .C(clock), .en(1'b1), .Q(S_vld));
  RAMDualAccess #(.Bits(16)) ramdualaccess_1 (
    .str(D_vld), .C(clock), .ld(1'b0), .A1(D_addr), .Din1(D_data), .A2(S_addr), .D2(S_data));  // open: D1

  assign D_rdy = 1'b1;
endmodule
