// Digital circuit fifo-cdc.dig as structural Verilog
module fifo_cdc (
  input  wclk,
  input  wput,
  input  [15:0] D_in,
  input  rclk,
  input  rget,
  output wrdy,
  output [15:0] D_out,
  output rrdy
);

  wire and_1_out, and_2_out, d_ff_1_q, d_ff_2_q, d_ff_3_q, d_ff_4_q, d_ff_5_q, d_ff_6_q, xor_1_out, xor_3_out;

  and and_1 (and_1_out, wput, wrdy);
  xor xor_1 (xor_1_out, d_ff_1_q, and_1_out);
  xnor xnor_1 (wrdy, d_ff_2_q, d_ff_1_q);
  D_FF d_ff_1 (.D(xor_1_out), .C(wclk), .Q(d_ff_1_q));  // open: nQ
  D_FF d_ff_2 (.D(d_ff_5_q), .C(wclk), .Q(d_ff_2_q));  // open: nQ
  D_FF d_ff_3 (.D(d_ff_1_q), .C(rclk), .Q(d_ff_3_q));  // open: nQ
  RAMDualAccess #(.AddrBits(1), .Bits(16)) ramdualaccess_1 (
    .str(and_1_out), .C(wclk), .ld(1'b0), .A1(d_ff_1_q), .Din1(D_in), .A2(d_ff_6_q), .D2(D_out));  // open: D1
  D_FF d_ff_4 (.D(d_ff_3_q), .C(rclk), .Q(d_ff_4_q));  // open: nQ
  D_FF d_ff_5 (.D(d_ff_6_q), .C(wclk), .Q(d_ff_5_q));  // open: nQ
  xor xor_2 (rrdy, d_ff_6_q, d_ff_4_q);
  D_FF d_ff_6 (.D(xor_3_out), .C(rclk), .Q(d_ff_6_q));  // open: nQ
  xor xor_3 (xor_3_out, and_2_out, d_ff_6_q);
  and and_2 (and_2_out, rrdy, rget);

  // Other names for the same wires on the sheet: RC = rclk; WC = wclk

  // Notes on the sheet:
  //   http://www.sunburst-design.com/papers/CummingsSNUG2008Boston_CDC.pdf
  //   fifo from 5.8.2
endmodule
