// Digital circuit fifo.dig as structural Verilog
module fifo (
  input  clk,
  input  [15:0] D,
  input  rd,
  input  wr,
  input  clr,
  output [15:0] Q,
  output full,
  output empty
);

  wire and_1_out, and_2_out;
  wire [2:0] Read_out, sub_1_s, Write_out;

  and and_1 (and_1_out, ~empty, rd);  // And
  and and_2 (and_2_out, wr, ~full);  // And
  Counter #(.Bits(3)) Read (.en(and_1_out), .C(clk), .clr(clr), .out(Read_out));  // open: ovf
  Counter #(.Bits(3)) Write (.en(and_2_out), .C(clk), .clr(clr), .out(Write_out));  // open: ovf
  Sub #(.Bits(3)) sub_1 (.a(Write_out), .b(Read_out), .c_i(1'b0), .s(sub_1_s));  // open: c_o
  RAMDualAccess #(.Bits(16)) ramdualaccess_1 (
    .str(and_2_out), .C(clk), .ld(1'b1), .A1(Write_out[1:0]), .Din1(D), .A2(Read_out[1:0]), .D2(Q));  // open: D1
  Comparator #(.Bits(3)) comparator_1 (.a(sub_1_s), .b(3'b000), .eq(empty));  // open: gt, lt
  Comparator #(.Bits(3)) comparator_2 (.a(sub_1_s), .b(3'b100), .eq(full));  // open: gt, lt

  // Other names for the same wires on the sheet: C = clk; rst = clr
endmodule

/* Test case:
clk rd wr clr D    full empty Q

C    0  0   0 42      0     1 0
C    0  0   0 42      0     1 0

C    0  1   0 42      0     0 42
C    0  1   0 25      0     0 42
C    0  1   0 19      0     0 42
C    0  1   0 36      1     0 42
C    0  1   0 45      1     0 42

C    1  0   0 11      0     0 25
C    1  0   0 22      0     0 19
C    1  0   0 33      0     0 36
C    1  0   0 44      0     1 42
C    1  0   0 55      0     1 42
*/
