// Digital circuit glossary.dig as structural Verilog
module glossary (
  input  \input ,
  input  clk,
  input  rst,
  output \output 
);

  wire and_1_out, data_in_1, data_out, data_out_1, data_out_2, enable, enable_output, input_1, input_2, load,
       or_1_out, overflow, reset, selector, set, store, undriven, undriven_2, undriven_3, undriven_4;
  wire [1:0] address, address_1, address_2;
  wire [23:0] input_t, not_output, output_t;

  and and_1 (and_1_out, undriven, undriven_2);
  or or_1 (or_1_out, undriven_3, undriven_4);
  Counter #(.Bits(10)) Counter (.en(enable), .C(clk), .clr(rst), .out(output_t[9:0]), .ovf(overflow));
  Multiplexer multiplexer_1 (.sel(selector), .in_0(input_1), .in_1(input_2), .out(output_t[0]));
  D_FF #(.Bits(24)) Register (.D(input_t), .C(clk), .Q(output_t), .nQ(not_output));
  RS_FF RS_Flip_Flop (.S(set), .C(clk), .R(reset));  // open: Q, nQ
  ROM Read_Only_Memory (.A(address), .sel(enable_output), .D(data_out));
  RAMDualAccess Dual_Port_Block_RAM (
    .str(store), .C(clk), .ld(load), .A1(address_1), .Din1(data_in_1), .A2(address_2), .D1(data_out_1),
    .D2(data_out_2));
  // Pins of 1 and 10 and 24 bits meet at output_t

  assign \output  = \input ;

  // Other names for the same wires on the sheet: C = clk; R = rst

  // Notes on the sheet:
  //   Clock
  //   Reset
  //   Splitter
  //   Merger
  //   And
  //   Or
  //   Multiplexer
endmodule
