// Digital circuit gt4add3.dig as structural Verilog
module gt4add3 (
  input  [3:0] I,
  output [3:0] O
);

  wire comparator_1_gt;
  wire [3:0] multiplexer_1_out;

  Comparator #(.Bits(4)) comparator_1 (.a(I), .b(4'b0100), .gt(comparator_1_gt));  // open: eq, lt
  Multiplexer #(.Bits(4)) multiplexer_1 (
    .sel(comparator_1_gt), .in_0(4'b0000), .in_1(4'b0011), .out(multiplexer_1_out));
  Add #(.Bits(4)) add_1 (.a(I), .b(multiplexer_1_out), .c_i(1'b0), .s(O));  // open: c_o
endmodule
