// Digital circuit mc_seq_idea.dig as structural Verilog
module mc_seq_idea (
  input  clock,
  input  flag_1,
  input  flag_2,
  input  flag_3,
  input  flag_4,
  input  [6:0] opcode,
  output control_1,
  output control_2,
  output control_3,
  output control_4,
  output control_5,
  output control_6,
  output control_7,
  output control_8
);

  wire [6:0] multiplexer_1_out, Step_q;
  wire [7:0] NextStep_d;
  wire [7:7] Step_q_2;

  Multiplexer #(.Bits(7)) multiplexer_1 (.sel(Step_q_2[7]), .in_0(Step_q), .in_1(opcode), .out(multiplexer_1_out));
  ROM #(.AddrBits(11), .Bits(8)) NextStep (
    .A({multiplexer_1_out, flag_4, flag_3, flag_2, flag_1}), .sel(1'b1), .D(NextStep_d));
  Register #(.Bits(8)) Step (.D(NextStep_d), .C(clock), .en(1'b1), .Q({Step_q_2[7], Step_q}));
  ROM #(.AddrBits(7), .Bits(4)) Microcode (.A(Step_q), .sel(1'b1), .D({control_4, control_3, control_2, control_1}));
  ROM #(.AddrBits(7), .Bits(4)) Microcode_2 (.A(Step_q), .sel(1'b1), .D({control_8, control_7, control_6, control_5}));

  // Other names for the same wires on the sheet: C = clock
endmodule
