// Digital circuit parabin2bcd.dig as structural Verilog
module parabin2bcd (
  input  [15:0] in_1
);

  wire [0:0] gt4add3_1_o_2;
  wire [3:0] gt4add3_1_o, gt4add3_5_o, gt4add3_12_o;
  wire [3:1] gt4add3_22_o;
  wire [14:12] gt4add3_33_o;
  wire [15:9] gt4add3_20_o;
  wire [15:13] gt4add3_34_o;
  wire [16:5] gt4add3_9_o;
  wire [16:10] gt4add3_21_o;
  wire [16:11] gt4add3_32_o;
  wire [17:3] gt4add3_3_o;
  wire [17:7] gt4add3_11_o;
  wire [17:8] gt4add3_19_o;
  wire [18:4] gt4add3_4_o;
  wire [18:6] gt4add3_10_o;
  wire [19:2] gt4add3_2_o;

  Seven_Seg_Hex seven_seg_hex_1 (.d({gt4add3_2_o[19:17], gt4add3_1_o_2[0]}), .dp(1'b0));
  Seven_Seg_Hex seven_seg_hex_2 (.d(gt4add3_1_o), .dp(1'b0));
  gt4add3 gt4add3_1 (.I(gt4add3_2_o[16:13]), .O({gt4add3_1_o_2[0], gt4add3_1_o[3:1]}));
  gt4add3 gt4add3_2 (.I(gt4add3_3_o[17:14]), .O(gt4add3_2_o[17:14]));
  gt4add3 gt4add3_3 (.I(gt4add3_4_o[18:15]), .O({gt4add3_2_o[18], gt4add3_3_o[17:15]}));
  gt4add3 gt4add3_4 (.I({1'b0, gt4add3_10_o[18:17], gt4add3_9_o[16]}), .O({gt4add3_2_o[19], gt4add3_4_o[18:16]}));
  Seven_Seg_Hex seven_seg_hex_3 (.d(gt4add3_5_o), .dp(1'b0));
  gt4add3 gt4add3_5 (.I(gt4add3_2_o[12:9]), .O({gt4add3_1_o[0], gt4add3_5_o[3:1]}));
  gt4add3 gt4add3_6 (.I(gt4add3_3_o[13:10]), .O(gt4add3_2_o[13:10]));
  gt4add3 gt4add3_7 (.I(gt4add3_4_o[14:11]), .O(gt4add3_3_o[14:11]));
  gt4add3 gt4add3_8 (.I(gt4add3_9_o[15:12]), .O(gt4add3_4_o[15:12]));
  gt4add3 gt4add3_9 (.I(gt4add3_10_o[16:13]), .O(gt4add3_9_o[16:13]));
  gt4add3 gt4add3_10 (.I(gt4add3_11_o[17:14]), .O(gt4add3_10_o[17:14]));
  gt4add3 gt4add3_11 (.I({1'b0, gt4add3_19_o[17:15]}), .O({gt4add3_10_o[18], gt4add3_11_o[17:15]}));
  Seven_Seg_Hex seven_seg_hex_4 (.d(gt4add3_12_o), .dp(1'b0));
  gt4add3 gt4add3_12 (.I(gt4add3_2_o[8:5]), .O({gt4add3_5_o[0], gt4add3_12_o[3:1]}));
  gt4add3 gt4add3_13 (.I(gt4add3_3_o[9:6]), .O(gt4add3_2_o[9:6]));
  gt4add3 gt4add3_14 (.I(gt4add3_4_o[10:7]), .O(gt4add3_3_o[10:7]));
  gt4add3 gt4add3_15 (.I(gt4add3_9_o[11:8]), .O(gt4add3_4_o[11:8]));
  gt4add3 gt4add3_16 (.I(gt4add3_10_o[12:9]), .O(gt4add3_9_o[12:9]));
  gt4add3 gt4add3_17 (.I(gt4add3_11_o[13:10]), .O(gt4add3_10_o[13:10]));
  gt4add3 gt4add3_18 (.I(gt4add3_19_o[14:11]), .O(gt4add3_11_o[14:11]));
  gt4add3 gt4add3_19 (.I(gt4add3_20_o[15:12]), .O(gt4add3_19_o[15:12]));
  gt4add3 gt4add3_20 (.I(gt4add3_21_o[16:13]), .O({gt4add3_19_o[16], gt4add3_20_o[15:13]}));
  gt4add3 gt4add3_21 (.I({1'b0, gt4add3_32_o[16:14]}), .O({gt4add3_19_o[17], gt4add3_21_o[16:14]}));
  Seven_Seg_Hex seven_seg_hex_5 (.d({gt4add3_22_o, in_1[0]}), .dp(1'b0));
  gt4add3 gt4add3_22 (.I({gt4add3_2_o[4:2], in_1[1]}), .O({gt4add3_12_o[0], gt4add3_22_o}));
  gt4add3 gt4add3_23 (.I({gt4add3_3_o[5:3], in_1[2]}), .O(gt4add3_2_o[5:2]));
  gt4add3 gt4add3_24 (.I({gt4add3_4_o[6:4], in_1[3]}), .O(gt4add3_3_o[6:3]));
  gt4add3 gt4add3_25 (.I({gt4add3_9_o[7:5], in_1[4]}), .O(gt4add3_4_o[7:4]));
  gt4add3 gt4add3_26 (.I({gt4add3_10_o[8:6], in_1[5]}), .O(gt4add3_9_o[8:5]));
  gt4add3 gt4add3_27 (.I({gt4add3_11_o[9:7], in_1[6]}), .O(gt4add3_10_o[9:6]));
  gt4add3 gt4add3_28 (.I({gt4add3_19_o[10:8], in_1[7]}), .O(gt4add3_11_o[10:7]));
  gt4add3 gt4add3_29 (.I({gt4add3_20_o[11:9], in_1[8]}), .O(gt4add3_19_o[11:8]));
  gt4add3 gt4add3_30 (.I({gt4add3_21_o[12:10], in_1[9]}), .O(gt4add3_20_o[12:9]));
  gt4add3 gt4add3_31 (.I({gt4add3_32_o[13:11], in_1[10]}), .O(gt4add3_21_o[13:10]));
  gt4add3 gt4add3_32 (.I({gt4add3_33_o, in_1[11]}), .O(gt4add3_32_o[14:11]));
  gt4add3 gt4add3_33 (.I({gt4add3_34_o, in_1[12]}), .O({gt4add3_32_o[15], gt4add3_33_o}));
  gt4add3 gt4add3_34 (.I({1'b0, in_1[15:13]}), .O({gt4add3_32_o[16], gt4add3_34_o}));

  // Notes on the sheet:
  //   in_1: default 492357816
endmodule
