// Digital circuit parabin2bcd32.dig as structural Verilog
module parabin2bcd32 (
  input  [31:0] in_1
);

  wire [0:0] gt4add3_1_o_2;
  wire [3:0] gt4add3_1_o, gt4add3_4_o, gt4add3_10_o, gt4add3_19_o, gt4add3_34_o, gt4add3_52_o, gt4add3_73_o,
       gt4add3_97_o;
  wire [3:1] gt4add3_124_o;
  wire [31:29] gt4add3_152_o;
  wire [32:26] gt4add3_122_o;
  wire [32:30] gt4add3_153_o;
  wire [33:11] gt4add3_29_o;
  wire [33:23] gt4add3_95_o;
  wire [33:27] gt4add3_123_o;
  wire [33:28] gt4add3_151_o;
  wire [34:8] gt4add3_17_o;
  wire [34:12] gt4add3_30_o;
  wire [34:20] gt4add3_71_o;
  wire [34:24] gt4add3_96_o;
  wire [34:25] gt4add3_121_o;
  wire [35:5] gt4add3_8_o;
  wire [35:9] gt4add3_18_o;
  wire [35:13] gt4add3_31_o;
  wire [35:17] gt4add3_50_o;
  wire [35:21] gt4add3_72_o;
  wire [35:22] gt4add3_94_o;
  wire [36:4] gt4add3_7_o;
  wire [36:10] gt4add3_28_o;
  wire [36:14] gt4add3_32_o;
  wire [36:18] gt4add3_51_o;
  wire [36:19] gt4add3_70_o;
  wire [37:3] gt4add3_3_o;
  wire [37:7] gt4add3_16_o;
  wire [37:15] gt4add3_33_o;
  wire [37:16] gt4add3_49_o;
  wire [38:2] gt4add3_2_o;
  wire [38:6] gt4add3_9_o;

  Seven_Seg_Hex seven_seg_hex_1 (.d({1'b0, gt4add3_2_o[38:37], gt4add3_1_o_2[0]}), .dp(1'b0));
  Seven_Seg_Hex seven_seg_hex_2 (.d(gt4add3_1_o), .dp(1'b0));
  gt4add3 gt4add3_1 (.I(gt4add3_2_o[36:33]), .O({gt4add3_1_o_2[0], gt4add3_1_o[3:1]}));
  gt4add3 gt4add3_2 (.I(gt4add3_3_o[37:34]), .O(gt4add3_2_o[37:34]));
  gt4add3 gt4add3_3 (.I({gt4add3_9_o[38:37], gt4add3_7_o[36:35]}), .O({gt4add3_2_o[38], gt4add3_3_o[37:35]}));
  Seven_Seg_Hex seven_seg_hex_3 (.d(gt4add3_4_o), .dp(1'b0));
  gt4add3 gt4add3_4 (.I(gt4add3_2_o[32:29]), .O({gt4add3_1_o[0], gt4add3_4_o[3:1]}));
  gt4add3 gt4add3_5 (.I(gt4add3_3_o[33:30]), .O(gt4add3_2_o[33:30]));
  gt4add3 gt4add3_6 (.I(gt4add3_7_o[34:31]), .O(gt4add3_3_o[34:31]));
  gt4add3 gt4add3_7 (.I(gt4add3_8_o[35:32]), .O(gt4add3_7_o[35:32]));
  gt4add3 gt4add3_8 (.I(gt4add3_9_o[36:33]), .O({gt4add3_7_o[36], gt4add3_8_o[35:33]}));
  gt4add3 gt4add3_9 (.I(gt4add3_16_o[37:34]), .O(gt4add3_9_o[37:34]));
  Seven_Seg_Hex seven_seg_hex_4 (.d(gt4add3_10_o), .dp(1'b0));
  gt4add3 gt4add3_10 (.I(gt4add3_2_o[28:25]), .O({gt4add3_4_o[0], gt4add3_10_o[3:1]}));
  gt4add3 gt4add3_11 (.I(gt4add3_3_o[29:26]), .O(gt4add3_2_o[29:26]));
  gt4add3 gt4add3_12 (.I(gt4add3_7_o[30:27]), .O(gt4add3_3_o[30:27]));
  gt4add3 gt4add3_13 (.I(gt4add3_8_o[31:28]), .O(gt4add3_7_o[31:28]));
  gt4add3 gt4add3_14 (.I(gt4add3_9_o[32:29]), .O(gt4add3_8_o[32:29]));
  gt4add3 gt4add3_15 (.I(gt4add3_16_o[33:30]), .O(gt4add3_9_o[33:30]));
  gt4add3 gt4add3_16 (.I(gt4add3_17_o[34:31]), .O(gt4add3_16_o[34:31]));
  gt4add3 gt4add3_17 (.I(gt4add3_18_o[35:32]), .O({gt4add3_16_o[35], gt4add3_17_o[34:32]}));
  gt4add3 gt4add3_18 (.I(gt4add3_28_o[36:33]), .O({gt4add3_16_o[36], gt4add3_18_o[35:33]}));
  Seven_Seg_Hex seven_seg_hex_5 (.d(gt4add3_19_o), .dp(1'b0));
  gt4add3 gt4add3_19 (.I(gt4add3_2_o[24:21]), .O({gt4add3_10_o[0], gt4add3_19_o[3:1]}));
  gt4add3 gt4add3_20 (.I(gt4add3_3_o[25:22]), .O(gt4add3_2_o[25:22]));
  gt4add3 gt4add3_21 (.I(gt4add3_7_o[26:23]), .O(gt4add3_3_o[26:23]));
  gt4add3 gt4add3_22 (.I(gt4add3_8_o[27:24]), .O(gt4add3_7_o[27:24]));
  gt4add3 gt4add3_23 (.I(gt4add3_9_o[28:25]), .O(gt4add3_8_o[28:25]));
  gt4add3 gt4add3_24 (.I(gt4add3_16_o[29:26]), .O(gt4add3_9_o[29:26]));
  gt4add3 gt4add3_25 (.I(gt4add3_17_o[30:27]), .O(gt4add3_16_o[30:27]));
  gt4add3 gt4add3_26 (.I(gt4add3_18_o[31:28]), .O(gt4add3_17_o[31:28]));
  gt4add3 gt4add3_27 (.I(gt4add3_28_o[32:29]), .O(gt4add3_18_o[32:29]));
  gt4add3 gt4add3_28 (.I(gt4add3_29_o[33:30]), .O(gt4add3_28_o[33:30]));
  gt4add3 gt4add3_29 (.I(gt4add3_30_o[34:31]), .O({gt4add3_28_o[34], gt4add3_29_o[33:31]}));
  gt4add3 gt4add3_30 (.I(gt4add3_31_o[35:32]), .O({gt4add3_28_o[35], gt4add3_30_o[34:32]}));
  gt4add3 gt4add3_31 (.I(gt4add3_32_o[36:33]), .O({gt4add3_28_o[36], gt4add3_31_o[35:33]}));
  gt4add3 gt4add3_32 (.I(gt4add3_33_o[37:34]), .O({gt4add3_16_o[37], gt4add3_32_o[36:34]}));
  gt4add3 gt4add3_33 (.I({1'b0, gt4add3_49_o[37:35]}), .O({gt4add3_9_o[38], gt4add3_33_o[37:35]}));
  Seven_Seg_Hex seven_seg_hex_6 (.d(gt4add3_34_o), .dp(1'b0));
  gt4add3 gt4add3_34 (.I(gt4add3_2_o[20:17]), .O({gt4add3_19_o[0], gt4add3_34_o[3:1]}));
  gt4add3 gt4add3_35 (.I(gt4add3_3_o[21:18]), .O(gt4add3_2_o[21:18]));
  gt4add3 gt4add3_36 (.I(gt4add3_7_o[22:19]), .O(gt4add3_3_o[22:19]));
  gt4add3 gt4add3_37 (.I(gt4add3_8_o[23:20]), .O(gt4add3_7_o[23:20]));
  gt4add3 gt4add3_38 (.I(gt4add3_9_o[24:21]), .O(gt4add3_8_o[24:21]));
  gt4add3 gt4add3_39 (.I(gt4add3_16_o[25:22]), .O(gt4add3_9_o[25:22]));
  gt4add3 gt4add3_40 (.I(gt4add3_17_o[26:23]), .O(gt4add3_16_o[26:23]));
  gt4add3 gt4add3_41 (.I(gt4add3_18_o[27:24]), .O(gt4add3_17_o[27:24]));
  gt4add3 gt4add3_42 (.I(gt4add3_28_o[28:25]), .O(gt4add3_18_o[28:25]));
  gt4add3 gt4add3_43 (.I(gt4add3_29_o[29:26]), .O(gt4add3_28_o[29:26]));
  gt4add3 gt4add3_44 (.I(gt4add3_30_o[30:27]), .O(gt4add3_29_o[30:27]));
  gt4add3 gt4add3_45 (.I(gt4add3_31_o[31:28]), .O(gt4add3_30_o[31:28]));
  gt4add3 gt4add3_46 (.I(gt4add3_32_o[32:29]), .O(gt4add3_31_o[32:29]));
  gt4add3 gt4add3_47 (.I(gt4add3_33_o[33:30]), .O(gt4add3_32_o[33:30]));
  gt4add3 gt4add3_48 (.I(gt4add3_49_o[34:31]), .O(gt4add3_33_o[34:31]));
  gt4add3 gt4add3_49 (.I(gt4add3_50_o[35:32]), .O(gt4add3_49_o[35:32]));
  gt4add3 gt4add3_50 (.I(gt4add3_51_o[36:33]), .O({gt4add3_49_o[36], gt4add3_50_o[35:33]}));
  gt4add3 gt4add3_51 (.I({1'b0, gt4add3_70_o[36:34]}), .O({gt4add3_49_o[37], gt4add3_51_o[36:34]}));
  Seven_Seg_Hex seven_seg_hex_7 (.d(gt4add3_52_o), .dp(1'b0));
  gt4add3 gt4add3_52 (.I(gt4add3_2_o[16:13]), .O({gt4add3_34_o[0], gt4add3_52_o[3:1]}));
  gt4add3 gt4add3_53 (.I(gt4add3_3_o[17:14]), .O(gt4add3_2_o[17:14]));
  gt4add3 gt4add3_54 (.I(gt4add3_7_o[18:15]), .O(gt4add3_3_o[18:15]));
  gt4add3 gt4add3_55 (.I(gt4add3_8_o[19:16]), .O(gt4add3_7_o[19:16]));
  gt4add3 gt4add3_56 (.I(gt4add3_9_o[20:17]), .O(gt4add3_8_o[20:17]));
  gt4add3 gt4add3_57 (.I(gt4add3_16_o[21:18]), .O(gt4add3_9_o[21:18]));
  gt4add3 gt4add3_58 (.I(gt4add3_17_o[22:19]), .O(gt4add3_16_o[22:19]));
  gt4add3 gt4add3_59 (.I(gt4add3_18_o[23:20]), .O(gt4add3_17_o[23:20]));
  gt4add3 gt4add3_60 (.I(gt4add3_28_o[24:21]), .O(gt4add3_18_o[24:21]));
  gt4add3 gt4add3_61 (.I(gt4add3_29_o[25:22]), .O(gt4add3_28_o[25:22]));
  gt4add3 gt4add3_62 (.I(gt4add3_30_o[26:23]), .O(gt4add3_29_o[26:23]));
  gt4add3 gt4add3_63 (.I(gt4add3_31_o[27:24]), .O(gt4add3_30_o[27:24]));
  gt4add3 gt4add3_64 (.I(gt4add3_32_o[28:25]), .O(gt4add3_31_o[28:25]));
  gt4add3 gt4add3_65 (.I(gt4add3_33_o[29:26]), .O(gt4add3_32_o[29:26]));
  gt4add3 gt4add3_66 (.I(gt4add3_49_o[30:27]), .O(gt4add3_33_o[30:27]));
  gt4add3 gt4add3_67 (.I(gt4add3_50_o[31:28]), .O(gt4add3_49_o[31:28]));
  gt4add3 gt4add3_68 (.I(gt4add3_51_o[32:29]), .O(gt4add3_50_o[32:29]));
  gt4add3 gt4add3_69 (.I(gt4add3_70_o[33:30]), .O(gt4add3_51_o[33:30]));
  gt4add3 gt4add3_70 (.I(gt4add3_71_o[34:31]), .O(gt4add3_70_o[34:31]));
  gt4add3 gt4add3_71 (.I(gt4add3_72_o[35:32]), .O({gt4add3_70_o[35], gt4add3_71_o[34:32]}));
  gt4add3 gt4add3_72 (.I({1'b0, gt4add3_94_o[35:33]}), .O({gt4add3_70_o[36], gt4add3_72_o[35:33]}));
  Seven_Seg_Hex seven_seg_hex_8 (.d(gt4add3_73_o), .dp(1'b0));
  gt4add3 gt4add3_73 (.I(gt4add3_2_o[12:9]), .O({gt4add3_52_o[0], gt4add3_73_o[3:1]}));
  gt4add3 gt4add3_74 (.I(gt4add3_3_o[13:10]), .O(gt4add3_2_o[13:10]));
  gt4add3 gt4add3_75 (.I(gt4add3_7_o[14:11]), .O(gt4add3_3_o[14:11]));
  gt4add3 gt4add3_76 (.I(gt4add3_8_o[15:12]), .O(gt4add3_7_o[15:12]));
  gt4add3 gt4add3_77 (.I(gt4add3_9_o[16:13]), .O(gt4add3_8_o[16:13]));
  gt4add3 gt4add3_78 (.I(gt4add3_16_o[17:14]), .O(gt4add3_9_o[17:14]));
  gt4add3 gt4add3_79 (.I(gt4add3_17_o[18:15]), .O(gt4add3_16_o[18:15]));
  gt4add3 gt4add3_80 (.I(gt4add3_18_o[19:16]), .O(gt4add3_17_o[19:16]));
  gt4add3 gt4add3_81 (.I(gt4add3_28_o[20:17]), .O(gt4add3_18_o[20:17]));
  gt4add3 gt4add3_82 (.I(gt4add3_29_o[21:18]), .O(gt4add3_28_o[21:18]));
  gt4add3 gt4add3_83 (.I(gt4add3_30_o[22:19]), .O(gt4add3_29_o[22:19]));
  gt4add3 gt4add3_84 (.I(gt4add3_31_o[23:20]), .O(gt4add3_30_o[23:20]));
  gt4add3 gt4add3_85 (.I(gt4add3_32_o[24:21]), .O(gt4add3_31_o[24:21]));
  gt4add3 gt4add3_86 (.I(gt4add3_33_o[25:22]), .O(gt4add3_32_o[25:22]));
  gt4add3 gt4add3_87 (.I(gt4add3_49_o[26:23]), .O(gt4add3_33_o[26:23]));
  gt4add3 gt4add3_88 (.I(gt4add3_50_o[27:24]), .O(gt4add3_49_o[27:24]));
  gt4add3 gt4add3_89 (.I(gt4add3_51_o[28:25]), .O(gt4add3_50_o[28:25]));
  gt4add3 gt4add3_90 (.I(gt4add3_70_o[29:26]), .O(gt4add3_51_o[29:26]));
  gt4add3 gt4add3_91 (.I(gt4add3_71_o[30:27]), .O(gt4add3_70_o[30:27]));
  gt4add3 gt4add3_92 (.I(gt4add3_72_o[31:28]), .O(gt4add3_71_o[31:28]));
  gt4add3 gt4add3_93 (.I(gt4add3_94_o[32:29]), .O(gt4add3_72_o[32:29]));
  gt4add3 gt4add3_94 (.I(gt4add3_95_o[33:30]), .O(gt4add3_94_o[33:30]));
  gt4add3 gt4add3_95 (.I(gt4add3_96_o[34:31]), .O({gt4add3_94_o[34], gt4add3_95_o[33:31]}));
  gt4add3 gt4add3_96 (.I({1'b0, gt4add3_121_o[34:32]}), .O({gt4add3_94_o[35], gt4add3_96_o[34:32]}));
  Seven_Seg_Hex seven_seg_hex_9 (.d(gt4add3_97_o), .dp(1'b0));
  gt4add3 gt4add3_97 (.I(gt4add3_2_o[8:5]), .O({gt4add3_73_o[0], gt4add3_97_o[3:1]}));
  gt4add3 gt4add3_98 (.I(gt4add3_3_o[9:6]), .O(gt4add3_2_o[9:6]));
  gt4add3 gt4add3_99 (.I(gt4add3_7_o[10:7]), .O(gt4add3_3_o[10:7]));
  gt4add3 gt4add3_100 (.I(gt4add3_8_o[11:8]), .O(gt4add3_7_o[11:8]));
  gt4add3 gt4add3_101 (.I(gt4add3_9_o[12:9]), .O(gt4add3_8_o[12:9]));
  gt4add3 gt4add3_102 (.I(gt4add3_16_o[13:10]), .O(gt4add3_9_o[13:10]));
  gt4add3 gt4add3_103 (.I(gt4add3_17_o[14:11]), .O(gt4add3_16_o[14:11]));
  gt4add3 gt4add3_104 (.I(gt4add3_18_o[15:12]), .O(gt4add3_17_o[15:12]));
  gt4add3 gt4add3_105 (.I(gt4add3_28_o[16:13]), .O(gt4add3_18_o[16:13]));
  gt4add3 gt4add3_106 (.I(gt4add3_29_o[17:14]), .O(gt4add3_28_o[17:14]));
  gt4add3 gt4add3_107 (.I(gt4add3_30_o[18:15]), .O(gt4add3_29_o[18:15]));
  gt4add3 gt4add3_108 (.I(gt4add3_31_o[19:16]), .O(gt4add3_30_o[19:16]));
  gt4add3 gt4add3_109 (.I(gt4add3_32_o[20:17]), .O(gt4add3_31_o[20:17]));
  gt4add3 gt4add3_110 (.I(gt4add3_33_o[21:18]), .O(gt4add3_32_o[21:18]));
  gt4add3 gt4add3_111 (.I(gt4add3_49_o[22:19]), .O(gt4add3_33_o[22:19]));
  gt4add3 gt4add3_112 (.I(gt4add3_50_o[23:20]), .O(gt4add3_49_o[23:20]));
  gt4add3 gt4add3_113 (.I(gt4add3_51_o[24:21]), .O(gt4add3_50_o[24:21]));
  gt4add3 gt4add3_114 (.I(gt4add3_70_o[25:22]), .O(gt4add3_51_o[25:22]));
  gt4add3 gt4add3_115 (.I(gt4add3_71_o[26:23]), .O(gt4add3_70_o[26:23]));
  gt4add3 gt4add3_116 (.I(gt4add3_72_o[27:24]), .O(gt4add3_71_o[27:24]));
  gt4add3 gt4add3_117 (.I(gt4add3_94_o[28:25]), .O(gt4add3_72_o[28:25]));
  gt4add3 gt4add3_118 (.I(gt4add3_95_o[29:26]), .O(gt4add3_94_o[29:26]));
  gt4add3 gt4add3_119 (.I(gt4add3_96_o[30:27]), .O(gt4add3_95_o[30:27]));
  gt4add3 gt4add3_120 (.I(gt4add3_121_o[31:28]), .O(gt4add3_96_o[31:28]));
  gt4add3 gt4add3_121 (.I(gt4add3_122_o[32:29]), .O(gt4add3_121_o[32:29]));
  gt4add3 gt4add3_122 (.I(gt4add3_123_o[33:30]), .O({gt4add3_121_o[33], gt4add3_122_o[32:30]}));
  gt4add3 gt4add3_123 (.I({1'b0, gt4add3_151_o[33:31]}), .O({gt4add3_121_o[34], gt4add3_123_o[33:31]}));
  Seven_Seg_Hex seven_seg_hex_10 (.d({gt4add3_124_o, in_1[0]}), .dp(1'b0));
  gt4add3 gt4add3_124 (.I({gt4add3_2_o[4:2], in_1[1]}), .O({gt4add3_97_o[0], gt4add3_124_o}));
  gt4add3 gt4add3_125 (.I({gt4add3_3_o[5:3], in_1[2]}), .O(gt4add3_2_o[5:2]));
  gt4add3 gt4add3_126 (.I({gt4add3_7_o[6:4], in_1[3]}), .O(gt4add3_3_o[6:3]));
  gt4add3 gt4add3_127 (.I({gt4add3_8_o[7:5], in_1[4]}), .O(gt4add3_7_o[7:4]));
  gt4add3 gt4add3_128 (.I({gt4add3_9_o[8:6], in_1[5]}), .O(gt4add3_8_o[8:5]));
  gt4add3 gt4add3_129 (.I({gt4add3_16_o[9:7], in_1[6]}), .O(gt4add3_9_o[9:6]));
  gt4add3 gt4add3_130 (.I({gt4add3_17_o[10:8], in_1[7]}), .O(gt4add3_16_o[10:7]));
  gt4add3 gt4add3_131 (.I({gt4add3_18_o[11:9], in_1[8]}), .O(gt4add3_17_o[11:8]));
  gt4add3 gt4add3_132 (.I({gt4add3_28_o[12:10], in_1[9]}), .O(gt4add3_18_o[12:9]));
  gt4add3 gt4add3_133 (.I({gt4add3_29_o[13:11], in_1[10]}), .O(gt4add3_28_o[13:10]));
  gt4add3 gt4add3_134 (.I({gt4add3_30_o[14:12], in_1[11]}), .O(gt4add3_29_o[14:11]));
  gt4add3 gt4add3_135 (.I({gt4add3_31_o[15:13], in_1[12]}), .O(gt4add3_30_o[15:12]));
  gt4add3 gt4add3_136 (.I({gt4add3_32_o[16:14], in_1[13]}), .O(gt4add3_31_o[16:13]));
  gt4add3 gt4add3_137 (.I({gt4add3_33_o[17:15], in_1[14]}), .O(gt4add3_32_o[17:14]));
  gt4add3 gt4add3_138 (.I({gt4add3_49_o[18:16], in_1[15]}), .O(gt4add3_33_o[18:15]));
  gt4add3 gt4add3_139 (.I({gt4add3_50_o[19:17], in_1[16]}), .O(gt4add3_49_o[19:16]));
  gt4add3 gt4add3_140 (.I({gt4add3_51_o[20:18], in_1[17]}), .O(gt4add3_50_o[20:17]));
  gt4add3 gt4add3_141 (.I({gt4add3_70_o[21:19], in_1[18]}), .O(gt4add3_51_o[21:18]));
  gt4add3 gt4add3_142 (.I({gt4add3_71_o[22:20], in_1[19]}), .O(gt4add3_70_o[22:19]));
  gt4add3 gt4add3_143 (.I({gt4add3_72_o[23:21], in_1[20]}), .O(gt4add3_71_o[23:20]));
  gt4add3 gt4add3_144 (.I({gt4add3_94_o[24:22], in_1[21]}), .O(gt4add3_72_o[24:21]));
  gt4add3 gt4add3_145 (.I({gt4add3_95_o[25:23], in_1[22]}), .O(gt4add3_94_o[25:22]));
  gt4add3 gt4add3_146 (.I({gt4add3_96_o[26:24], in_1[23]}), .O(gt4add3_95_o[26:23]));
  gt4add3 gt4add3_147 (.I({gt4add3_121_o[27:25], in_1[24]}), .O(gt4add3_96_o[27:24]));
  gt4add3 gt4add3_148 (.I({gt4add3_122_o[28:26], in_1[25]}), .O(gt4add3_121_o[28:25]));
  gt4add3 gt4add3_149 (.I({gt4add3_123_o[29:27], in_1[26]}), .O(gt4add3_122_o[29:26]));
  gt4add3 gt4add3_150 (.I({gt4add3_151_o[30:28], in_1[27]}), .O(gt4add3_123_o[30:27]));
  gt4add3 gt4add3_151 (.I({gt4add3_152_o, in_1[28]}), .O(gt4add3_151_o[31:28]));
  gt4add3 gt4add3_152 (.I({gt4add3_153_o, in_1[29]}), .O({gt4add3_151_o[32], gt4add3_152_o}));
  gt4add3 gt4add3_153 (.I({2'b00, in_1[31:30]}), .O({gt4add3_151_o[33], gt4add3_153_o}));

  // Notes on the sheet:
  //   in_1: default 492357816
endmodule
