// Digital circuit abstraction.dig as structural Verilog
module abstraction (
);

  wire button_1_out, dipswitch_1_out, switch_1_b, switch_2_b, tunnel;

  Button button_1 (.out(button_1_out));
  DipSwitch dipswitch_1 (.out(dipswitch_1_out));
  Button button_2 (.out(tunnel));
  Switch switch_1 (.A(1'b1), .B(switch_1_b));
  Switch switch_2 (.A(1'b1), .B(switch_2_b));
  // PolarityAwareLED polarityawareled_1: pin names not known; wires that end beside it: switch_1_b, 1'b0
  LED led_1 (.in(switch_2_b));
  LED led_2 (.in(button_1_out));
  LED led_3 (.in(dipswitch_1_out));
  LED led_4 (.in(tunnel));
  LED led_5 (.in(1'b1));
  LED led_6 (.in(1'b0));

  // Notes on the sheet:
  //   Positive Voltage
  //   Negative Voltage
endmodule
