// Digital circuit busses.dig as structural Verilog
module busses (
  input  A,
  input  [3:0] B,
  input  [3:0] C,
  output Y,
  output [3:0] X,
  output [3:0] Z
);

  DipSwitch dipswitch_1 (.out(Z[0]));
  DipSwitch dipswitch_2 (.out(Z[1]));
  DipSwitch dipswitch_3 (.out(Z[2]));
  DipSwitch dipswitch_4 (.out(Z[3]));
  LED led_1 (.in(C[0]));
  LED led_2 (.in(C[1]));
  LED led_3 (.in(C[2]));
  LED led_4 (.in(C[3]));

  assign X = B;
  assign Y = A;
endmodule
