// Digital circuit combinational.dig as structural Verilog
module combinational (
);

  wire and_1_out, and_2_out, and_3_out, and_4_out, and_5_out, and_6_out, and_7_out, and_8_out, and_9_out,
       and_10_out, and_11_out, and_12_out, and_13_out, and_14_out, and_15_out, and_16_out, and_17_out,
       and_18_out, and_19_out, and_20_out, and_21_out, dipswitch_1_out, dipswitch_2_out, dipswitch_3_out,
       dipswitch_4_out, dipswitch_5_out, dipswitch_6_out, dipswitch_7_out, dipswitch_8_out, dipswitch_9_out,
       dipswitch_10_out, dipswitch_11_out, dipswitch_12_out, dipswitch_15_out, dipswitch_16_out,
       dipswitch_17_out, dipswitch_18_out, dipswitch_19_out, dipswitch_20_out, dipswitch_21_out,
       dipswitch_22_out, multiplexer_1_out, not_1_out, not_2_out, not_3_out, not_4_out, not_5_out, not_6_out,
       not_7_out, not_8_out, not_9_out, or_1_out, or_2_out, or_3_out, or_4_out, or_5_out, or_6_out, or_7_out,
       or_8_out, or_9_out, or_10_out, or_11_out, xor_1_out, xor_2_out, xor_3_out, xor_4_out, xor_5_out;
  wire [1:0] dipswitch_13_out;

  DipSwitch dipswitch_1 (.out(dipswitch_1_out));
  DipSwitch dipswitch_2 (.out(dipswitch_2_out));
  DipSwitch dipswitch_3 (.out(dipswitch_3_out));
  DipSwitch dipswitch_4 (.out(dipswitch_4_out));
  DipSwitch dipswitch_5 (.out(dipswitch_5_out));
  DipSwitch dipswitch_6 (.out(dipswitch_6_out));
  DipSwitch dipswitch_7 (.out(dipswitch_7_out));
  not not_1 (not_1_out, dipswitch_1_out);
  and and_1 (and_1_out, dipswitch_1_out, dipswitch_6_out);
  or or_1 (or_1_out, dipswitch_1_out, dipswitch_6_out);
  xor xor_1 (xor_1_out, dipswitch_1_out, dipswitch_6_out);
  DipSwitch dipswitch_8 (.out(dipswitch_8_out));
  DipSwitch dipswitch_9 (.out(dipswitch_9_out));
  DipSwitch dipswitch_10 (.out(dipswitch_10_out));
  DipSwitch dipswitch_11 (.out(dipswitch_11_out));
  DipSwitch dipswitch_12 (.out(dipswitch_12_out));
  not not_2 (not_2_out, dipswitch_2_out);
  and and_2 (and_2_out, dipswitch_2_out, dipswitch_7_out);
  or or_2 (or_2_out, dipswitch_2_out, dipswitch_7_out);
  xor xor_2 (xor_2_out, dipswitch_2_out, dipswitch_7_out);
  not not_3 (not_3_out, dipswitch_4_out);
  and and_3 (and_3_out, dipswitch_4_out, dipswitch_9_out);
  or or_3 (or_3_out, dipswitch_4_out, dipswitch_9_out);
  xor xor_3 (xor_3_out, dipswitch_4_out, dipswitch_9_out);
  not not_4 (not_4_out, dipswitch_5_out);
  and and_4 (and_4_out, dipswitch_5_out, dipswitch_10_out);
  or or_4 (or_4_out, dipswitch_5_out, dipswitch_10_out);
  xor xor_4 (xor_4_out, dipswitch_5_out, dipswitch_10_out);
  DipSwitch dipswitch_13 (.out(dipswitch_13_out[0]));
  DipSwitch dipswitch_14 (.out(dipswitch_13_out[1]));
  not not_5 (not_5_out, dipswitch_3_out);
  and and_5 (and_5_out, dipswitch_3_out, dipswitch_8_out);
  or or_5 (or_5_out, dipswitch_3_out, dipswitch_8_out);
  xor xor_5 (xor_5_out, dipswitch_3_out, dipswitch_8_out);
  DipSwitch dipswitch_15 (.out(dipswitch_15_out));
  DipSwitch dipswitch_16 (.out(dipswitch_16_out));
  DipSwitch dipswitch_17 (.out(dipswitch_17_out));
  DipSwitch dipswitch_18 (.out(dipswitch_18_out));
  DipSwitch dipswitch_19 (.out(dipswitch_19_out));
  DipSwitch dipswitch_20 (.out(dipswitch_20_out));
  DipSwitch dipswitch_21 (.out(dipswitch_21_out));
  DipSwitch dipswitch_22 (.out(dipswitch_22_out));
  not not_6 (not_6_out, dipswitch_12_out);
  not not_7 (not_7_out, dipswitch_11_out);
  not not_8 (not_8_out, dipswitch_11_out);
  not not_9 (not_9_out, dipswitch_12_out);
  and and_6 (and_6_out, not_6_out, not_7_out);
  and and_7 (and_7_out, dipswitch_12_out, not_8_out);
  and and_8 (and_8_out, not_9_out, dipswitch_11_out);
  and and_9 (and_9_out, dipswitch_11_out, dipswitch_12_out);
  and and_10 (and_10_out, dipswitch_15_out, not_3_out);
  and and_11 (and_11_out, dipswitch_16_out, and_3_out);
  and and_12 (and_12_out, dipswitch_17_out, or_3_out);
  and and_13 (and_13_out, dipswitch_18_out, xor_3_out);
  and and_14 (and_14_out, dipswitch_19_out, not_4_out);
  and and_15 (and_15_out, dipswitch_20_out, and_4_out);
  and and_16 (and_16_out, dipswitch_21_out, or_4_out);
  and and_17 (and_17_out, dipswitch_22_out, xor_4_out);
  and and_18 (and_18_out, and_6_out, not_1_out);
  and and_19 (and_19_out, and_7_out, and_1_out);
  and and_20 (and_20_out, and_8_out, or_1_out);
  and and_21 (and_21_out, and_9_out, xor_1_out);
  Multiplexer #(.Selector_Bits(2)) multiplexer_1 (
    .sel(dipswitch_13_out), .in_0(not_2_out), .in_1(and_2_out), .in_2(or_2_out), .in_3(xor_2_out),
    .out(multiplexer_1_out));
  LED led_1 (.in(not_5_out));
  LED led_2 (.in(and_5_out));
  LED led_3 (.in(or_5_out));
  LED led_4 (.in(xor_5_out));
  LED led_5 (.in(and_10_out));
  LED led_6 (.in(and_11_out));
  LED led_7 (.in(and_12_out));
  LED led_8 (.in(and_13_out));
  or or_6 (or_6_out, and_18_out, and_19_out);
  or or_7 (or_7_out, and_20_out, and_21_out);
  or or_8 (or_8_out, and_14_out, and_15_out);
  or or_9 (or_9_out, and_16_out, and_17_out);
  or or_10 (or_10_out, or_8_out, or_9_out);
  or or_11 (or_11_out, or_6_out, or_7_out);
  LED led_9 (.in(or_11_out));
  LED led_10 (.in(or_10_out));
  LED led_11 (.in(multiplexer_1_out));
endmodule
