// Digital circuit intro.dig as structural Verilog
module intro (
);

  digital digital_1 ();
  logicgates logicgates_1 ();
  busses busses_1 ();  // open: A, B, C, Y, X, Z
  wires wires_1 ();
  abstraction abstraction_1 ();
  combinational combinational_1 ();
  switches switches_1 ();
  inputoutput inputoutput_1 ();  // open: A, B, Y
  sequential sequential_1 ();
endmodule
