// Digital circuit logicgates.dig as structural Verilog
module logicgates (
);

  wire A_2_b, A_3_p3, A_4_b, A_5_p3, A_6_p3, A_7_p3, A_8_p3, A_9_b, A_10_b, A_11_p2, A_11_p3, A_p3,
       and_1_out, B_2_p3, B_3_b, B_4_p3, B_5_p3, B_6_p3, B_7_b, B_9_p3, B_b, nfet_3_s, nfet_4_s, nfet_5_s,
       not_1_out, or_1_out, pfet_1_d, pfet_2_d, pfet_3_d, switch_1_b, xor_1_out;

  // SwitchDT A: pin names not known; wires that end beside it: 1'b1, 1'b0, A_p3
  Switch A_2 (.A(1'b1), .B(A_2_b));
  Switch B (.A(1'b1), .B(B_b));
  // SwitchDT A_3: pin names not known; wires that end beside it: 1'b1, 1'b0, A_3_p3
  // SwitchDT B_2: pin names not known; wires that end beside it: 1'b1, 1'b0, B_2_p3
  Switch A_4 (.A(1'b1), .B(A_4_b));
  Switch B_3 (.A(1'b1), .B(B_3_b));
  // SwitchDT A_5: pin names not known; wires that end beside it: 1'b1, 1'b0, A_5_p3
  // SwitchDT B_4: pin names not known; wires that end beside it: 1'b1, 1'b0, B_4_p3
  // SwitchDT A_6: pin names not known; wires that end beside it: 1'b1, 1'b0, A_6_p3
  // SwitchDT B_5: pin names not known; wires that end beside it: 1'b1, 1'b0, B_5_p3
  // SwitchDT A_7: pin names not known; wires that end beside it: 1'b1, 1'b0, A_7_p3
  // SwitchDT B_6: pin names not known; wires that end beside it: 1'b1, 1'b0, B_6_p3
  // SwitchDT A_8: pin names not known; wires that end beside it: 1'b1, 1'b0, A_8_p3
  Switch A_9 (.A(1'b1), .B(A_9_b));
  Switch A_10 (.A(1'b1), .B(A_10_b));
  // SwitchDT A_11: pin names not known; wires that end beside it: 1'b1, A_11_p2, A_11_p3
  PFET pfet_1 (.G(A_6_p3), .S(1'b1), .D(pfet_1_d));
  NFET nfet_1 (.G(A_6_p3), .D(pfet_1_d), .S(1'b0));
  Switch #(.Closed("true")) switch_1 (.A(1'b1), .B(switch_1_b));
  PFET pfet_2 (.G(A_8_p3), .S(1'b1), .D(pfet_2_d));
  NFET nfet_2 (.G(A_8_p3), .D(pfet_2_d), .S(1'b0));
  not not_1 (not_1_out, A_p3);
  NFET nfet_3 (.G(A_2_b), .D(1'b1), .S(nfet_3_s));
  NFET nfet_4 (.G(B_b), .D(nfet_3_s), .S(nfet_4_s));
  and and_1 (and_1_out, A_3_p3, B_2_p3);
  NFET nfet_5 (.G(A_4_b), .D(1'b1), .S(nfet_5_s));
  NFET nfet_6 (.G(B_3_b), .D(1'b1), .S(nfet_5_s));
  or or_1 (or_1_out, A_5_p3, B_4_p3);
  xor xor_1 (xor_1_out, A_7_p3, B_6_p3);
  Switch B_7 (.A(A_9_b), .B(B_7_b));
  Switch B_8 (.A(1'b1), .B(A_10_b));
  // SwitchDT B_9: pin names not known; wires that end beside it: A_11_p3, A_11_p2, B_9_p3
  PFET pfet_3 (.G(B_5_p3), .S(A_6_p3), .D(pfet_3_d));
  NFET nfet_7 (.G(B_5_p3), .D(pfet_3_d), .S(pfet_1_d));
  // PolarityAwareLED polarityawareled_1: pin names not known; wires that end beside it: nfet_5_s, 1'b0
  // PolarityAwareLED polarityawareled_2: pin names not known; wires that end beside it: pfet_3_d, 1'b0
  // PolarityAwareLED polarityawareled_3: pin names not known; wires that end beside it: switch_1_b, 1'b0
  // PolarityAwareLED polarityawareled_4: pin names not known; wires that end beside it: pfet_2_d, 1'b0
  // PolarityAwareLED polarityawareled_5: pin names not known; wires that end beside it: not_1_out, 1'b0
  // PolarityAwareLED polarityawareled_6: pin names not known; wires that end beside it: B_7_b, 1'b0
  // PolarityAwareLED polarityawareled_7: pin names not known; wires that end beside it: nfet_4_s, 1'b0
  // PolarityAwareLED polarityawareled_8: pin names not known; wires that end beside it: and_1_out, 1'b0
  // PolarityAwareLED polarityawareled_9: pin names not known; wires that end beside it: A_10_b, 1'b0
  // PolarityAwareLED polarityawareled_10: pin names not known; wires that end beside it: or_1_out, 1'b0
  // PolarityAwareLED polarityawareled_11: pin names not known; wires that end beside it: B_9_p3, 1'b0
  // PolarityAwareLED polarityawareled_12: pin names not known; wires that end beside it: xor_1_out, 1'b0

  // Notes on the sheet:
  //   NOT
  //   AND
  //   OR
  //   XOR
endmodule
