// Digital circuit sequential.dig as structural Verilog
module sequential (
);

  wire and_1_out, and_2_out, and_3_out, and_4_out, button_1_out, button_2_out, button_3_out, button_4_out,
       button_5_out, clock_out, d_ff_1_q, d_ff_2_q, d_ff_3_q, d_ff_4_q, d_ff_5_q, d_ff_6_q, d_ff_7_q,
       d_ff_8_q, d_ff_9_q, d_ff_10_q, D_out, dipswitch_1_out, dipswitch_2_out, dipswitch_3_out,
       dipswitch_4_out, dipswitch_5_out, dipswitch_6_out, dipswitch_7_out, dipswitch_8_out, nor_1_out,
       nor_2_out, nor_3_out, nor_4_out, nor_5_out, nor_6_out, nor_7_out, not_1_out, not_2_out, or_1_out;

  DipSwitch dipswitch_1 (.out(dipswitch_1_out));
  Button button_1 (.out(button_1_out));
  DipSwitch D (.out(D_out));
  D_FF d_ff_1 (.D(dipswitch_1_out), .C(button_1_out), .Q(d_ff_1_q));  // open: nQ
  Button button_2 (.out(button_2_out));
  Button button_3 (.out(button_3_out));
  DipSwitch dipswitch_2 (.out(dipswitch_2_out));
  // Probe D on D_out
  Button clock (.out(clock_out));
  LED led_1 (.in(d_ff_1_q));
  D_FF d_ff_2 (.D(d_ff_1_q), .C(button_1_out), .Q(d_ff_2_q));  // open: nQ
  DipSwitch dipswitch_3 (.out(dipswitch_3_out));
  DipSwitch dipswitch_4 (.out(dipswitch_4_out));
  DipSwitch dipswitch_5 (.out(dipswitch_5_out));
  DipSwitch dipswitch_6 (.out(dipswitch_6_out));
  Button button_4 (.out(button_4_out));
  Button button_5 (.out(button_5_out));
  DipSwitch dipswitch_7 (.out(dipswitch_7_out));
  DipSwitch dipswitch_8 (.out(dipswitch_8_out));
  LED led_2 (.in(d_ff_2_q));
  or or_1 (or_1_out, dipswitch_3_out, dipswitch_4_out);
  nor nor_1 (nor_1_out, dipswitch_5_out, dipswitch_6_out);
  nor nor_2 (nor_2_out, button_4_out, nor_3_out);
  nor nor_3 (nor_3_out, nor_2_out, button_5_out);
  and and_1 (and_1_out, button_2_out, dipswitch_7_out);
  and and_2 (and_2_out, dipswitch_7_out, button_3_out);
  not not_1 (not_1_out, dipswitch_2_out);
  D_FF d_ff_3 (.D(d_ff_2_q), .C(button_1_out), .Q(d_ff_3_q));  // open: nQ
  not not_2 (not_2_out, or_1_out);
  and and_3 (and_3_out, dipswitch_2_out, dipswitch_8_out);
  and and_4 (and_4_out, dipswitch_8_out, not_1_out);
  D_FF d_ff_4 (.D(D_out), .C(clock_out), .Q(d_ff_4_q));  // open: nQ
  LED led_3 (.in(d_ff_3_q));
  D_FF d_ff_5 (.D(d_ff_3_q), .C(button_1_out), .Q(d_ff_5_q));  // open: nQ
  nor nor_4 (nor_4_out, and_1_out, nor_5_out);
  nor nor_5 (nor_5_out, nor_4_out, and_2_out);
  nor nor_6 (nor_6_out, and_3_out, nor_7_out);
  nor nor_7 (nor_7_out, nor_6_out, and_4_out);
  LED led_4 (.in(d_ff_5_q));
  D_FF d_ff_6 (.D(d_ff_5_q), .C(button_1_out), .Q(d_ff_6_q));  // open: nQ
  LED led_5 (.in(not_2_out));
  LED led_6 (.in(nor_1_out));
  LED led_7 (.in(nor_3_out));
  // Probe Q on d_ff_4_q
  LED led_8 (.in(d_ff_6_q));
  D_FF d_ff_7 (.D(d_ff_6_q), .C(button_1_out), .Q(d_ff_7_q));  // open: nQ
  LED led_9 (.in(d_ff_7_q));
  LED led_10 (.in(nor_5_out));
  LED led_11 (.in(nor_7_out));
  LED led_12 (.in(d_ff_4_q));
  D_FF d_ff_8 (.D(d_ff_7_q), .C(button_1_out), .Q(d_ff_8_q));  // open: nQ
  LED led_13 (.in(d_ff_8_q));
  D_FF d_ff_9 (.D(d_ff_8_q), .C(button_1_out), .Q(d_ff_9_q));  // open: nQ
  LED led_14 (.in(d_ff_9_q));
  D_FF d_ff_10 (.D(d_ff_9_q), .C(button_1_out), .Q(d_ff_10_q));  // open: nQ
  LED led_15 (.in(d_ff_10_q));

  // Notes on the sheet:
  //   S-R Flip Flop with Enable
  //   D Flip Flop with Clock
  //   OR
  //   NOR
  //   S-R Flip Flop
  //   D Flip Flop
  //   NOT
endmodule
