// Digital circuit switches.dig as structural Verilog
module switches (
);

  wire A_2_b, A_3_p2, A_3_p3, A_b, B_3_p3, B_b, switch_1_b;

  Switch A (.A(1'b1), .B(A_b));
  Switch A_2 (.A(1'b1), .B(A_2_b));
  // SwitchDT A_3: pin names not known; wires that end beside it: 1'b1, A_3_p2, A_3_p3
  Switch #(.Closed("true")) switch_1 (.A(1'b1), .B(switch_1_b));
  Switch B (.A(A_b), .B(B_b));
  Switch B_2 (.A(1'b1), .B(A_2_b));
  // SwitchDT B_3: pin names not known; wires that end beside it: A_3_p3, A_3_p2, B_3_p3
  // PolarityAwareLED polarityawareled_1: pin names not known; wires that end beside it: switch_1_b, 1'b0
  // PolarityAwareLED polarityawareled_2: pin names not known; wires that end beside it: B_b, 1'b0
  // PolarityAwareLED polarityawareled_3: pin names not known; wires that end beside it: A_2_b, 1'b0
  // PolarityAwareLED polarityawareled_4: pin names not known; wires that end beside it: B_3_p3, 1'b0

  // Notes on the sheet:
  //   NOT
  //   AND
  //   OR
  //   XOR
endmodule
