// Digital circuit transistors.dig as structural Verilog
module transistors (
);

  wire A_2_p3, A_3_b, A_4_p3, A_5_p3, A_6_p3, A_7_p3, A_8_b, A_9_b, A_10_p2, A_10_p3, A_b, and_1_out, B_2_p3,
       B_3_b, B_4_p3, B_5_p3, B_6_p3, B_7_b, B_9_p3, B_b, nfet_3_s, nfet_4_s, nfet_5_s, or_1_out, pfet_1_d,
       pfet_2_d, pfet_3_d, switch_1_b, xor_1_out;

  Switch A (.A(1'b1), .B(A_b));
  Switch B (.A(1'b1), .B(B_b));
  // SwitchDT A_2: pin names not known; wires that end beside it: 1'b1, 1'b0, A_2_p3
  // SwitchDT B_2: pin names not known; wires that end beside it: 1'b1, 1'b0, B_2_p3
  Switch A_3 (.A(1'b1), .B(A_3_b));
  Switch B_3 (.A(1'b1), .B(B_3_b));
  // SwitchDT A_4: pin names not known; wires that end beside it: 1'b1, 1'b0, A_4_p3
  // SwitchDT B_4: pin names not known; wires that end beside it: 1'b1, 1'b0, B_4_p3
  // SwitchDT A_5: pin names not known; wires that end beside it: 1'b1, 1'b0, A_5_p3
  // SwitchDT B_5: pin names not known; wires that end beside it: 1'b1, 1'b0, B_5_p3
  // SwitchDT A_6: pin names not known; wires that end beside it: 1'b1, 1'b0, A_6_p3
  // SwitchDT B_6: pin names not known; wires that end beside it: 1'b1, 1'b0, B_6_p3
  // SwitchDT A_7: pin names not known; wires that end beside it: 1'b1, 1'b0, A_7_p3
  Switch A_8 (.A(1'b1), .B(A_8_b));
  Switch A_9 (.A(1'b1), .B(A_9_b));
  // SwitchDT A_10: pin names not known; wires that end beside it: 1'b1, A_10_p2, A_10_p3
  PFET pfet_1 (.G(A_5_p3), .S(1'b1), .D(pfet_1_d));
  NFET nfet_1 (.G(A_5_p3), .D(pfet_1_d), .S(1'b0));
  Switch #(.Closed("true")) switch_1 (.A(1'b1), .B(switch_1_b));
  PFET pfet_2 (.G(A_7_p3), .S(1'b1), .D(pfet_2_d));
  NFET nfet_2 (.G(A_7_p3), .D(pfet_2_d), .S(1'b0));
  NFET nfet_3 (.G(A_b), .D(1'b1), .S(nfet_3_s));
  NFET nfet_4 (.G(B_b), .D(nfet_3_s), .S(nfet_4_s));
  and and_1 (and_1_out, A_2_p3, B_2_p3);
  NFET nfet_5 (.G(A_3_b), .D(1'b1), .S(nfet_5_s));
  NFET nfet_6 (.G(B_3_b), .D(1'b1), .S(nfet_5_s));
  or or_1 (or_1_out, A_4_p3, B_4_p3);
  PullDown pulldown_1 (.out(B_5_p3));
  xor xor_1 (xor_1_out, A_6_p3, B_6_p3);
  Switch B_7 (.A(A_8_b), .B(B_7_b));
  Switch B_8 (.A(1'b1), .B(A_9_b));
  // SwitchDT B_9: pin names not known; wires that end beside it: A_10_p3, A_10_p2, B_9_p3
  PFET pfet_3 (.G(B_5_p3), .S(A_5_p3), .D(pfet_3_d));
  NFET nfet_7 (.G(B_5_p3), .D(pfet_3_d), .S(pfet_1_d));
  // PolarityAwareLED polarityawareled_1: pin names not known; wires that end beside it: nfet_5_s, 1'b0
  // PolarityAwareLED polarityawareled_2: pin names not known; wires that end beside it: pfet_3_d, 1'b0
  // PolarityAwareLED polarityawareled_3: pin names not known; wires that end beside it: switch_1_b, 1'b0
  // PolarityAwareLED polarityawareled_4: pin names not known; wires that end beside it: pfet_2_d, 1'b0
  // PolarityAwareLED polarityawareled_5: pin names not known; wires that end beside it: B_7_b, 1'b0
  // PolarityAwareLED polarityawareled_6: pin names not known; wires that end beside it: nfet_4_s, 1'b0
  // PolarityAwareLED polarityawareled_7: pin names not known; wires that end beside it: and_1_out, 1'b0
  // PolarityAwareLED polarityawareled_8: pin names not known; wires that end beside it: A_9_b, 1'b0
  // PolarityAwareLED polarityawareled_9: pin names not known; wires that end beside it: or_1_out, 1'b0
  // PolarityAwareLED polarityawareled_10: pin names not known; wires that end beside it: B_9_p3, 1'b0
  // PolarityAwareLED polarityawareled_11: pin names not known; wires that end beside it: xor_1_out, 1'b0

  // Notes on the sheet:
  //   NOT
  //   AND
  //   OR
  //   XOR
endmodule
