// Digital circuit wires.dig as structural Verilog
module wires (
);

  wire switch_1_b;

  Switch switch_1 (.A(1'b1), .B(switch_1_b));
  // PolarityAwareLED polarityawareled_1: pin names not known; wires that end beside it: 1'b1, 1'b0
  // PolarityAwareLED polarityawareled_2: pin names not known; wires that end beside it: switch_1_b, 1'b0

  // Notes on the sheet:
  //   Positive Voltage
  //   Negative Voltage
endmodule
