// Digital circuit bram.dig as structural Verilog
module bram (
  input  [8:0] addr_rd,
  input  [8:0] addr_wr,
  input  clk,
  input  en_wr,
  input  [7:0] data_wr,
  output [7:0] data_rd
);

  wire [7:0] ramdualaccess_1_d2;

  RAMDualAccess #(.AddrBits(9), .Bits(8)) ramdualaccess_1 (
    .str(en_wr), .C(clk), .ld(1'b1), .A1(addr_wr), .Din1(data_wr), .A2(addr_rd), .D2(ramdualaccess_1_d2));  // open: D1
  D_FF #(.Bits(8)) d_ff_1 (.D(ramdualaccess_1_d2), .C(clk), .Q(data_rd));  // open: nQ

  // Other names for the same wires on the sheet: C = clk
endmodule
