// Digital circuit fifo.dig as structural Verilog
module fifo (
  input  rd,
  input  wr,
  input  [7:0] D,
  input  clk,
  input  clr,
  output [7:0] Q,
  output full,
  output empty
);

  wire and_1_out, and_2_out;
  wire [9:0] Read_out, sub_1_s, Write_out;

  and and_1 (and_1_out, ~empty, rd);  // And
  and and_2 (and_2_out, wr, ~full);  // And
  Counter #(.Bits(10)) Read (.en(and_1_out), .C(clk), .clr(clr), .out(Read_out));  // open: ovf
  Counter #(.Bits(10)) Write (.en(and_2_out), .C(clk), .clr(clr), .out(Write_out));  // open: ovf
  bram bram_1 (
    .addr_rd(Read_out[8:0]), .addr_wr(Write_out[8:0]), .clk(clk), .en_wr(and_2_out), .data_wr(D), .data_rd(Q));
  Sub #(.Bits(10)) sub_1 (.a(Write_out), .b(Read_out), .c_i(1'b0), .s(sub_1_s));  // open: c_o
  Comparator #(.Bits(10)) comparator_1 (.a(sub_1_s), .b({10{1'b0}}), .eq(empty));  // open: gt, lt
  Comparator #(.Bits(10)) comparator_2 (.a(sub_1_s), .b(10'h200), .eq(full));  // open: gt, lt

  // Other names for the same wires on the sheet: C = clk; rst = clr
endmodule

/* Test case:
clk rd wr clr D    full empty Q

C    0  0   0 42      0     1 0
C    0  0   0 42      0     1 0

C    0  1   0 42      0     0 42
C    0  1   0 25      0     0 42
C    0  1   0 19      0     0 42
C    0  1   0 36      1     0 42
C    0  1   0 45      1     0 42

C    1  0   0 11      0     0 25
C    1  0   0 22      0     0 19
C    1  0   0 33      0     0 36
C    1  0   0 44      0     1 42
C    1  0   0 55      0     1 42
*/
