// Digital circuit filt0.dig as structural Verilog
module filt0 (
  input  [7:0] I,
  output [7:0] O
);

  wire comparator_1_eq;

  Comparator #(.Bits(8)) comparator_1 (.a(I), .b({8{1'b0}}), .eq(comparator_1_eq));  // open: gt, lt
  Multiplexer #(.Bits(8)) multiplexer_1 (.sel(comparator_1_eq), .in_0(I), .in_1(8'ha), .out(O));
endmodule
