// Digital circuit fpga101.dig as structural Verilog
module fpga101 (
  input  rx,
  input  clk,
  output tx
);

  wire C, fsm_1_tx_rd, fsm_1_tx_start, pll_1_locked, R, rx_empty, TX_empty, uart_1_rx_ready, uart_1_tx_busy,
       xfer;
  wire [7:0] QD, rx_data, TX_q, uart_1_rx_data;

  pll pll_1 (.clock_in(clk), .clock_out(C), .locked(pll_1_locked));
  fifo u_TX (.rd(fsm_1_tx_rd), .wr(xfer), .D(QD), .clk(C), .clr(R), .Q(TX_q), .empty(TX_empty));  // open: full
  not not_1 (R, pll_1_locked);
  uart uart_1 (
    .rx(rx), .clk(C), .tx_start(fsm_1_tx_start), .tx_data(TX_q), .tx(tx), .rx_ready(uart_1_rx_ready),
    .rx_data(uart_1_rx_data), .tx_busy(uart_1_tx_busy));
  filt0 filt0_1 (.I(uart_1_rx_data), .O(rx_data));
  fsm fsm_1 (
    .rx_data(rx_data), .tx_busy(uart_1_tx_busy), .tx_empty(TX_empty), .clk(C), .rx_empty(rx_empty),
    .xfer(xfer), .tx_start(fsm_1_tx_start), .tx_rd(fsm_1_tx_rd));
  fifo u_RX (.rd(xfer), .wr(uart_1_rx_ready), .D(rx_data), .clk(C), .clr(R), .Q(QD), .empty(rx_empty));  // open: full

  // Notes on the sheet:
  //   clk: Hz: 10
endmodule
