// Digital circuit fsm.dig as structural Verilog
module fsm (
  input  [7:0] rx_data,
  input  tx_busy,
  input  tx_empty,
  input  clk,
  input  rx_empty,
  output xfer,
  output tx_start,
  output tx_rd
);

  wire d_ff_1_q, equals_1_q, rsff_1_q;

  rsff rsff_1 (.S(xfer), .C(clk), .R(tx_empty), .Q(rsff_1_q));  // open: nQ
  equals #(.generic("bitWidth := 8;")) equals_1 (.A(rx_data), .B(8'ha), .Q(equals_1_q));
  and and_1 (tx_rd, rsff_1_q, ~tx_empty, ~tx_busy);  // And
  rsff rsff_2 (.S(equals_1_q), .C(clk), .R(rx_empty), .Q(xfer));  // open: nQ
  D_FF d_ff_1 (.D(rsff_1_q), .C(clk), .Q(d_ff_1_q));  // open: nQ
  and and_2 (tx_start, d_ff_1_q, tx_rd);

  // Other names for the same wires on the sheet: C = clk
endmodule
