// Digital circuit uart.dig as structural Verilog
module uart (
  input  rx,
  input  clk,
  input  tx_start,
  input  [7:0] tx_data,
  output tx,
  output rx_ready,
  output [7:0] rx_data,
  output tx_busy
);

  wire d_ff_1_q, d_ff_2_q;

  D_FF d_ff_1 (.D(tx_start), .C(clk), .Q(d_ff_1_q));  // open: nQ
  Telnet #(.telnetEscape("false"), .port(2323)) Telnet (
    .in(tx_data), .C(clk), .wr(tx_start), .rd(1'b1), .out(rx_data), .av(rx_ready));
  D_FF d_ff_2 (.D(d_ff_1_q), .C(clk), .Q(d_ff_2_q));  // open: nQ
  or or_1 (tx_busy, d_ff_1_q, d_ff_2_q);

  assign tx = 1'b0;

  // Other names for the same wires on the sheet: C = clk
endmodule
